// Logisim project mimo_32bit_v4.3 - Predikcije.circ as structural Verilog: 29 circuits, main circuit MiMo_Pipelined_v2
module MiMo_Pipelined_v2 (
  input  Stop_Addr,
  input  Cycle,
  input  [15:0] Break_Addr
);

  wire ADDR_DEC_output_3, alu_1_carry, alu_1_negative, alu_1_overflow, alu_1_zero, and_1_out, and_2_out,
       and_3_out, and_4_out, and_5_out, and_6_out, and_7_out, and_8_out, and_9_out, and_10_out, and_11_out,
       and_12_out, and_13_out, and_14_out, and_16_out, and_17_out, and_18_out, and_19_out, and_20_out,
       bubble, button_2_out, button_3_out, button_4_out, button_5_out, button_6_out, button_7_out, C,
       Clear_out, Clear_Screen_out, CLK, CLKin, cond_met, cont, corrPred, corrPred2, crnt_cond_met,
       datawrite, dwrite, dwrite_ID, ex_to_ma_1_dwrite_out, ex_to_ma_1_imload_out, ex_to_ma_1_swrite_out,
       ex_to_ma_1_twrite_out, FB_LED, flagsForward, flgset, flush, id_to_ex_1_datawrite_out,
       id_to_ex_1_dwrite_out, id_to_ex_1_imload_out, id_to_ex_1_swrite_out, id_to_ex_1_twrite_out, imload,
       instruction_reg_1_set_flags, load_LR, LSB, LSB0, LSB1, LSB2, LSBc, LSBc1, LSBc2, LSBc3, LSBc4, MSB,
       MSB0, MSB1, MSB2, MSBc1, MSBc2, MSBc3, MSBc4, multiplexer_2_out, multiplexer_6_out, multiplexer_7_out,
       multiplexer_17_out, multiplexer_42_out, multiplexer_47_out, multiplexer_78_out, multiplexer_79_out, N,
       negOp2, nor_1_out, not_1_out, not_2_out, not_3_out, not_4_out, not_5_out, not_6_out, not_7_out,
       not_8_out, not_9_out, not_10_out, not_11_out, not_12_out, not_13_out, oneBit, or_1_out, or_2_out,
       or_4_out, or_5_out, or_6_out, predicted_jump, prediction_crct, prev_predicted_jump, prev_shld_predict,
       prev_uncond, RAMSel, register_4_q, register_5_q, register_6_q, register_8_q, register_9_q, Reset,
       rvrsOps, should_predict, stall, str_LR, swrite, tournament, TTYSel, twrite, uncond, update_c1,
       update_c2, update_c3, update_c4, V, Z;
  wire [1:0] addrsel, datasel, id_to_ex_1_addrsel_out, id_to_ex_1_datasel_out, multiplexer_8_out,
       multiplexer_9_out, multiplexer_10_out, multiplexer_11_out, multiplexer_12_out, multiplexer_13_out,
       multiplexer_14_out, multiplexer_15_out, multiplexer_18_out, multiplexer_19_out, multiplexer_20_out,
       multiplexer_21_out, multiplexer_22_out, multiplexer_23_out, multiplexer_24_out, multiplexer_25_out,
       multiplexer_26_out, multiplexer_27_out, multiplexer_28_out, multiplexer_29_out, multiplexer_30_out,
       multiplexer_31_out, multiplexer_32_out, multiplexer_33_out, multiplexer_36_out, multiplexer_37_out,
       multiplexer_38_out, multiplexer_39_out, multiplexer_40_out, multiplexer_41_out, multiplexer_48_out,
       multiplexer_49_out, multiplexer_50_out, multiplexer_51_out, multiplexer_52_out, multiplexer_53_out,
       multiplexer_54_out, multiplexer_55_out, multiplexer_56_out, multiplexer_57_out, multiplexer_58_out,
       multiplexer_59_out, multiplexer_60_out, multiplexer_61_out, multiplexer_62_out, multiplexer_63_out,
       multiplexer_65_out, multiplexer_66_out, multiplexer_67_out, multiplexer_68_out, multiplexer_69_out,
       multiplexer_70_out, multiplexer_71_out, multiplexer_72_out, op2sel, pc_prediction_logic_1_pcsel_out,
       pcsel, pcsel_IF, prevRegsrc, prevRegsrc1, raw_check_1_sselforward, raw_check_1_tselforward, regsrc,
       shift_register_2_q0, two_bit_update, two_bit_update_c, two_bit_update_c1, two_bit_update_c2,
       two_bit_update_c3, two_bit_update_c4, update_CPT, update_GPT, update_LPT;
  wire [2:0] dsel, ex_to_ma_1_dregsel_out, ex_to_ma_1_sregsel_out, ex_to_ma_1_tregsel_out,
       id_to_ex_1_dregselout, id_to_ex_1_sregselout, id_to_ex_1_tregselout, instruction_reg_1_dregsel,
       lht_1_lpt_addr, lht_1_r0, lht_1_r1, lht_1_r2, lht_1_r3, lht_1_r4, lht_1_r5, lht_1_r6, lht_1_r7,
       lht_2_lpt_addr, lht_2_r0, lht_2_r1, lht_2_r2, lht_2_r3, lht_2_r4, lht_2_r5, lht_2_r6, lht_2_r7,
       ma_to_wb_1_dregsel_out, ma_to_wb_1_sregsel_out, ma_to_wb_1_tregsel_out, multiplexer_5_out,
       opcode_decoder_1_rd, opcode_decoder_1_rs, opcode_decoder_1_rt, opcode_decoder_2_rd,
       opcode_decoder_2_rs, opcode_decoder_2_rt, opcode_decoder_3_rd, opcode_decoder_3_rs,
       opcode_decoder_3_rt, opcode_decoder_4_rd, opcode_decoder_4_rs, opcode_decoder_4_rt,
       opcode_decoder_5_rd, opcode_decoder_5_rs, opcode_decoder_5_rt, opcode_decoder_6_rd,
       opcode_decoder_6_rs, opcode_decoder_6_rt, opcode_decoder_7_rd, opcode_decoder_7_rs,
       opcode_decoder_7_rt, opcode_decoder_8_rd, opcode_decoder_8_rs, opcode_decoder_8_rt,
       shift_register_1_out, ssel, tsel;
  wire [3:0] aluop, instruction_reg_1_condition, multiplexer_84_out, showhexa_1_digit, showhexa_1_out_2,
       showhexa_1_out_3, showhexa_1_out_4, showhexa_1_out_5, showhexa_1_out_7, showhexa_1_out_8,
       showhexa_1_out_9, showhexa_2_digit, showhexa_2_out_2, showhexa_2_out_3, showhexa_2_out_4,
       showhexa_2_out_5, showhexa_2_out_7, showhexa_2_out_8, showhexa_2_out_9, showhexa_3_digit,
       showhexa_3_out_2, showhexa_3_out_3, showhexa_3_out_4, showhexa_3_out_5, showhexa_3_out_7,
       showhexa_3_out_8, showhexa_3_out_9, showhexa_4_digit, showhexa_4_out_2, showhexa_4_out_3,
       showhexa_4_out_4, showhexa_4_out_5, showhexa_4_out_7, showhexa_4_out_8, showhexa_4_out_9,
       showhexa_5_digit, showhexa_5_out_2, showhexa_5_out_3, showhexa_5_out_4, showhexa_5_out_5,
       showhexa_5_out_7, showhexa_5_out_8, showhexa_5_out_9, showhexa_6_digit, showhexa_6_out_2,
       showhexa_6_out_3, showhexa_6_out_4, showhexa_6_out_5, showhexa_6_out_7, showhexa_6_out_8,
       showhexa_6_out_9;
  wire [6:0] instruction_reg_1_opcode, multiplexer_3_out, multiplexer_4_out;
  wire [7:0] multiplexer_64_out;
  wire [9:0] id_to_ex_1_immedout, instruction_reg_1_immed, multiplexer_80_out, opcode_decoder_1_imm,
       opcode_decoder_2_imm, opcode_decoder_3_imm, opcode_decoder_4_imm, opcode_decoder_5_imm,
       opcode_decoder_6_imm, opcode_decoder_7_imm, opcode_decoder_8_imm;
  wire [15:0] counter_1_q, IFaddr;
  wire [31:0] adder_1_out, adder_2_out, adder_3_out, alu_1_result, alu_operands_1_operand_1,
       alu_operands_1_operand_2, datain, ex_to_ma_1_aluout_out, ex_to_ma_1_immed_out, ex_to_ma_1_rd_out,
       ex_to_ma_1_rs_out, ex_to_ma_1_rt_out, forwarding_unit_1_rs_out, forwarding_unit_1_rt_out,
       frame_buffer_16x32_1_out_6, frame_buffer_16x32_1_out_7, frame_buffer_16x32_1_out_8,
       frame_buffer_16x32_1_out_9, frame_buffer_16x32_1_out_10, frame_buffer_16x32_1_out_11,
       frame_buffer_16x32_1_out_12, frame_buffer_16x32_1_out_13, frame_buffer_16x32_1_out_14,
       frame_buffer_16x32_1_out_15, frame_buffer_16x32_1_out_16, frame_buffer_16x32_1_out_17,
       frame_buffer_16x32_1_out_18, frame_buffer_16x32_1_out_19, frame_buffer_16x32_1_out_20,
       frame_buffer_16x32_1_out_21, id_to_ex_1_rd_out, id_to_ex_1_rs_out, id_to_ex_1_rt_out,
       if_to_id_1_instructionout, immed, immed_IF, Instruction_RAM_data, IR_EX, IR_ID, IR_MA, IR_WB, LR,
       ma_to_wb_1_aluout_out, ma_to_wb_1_immed_out, ma_to_wb_1_operand_out, ma_to_wb_1_rs_out,
       multiplexer_1_out, multiplexer_73_out, multiplexer_83_out, multiplexer_86_out, multiplexer_87_out,
       pc_1_prev_pc, pc_prediction_logic_1_immed_out, r0, r1, r2, r3, r4, r5, r6, r7, ram_11_data,
       register_1_q, register_2_q, register_bank_1_dreg, register_bank_1_treg, regwrite, rom_1_data, Rs;
  wire [31:3] multiplexer_5_out_2;
  wire [31:4] multiplexer_84_out_2;
  wire [31:16] pcreg;

  Clock clock_1 (.out(CLKin));
  Button button_1 (.out(Reset));
  Counter #(.max('hffff), .width(16)) counter_1 (
    .count(CLK), .Q(counter_1_q), .up(1'b1), .clk(CLK), .clr(Reset));  // open: load, D, carry
  LED u_N (.in(N));
  LED u_V (.in(V));
  LED u_Z (.in(Z));
  LED u_C (.in(C));
  // Probe on multiplexer_1_out
  Multiplexer #(.width(32)) multiplexer_1 (
    .in0(pc_prediction_logic_1_immed_out), .in1(LR), .out(multiplexer_1_out), .sel(str_LR));
  // Probe on counter_1_q
  // Probe on pc_prediction_logic_1_pcsel_out
  Multiplexer multiplexer_2 (.in0(1'b1), .in1(1'b0), .out(multiplexer_2_out), .sel(stall));
  Button u_Cont (.out(cont));
  // Probe on Break_Addr
  // Probe on IFaddr
  PC_Prediction_Logic pc_prediction_logic_1 (
    .should_predict(should_predict), .prev_shld_predict(prev_shld_predict), .predicted_jump(predicted_jump),
    .prev_predicted_jump(prev_predicted_jump), .flush(flush), .pcsel(pcsel), .pcsel_IF(pcsel_IF),
    .immed(immed), .immed_IF(immed_IF), .immed_out(pc_prediction_logic_1_immed_out),
    .pcsel_out(pc_prediction_logic_1_pcsel_out));
  Shift_Register #(.length(3)) shift_register_1 (
    .shift(prev_shld_predict), .in(crnt_cond_met), .clk(CLK), .out(shift_register_1_out[0]), .clr(Reset),
    .q0(shift_register_1_out[2]), .q1(shift_register_1_out[1]));  // open: load, d0, d1, d2, q2
  DebugUnit debugunit_1 (
    .reset(Reset), .\continue (cont), .clock(CLKin), .IFaddr(IFaddr), .break_addr(Break_Addr),
    .break_on_addr(Stop_Addr), .break_on_cycle(Cycle), .clock_out(CLK));
  // Probe on pc_prediction_logic_1_immed_out
  // Probe on pc_prediction_logic_1_pcsel_out
  // Probe on {pcreg, IFaddr}
  Hex_Digit_Display hex_digit_display_1 (.value(showhexa_1_out_2));  // open: dp
  ShowHexa showhexa_1 (
    .Data({pcreg, IFaddr}), .out_3(showhexa_1_out_3), .out_4(showhexa_1_out_4), .out_5(showhexa_1_out_5),
    .Digit(showhexa_1_digit), .out_7(showhexa_1_out_7), .out_8(showhexa_1_out_8), .out_9(showhexa_1_out_9),
    .out_2(showhexa_1_out_2));
  PC pc_1 (
    .imreg(multiplexer_1_out), .pcsel(pc_prediction_logic_1_pcsel_out), .pcload(multiplexer_2_out),
    .flush(flush), .clock(CLK), .reset(Reset), .should_predict(should_predict), .pcout({pcreg, IFaddr}),
    .prev_pc(pc_1_prev_pc));
  Hex_Digit_Display hex_digit_display_2 (.value(showhexa_1_out_3));  // open: dp
  Hex_Digit_Display hex_digit_display_3 (.value(showhexa_1_out_4));  // open: dp
  Multiplexer #(.width(7)) multiplexer_3 (
    .in0(7'b1001110), .in1(7'b1010100), .out(multiplexer_3_out), .sel(crnt_cond_met));
  Multiplexer #(.width(7)) multiplexer_4 (
    .in0(7'b1001110), .in1(7'b1010100), .out(multiplexer_4_out), .sel(predicted_jump));
  Adder #(.width(32)) adder_1 (.a(register_1_q), .b(32'h1), .out(adder_1_out));  // open: cin, cout
  and and_1 (and_1_out, prev_shld_predict, not_1_out);
  not not_1 (not_1_out, prev_uncond);
  and and_2 (and_2_out, prev_shld_predict, not_2_out);
  not not_2 (not_2_out, prev_uncond);
  and and_3 (and_3_out, prev_shld_predict, not_3_out);
  not not_3 (not_3_out, prev_uncond);
  not not_4 (not_4_out, prev_uncond);
  and and_4 (and_4_out, prev_shld_predict, not_5_out);
  not not_5 (not_5_out, prev_uncond);
  // Probe on opcode_decoder_1_rd
  // Probe on opcode_decoder_1_rd
  // Probe on opcode_decoder_1_rs
  // Probe on opcode_decoder_1_rs
  // Probe on opcode_decoder_1_rt
  // Probe on opcode_decoder_1_rt
  Hex_Digit_Display hex_digit_display_4 (.value(showhexa_1_out_5));  // open: dp
  Hex_Digit_Display hex_digit_display_5 (.value(showhexa_1_digit));  // open: dp
  // Probe on {pcreg, IFaddr}
  // Probe on pc_1_prev_pc
  Register #(.width(32)) register_1 (.D(adder_1_out), .en(flush), .Q(register_1_q), .clk(CLK), .clr(Reset));
  and and_5 (and_5_out, prev_shld_predict, not_6_out);
  not not_6 (not_6_out, prev_uncond);
  // Probe on lht_1_r0
  // Probe on lht_1_r1
  // Probe on lht_1_r2
  // Probe on lht_1_r3
  // Probe on lht_1_r4
  // Probe on lht_1_r5
  // Probe on lht_1_r6
  // Probe on lht_1_r7
  and and_6 (and_6_out, prev_shld_predict, not_7_out);
  and and_7 (and_7_out, and_6_out, update_c1);
  not not_7 (not_7_out, prev_uncond);
  and and_8 (and_8_out, and_2_out, update_c2);
  and and_9 (and_9_out, and_3_out, update_c3);
  and and_10 (and_10_out, prev_shld_predict, not_4_out);
  and and_11 (and_11_out, and_10_out, update_c4);
  // Probe on lht_2_r0
  // Probe on lht_2_r1
  // Probe on lht_2_r2
  // Probe on lht_2_r3
  // Probe on lht_2_r4
  // Probe on lht_2_r5
  // Probe on lht_2_r6
  // Probe on lht_2_r7
  not not_8 (not_8_out, prev_uncond);
  OpCode_Decoder opcode_decoder_1 (
    .in_1(IR_ID), .Imm(opcode_decoder_1_imm), .Rd(opcode_decoder_1_rd), .Rs(opcode_decoder_1_rs),
    .Rt(opcode_decoder_1_rt));
  // Probe on opcode_decoder_1_imm
  // Probe on opcode_decoder_1_imm
  Hex_Digit_Display hex_digit_display_6 (.value(showhexa_1_out_7));  // open: dp
  Hex_Digit_Display hex_digit_display_7 (.value(showhexa_1_out_8));  // open: dp
  TTY #(.cols(16), .rows(4)) tty_1 (.data(multiplexer_3_out), .clk(CLK), .we(prev_shld_predict), .clr(Reset));
  TTY #(.cols(16), .rows(4)) tty_2 (.data(multiplexer_4_out), .clk(CLK), .we(should_predict), .clr(Reset));
  // Probe on register_1_q
  LHT lht_1 (
    .address(multiplexer_5_out), .store(prev_shld_predict), .data_in(crnt_cond_met), .clk(CLK),
    .reset(Reset), .lpt_addr(lht_1_lpt_addr), .r0(lht_1_r0), .r1(lht_1_r1), .r2(lht_1_r2), .r3(lht_1_r3),
    .r4(lht_1_r4), .r5(lht_1_r5), .r6(lht_1_r6), .r7(lht_1_r7));
  LHT lht_2 (
    .address(multiplexer_5_out), .store(prev_shld_predict), .data_in(crnt_cond_met), .clk(CLK),
    .reset(Reset), .lpt_addr(lht_2_lpt_addr), .r0(lht_2_r0), .r1(lht_2_r1), .r2(lht_2_r2), .r3(lht_2_r3),
    .r4(lht_2_r4), .r5(lht_2_r5), .r6(lht_2_r6), .r7(lht_2_r7));
  and and_12 (and_12_out, prev_shld_predict, not_9_out);
  not not_9 (not_9_out, prev_uncond);
  and and_13 (and_13_out, prev_shld_predict, not_8_out);
  Hex_Digit_Display hex_digit_display_8 (.value(showhexa_1_out_9));  // open: dp
  Multiplexer #(.width(32)) multiplexer_5 (
    .in0({pcreg, IFaddr}), .in1(pc_1_prev_pc), .out({multiplexer_5_out_2, multiplexer_5_out}),
    .sel(prev_shld_predict));
  Adder #(.width(32)) adder_2 (.a(register_2_q), .b(32'h1), .out(adder_2_out));  // open: cin, cout
  RAM #(.addrWidth(3), .asyncread("true"), .clearpin("true"), .dataWidth(2)) ram_1 (
    .addr(lht_1_lpt_addr), .we(and_1_out), .oe(should_predict), .clk(CLK), .din(two_bit_update_c),
    .dout({corrPred, LSBc}), .clr(Reset));
  RAM #(.addrWidth(16), .asyncread("true"), .dataWidth(32), .databus("bidir")) Instruction_RAM (
    .addr(IFaddr), .we(1'b0), .oe(1'b1), .clk(CLK), .data(Instruction_RAM_data));
  Adder #(.width(32)) adder_3 (.a(pc_1_prev_pc), .b(32'h1), .out(adder_3_out));  // open: cin, cout
  Register #(.width(32)) register_2 (.D(adder_2_out), .en(prev_shld_predict), .Q(register_2_q), .clk(CLK), .clr(Reset));
  RAM #(.addrWidth(3), .asyncread("true"), .clearpin("true"), .dataWidth(1)) ram_2 (
    .addr(multiplexer_5_out), .we(flush), .oe(should_predict), .clk(CLK), .din(not_10_out), .dout(oneBit),
    .clr(Reset));
  not not_10 (not_10_out, prev_predicted_jump);
  RAM #(.addrWidth(3), .asyncread("true"), .clearpin("true"), .dataWidth(2)) ram_3 (
    .addr(multiplexer_5_out), .we(and_5_out), .oe(should_predict), .clk(CLK), .din(two_bit_update),
    .dout({MSB, LSB}), .clr(Reset));
  RAM #(.addrWidth(3), .asyncread("true"), .clearpin("true"), .dataWidth(2)) ram_4 (
    .addr(multiplexer_5_out), .we(and_7_out), .oe(should_predict), .clk(CLK), .din(two_bit_update_c1),
    .dout({MSBc1, LSBc1}), .clr(Reset));
  RAM #(.addrWidth(3), .asyncread("true"), .clearpin("true"), .dataWidth(2)) ram_5 (
    .addr(multiplexer_5_out), .we(and_8_out), .oe(should_predict), .clk(CLK), .din(two_bit_update_c2),
    .dout({MSBc2, LSBc2}), .clr(Reset));
  RAM #(.addrWidth(3), .asyncread("true"), .clearpin("true"), .dataWidth(2)) ram_6 (
    .addr(multiplexer_5_out), .we(and_9_out), .oe(should_predict), .clk(CLK), .din(two_bit_update_c3),
    .dout({MSBc3, LSBc3}), .clr(Reset));
  RAM #(.addrWidth(3), .asyncread("true"), .clearpin("true"), .dataWidth(2)) ram_7 (
    .addr(multiplexer_5_out), .we(and_11_out), .oe(should_predict), .clk(CLK), .din(two_bit_update_c4),
    .dout({MSBc4, LSBc4}), .clr(Reset));
  RAM #(.addrWidth(3), .asyncread("true"), .clearpin("true"), .dataWidth(2)) ram_8 (
    .addr(lht_2_lpt_addr), .we(and_12_out), .oe(should_predict), .clk(CLK), .din(update_GPT),
    .dout({MSB0, LSB0}), .clr(Reset));
  RAM #(.addrWidth(3), .asyncread("true"), .clearpin("true"), .dataWidth(2)) ram_9 (
    .addr(shift_register_1_out), .we(and_13_out), .oe(should_predict), .clk(CLK), .din(update_GPT),
    .dout({MSB1, LSB1}), .clr(Reset));
  RAM #(.addrWidth(3), .asyncread("true"), .clearpin("true"), .dataWidth(2)) ram_10 (
    .addr(shift_register_1_out), .we(and_4_out), .oe(should_predict), .clk(CLK), .din(update_CPT),
    .dout({MSB2, LSB2}), .clr(Reset));
  // Probe on r0
  // Probe on r1
  // Probe on r2
  // Probe on r3
  // Probe on r4
  // Probe on r5
  // Probe on r6
  // Probe on r7
  Button button_2 (.out(button_2_out));
  LED led_1 (.in(nor_1_out));
  nor nor_1 (nor_1_out, register_8_q, register_6_q, register_9_q, register_5_q, register_4_q);
  // Probe on register_2_q
  // Probe on opcode_decoder_2_imm
  // Probe on opcode_decoder_2_imm
  // Probe on opcode_decoder_2_rd
  // Probe on opcode_decoder_2_rd
  // Probe on opcode_decoder_2_rs
  // Probe on opcode_decoder_2_rs
  // Probe on opcode_decoder_2_rt
  // Probe on opcode_decoder_2_rt
  OpCode_Decoder opcode_decoder_2 (
    .in_1(IR_EX), .Imm(opcode_decoder_2_imm), .Rd(opcode_decoder_2_rd), .Rs(opcode_decoder_2_rs),
    .Rt(opcode_decoder_2_rt));
  LED led_2 (.in(N));
  LED led_3 (.in(V));
  Register #(.width(32)) register_3 (.D(adder_3_out), .en(load_LR), .Q(LR), .clk(CLK), .clr(Reset));
  // Probe on LR
  Button button_3 (.out(button_3_out));
  LED led_4 (.in(register_4_q));
  Register #(.width(1)) register_4 (
    .D(button_3_out), .en(button_3_out), .Q(register_4_q), .clk(button_3_out), .clr(or_1_out));
  or or_1 (or_1_out, button_2_out, button_4_out, button_7_out, button_5_out, button_6_out);
  Multiplexer multiplexer_6 (.in0(1'b0), .in1(oneBit), .out(multiplexer_6_out), .sel(register_4_q));
  LED led_5 (.in(Z));
  LED led_6 (.in(C));
  Button button_4 (.out(button_4_out));
  LED led_7 (.in(register_5_q));
  Register #(.width(1)) register_5 (
    .D(button_4_out), .en(button_4_out), .Q(register_5_q), .clk(button_4_out), .clr(or_2_out));
  or or_2 (or_2_out, button_2_out, button_3_out, button_7_out, button_6_out, button_5_out);
  Multiplexer multiplexer_7 (.in0(multiplexer_6_out), .in1(MSB), .out(multiplexer_7_out), .sel(register_5_q));
  or or_3 (predicted_jump, uncond, multiplexer_47_out);
  // Probe on opcode_decoder_3_imm
  // Probe on opcode_decoder_3_rd
  // Probe on opcode_decoder_3_rd
  // Probe on opcode_decoder_3_rs
  // Probe on opcode_decoder_3_rs
  // Probe on opcode_decoder_3_rt
  // Probe on opcode_decoder_3_rt
  Button button_5 (.out(button_5_out));
  LED led_8 (.in(register_6_q));
  Multiplexer #(.width(2)) multiplexer_8 (.in0(2'b00), .in1(2'b01), .out(multiplexer_8_out), .sel(cond_met));
  Multiplexer #(.width(2)) multiplexer_9 (.in0(2'b00), .in1(2'b10), .out(multiplexer_9_out), .sel(cond_met));
  Multiplexer #(.width(2)) multiplexer_10 (.in0(2'b01), .in1(2'b11), .out(multiplexer_10_out), .sel(cond_met));
  Multiplexer #(.width(2)) multiplexer_11 (.in0(2'b10), .in1(2'b11), .out(multiplexer_11_out), .sel(cond_met));
  Multiplexer #(.width(2)) multiplexer_12 (.in0(2'b00), .in1(2'b01), .out(multiplexer_12_out), .sel(crnt_cond_met));
  Multiplexer #(.width(2)) multiplexer_13 (.in0(2'b00), .in1(2'b10), .out(multiplexer_13_out), .sel(crnt_cond_met));
  Multiplexer #(.width(2)) multiplexer_14 (.in0(2'b01), .in1(2'b11), .out(multiplexer_14_out), .sel(crnt_cond_met));
  Multiplexer #(.width(2)) multiplexer_15 (.in0(2'b10), .in1(2'b11), .out(multiplexer_15_out), .sel(crnt_cond_met));
  Multiplexer multiplexer_16 (.in0(MSB0), .in1(MSB1), .out(tournament), .sel(MSB2));
  OpCode_Decoder opcode_decoder_3 (
    .in_1(IR_MA), .Imm(opcode_decoder_3_imm), .Rd(opcode_decoder_3_rd), .Rs(opcode_decoder_3_rs),
    .Rt(opcode_decoder_3_rt));
  // Probe on opcode_decoder_3_imm
  Register #(.width(1)) register_6 (
    .D(button_5_out), .en(button_5_out), .Q(register_6_q), .clk(button_5_out), .clr(or_4_out));
  or or_4 (or_4_out, button_2_out, button_3_out, button_7_out, button_4_out, button_6_out);
  Multiplexer multiplexer_17 (.in0(multiplexer_7_out), .in1(corrPred), .out(multiplexer_17_out), .sel(register_6_q));
  Register #(.width(1)) register_7 (.D(predicted_jump), .en(CLK), .Q(prev_predicted_jump), .clk(CLK), .clr(Reset));
  Multiplexer #(.width(2)) multiplexer_18 (
    .in0(multiplexer_8_out), .in1(multiplexer_9_out), .out(multiplexer_18_out), .sel(LSB));
  Multiplexer #(.width(2)) multiplexer_19 (
    .in0(multiplexer_10_out), .in1(multiplexer_11_out), .out(multiplexer_19_out), .sel(LSB));
  Multiplexer #(.width(2)) multiplexer_20 (
    .in0(multiplexer_12_out), .in1(multiplexer_13_out), .out(multiplexer_20_out), .sel(LSBc));
  Multiplexer #(.width(2)) multiplexer_21 (
    .in0(multiplexer_14_out), .in1(multiplexer_15_out), .out(multiplexer_21_out), .sel(LSBc));
  and and_14 (and_14_out, prev_shld_predict, not_11_out);
  not not_11 (not_11_out, prev_uncond);
  Multiplexer #(.width(2)) multiplexer_22 (.in0(2'b00), .in1(2'b01), .out(multiplexer_22_out), .sel(crnt_cond_met));
  Multiplexer #(.width(2)) multiplexer_23 (.in0(2'b00), .in1(2'b10), .out(multiplexer_23_out), .sel(crnt_cond_met));
  Multiplexer #(.width(2)) multiplexer_24 (.in0(2'b01), .in1(2'b11), .out(multiplexer_24_out), .sel(crnt_cond_met));
  Multiplexer #(.width(2)) multiplexer_25 (.in0(2'b10), .in1(2'b11), .out(multiplexer_25_out), .sel(crnt_cond_met));
  Multiplexer #(.width(2)) multiplexer_26 (.in0(2'b00), .in1(2'b01), .out(multiplexer_26_out), .sel(crnt_cond_met));
  Multiplexer #(.width(2)) multiplexer_27 (.in0(2'b00), .in1(2'b10), .out(multiplexer_27_out), .sel(crnt_cond_met));
  Multiplexer #(.width(2)) multiplexer_28 (.in0(2'b01), .in1(2'b11), .out(multiplexer_28_out), .sel(crnt_cond_met));
  Multiplexer #(.width(2)) multiplexer_29 (.in0(2'b10), .in1(2'b11), .out(multiplexer_29_out), .sel(crnt_cond_met));
  Multiplexer #(.width(2)) multiplexer_30 (.in0(2'b00), .in1(2'b01), .out(multiplexer_30_out), .sel(crnt_cond_met));
  Multiplexer #(.width(2)) multiplexer_31 (.in0(2'b00), .in1(2'b10), .out(multiplexer_31_out), .sel(crnt_cond_met));
  Multiplexer #(.width(2)) multiplexer_32 (.in0(2'b01), .in1(2'b11), .out(multiplexer_32_out), .sel(crnt_cond_met));
  Multiplexer #(.width(2)) multiplexer_33 (.in0(2'b10), .in1(2'b11), .out(multiplexer_33_out), .sel(crnt_cond_met));
  Instruction_prediction_unit instruction_prediction_unit_1 (
    .Clk(CLK), .Reset(Reset), .instruction(Instruction_RAM_data), .stall(stall), .str_LR(str_LR),
    .pcsel_IF(pcsel_IF), .immed_IF(immed_IF), .should_predict(should_predict), .uncond(uncond),
    .prev_shld_predict(prev_shld_predict), .prev_uncond(prev_uncond));
  not not_12 (not_12_out, prediction_crct);
  and and_15 (flush, prev_shld_predict, not_12_out);
  Button button_6 (.out(button_6_out));
  LED led_9 (.in(register_8_q));
  or or_5 (or_5_out, button_2_out, button_3_out, button_7_out, button_4_out, button_5_out);
  Multiplexer #(.width(2)) multiplexer_34 (
    .in0(multiplexer_18_out), .in1(multiplexer_19_out), .out(two_bit_update), .sel(MSB));
  Multiplexer #(.width(2)) multiplexer_35 (
    .in0(multiplexer_20_out), .in1(multiplexer_21_out), .out(two_bit_update_c), .sel(corrPred));
  Multiplexer #(.width(2)) multiplexer_36 (
    .in0(multiplexer_22_out), .in1(multiplexer_23_out), .out(multiplexer_36_out), .sel(LSB0));
  Multiplexer #(.width(2)) multiplexer_37 (
    .in0(multiplexer_24_out), .in1(multiplexer_25_out), .out(multiplexer_37_out), .sel(LSB0));
  Multiplexer #(.width(2)) multiplexer_38 (
    .in0(multiplexer_26_out), .in1(multiplexer_27_out), .out(multiplexer_38_out), .sel(LSB1));
  Multiplexer #(.width(2)) multiplexer_39 (
    .in0(multiplexer_28_out), .in1(multiplexer_29_out), .out(multiplexer_39_out), .sel(LSB1));
  Multiplexer #(.width(2)) multiplexer_40 (
    .in0(multiplexer_30_out), .in1(multiplexer_31_out), .out(multiplexer_40_out), .sel(LSB2));
  Multiplexer #(.width(2)) multiplexer_41 (
    .in0(multiplexer_32_out), .in1(multiplexer_33_out), .out(multiplexer_41_out), .sel(LSB2));
  Register #(.width(1)) register_8 (
    .D(button_6_out), .en(button_6_out), .Q(register_8_q), .clk(button_6_out), .clr(or_5_out));
  Multiplexer multiplexer_42 (.in0(multiplexer_17_out), .in1(corrPred2), .out(multiplexer_42_out), .sel(register_8_q));
  Shift_Register #(.length(2)) shift_register_2 (
    .shift(and_14_out), .in(crnt_cond_met), .clk(CLK), .out(shift_register_2_q0[1]), .clr(Reset),
    .q0(shift_register_2_q0[0]));  // open: load, d0, d1, q1
  Multiplexer #(.width(2)) multiplexer_43 (
    .in0(multiplexer_36_out), .in1(multiplexer_37_out), .out(update_LPT), .sel(MSB0));
  Multiplexer #(.width(2)) multiplexer_44 (
    .in0(multiplexer_38_out), .in1(multiplexer_39_out), .out(update_GPT), .sel(MSB1));
  Multiplexer #(.width(2)) multiplexer_45 (
    .in0(multiplexer_40_out), .in1(multiplexer_41_out), .out(update_CPT), .sel(MSB2));
  // Probe on opcode_decoder_4_rd
  // Probe on opcode_decoder_4_rd
  // Probe on opcode_decoder_4_rs
  // Probe on opcode_decoder_4_rs
  // Probe on opcode_decoder_4_rt
  // Probe on opcode_decoder_4_rt
  Button button_7 (.out(button_7_out));
  LED led_10 (.in(register_9_q));
  Register #(.width(1)) register_9 (
    .D(button_7_out), .en(button_7_out), .Q(register_9_q), .clk(button_7_out), .clr(or_6_out));
  or or_6 (or_6_out, button_2_out, button_3_out, button_6_out, button_4_out, button_5_out);
  Multiplexer #(.select(2)) multiplexer_46 (
    .in0(MSBc1), .in1(MSBc2), .in2(MSBc3), .in3(MSBc4), .out(corrPred2), .sel(shift_register_2_q0));
  OpCode_Decoder opcode_decoder_4 (
    .in_1(IR_WB), .Imm(opcode_decoder_4_imm), .Rd(opcode_decoder_4_rd), .Rs(opcode_decoder_4_rs),
    .Rt(opcode_decoder_4_rt));
  // Probe on opcode_decoder_4_imm
  // Probe on opcode_decoder_4_imm
  Multiplexer multiplexer_47 (.in0(multiplexer_42_out), .in1(tournament), .out(multiplexer_47_out), .sel(register_9_q));
  Decoder #(.enable("false"), .select(2)) decoder_1 (
    .out0(update_c1), .out1(update_c2), .out2(update_c3), .out3(update_c4), .sel(shift_register_2_q0));
  Hex_Digit_Display hex_digit_display_9 (.value(showhexa_2_out_2));  // open: dp
  ShowHexa showhexa_2 (
    .Data(multiplexer_73_out), .out_3(showhexa_2_out_3), .out_4(showhexa_2_out_4), .out_5(showhexa_2_out_5),
    .Digit(showhexa_2_digit), .out_7(showhexa_2_out_7), .out_8(showhexa_2_out_8), .out_9(showhexa_2_out_9),
    .out_2(showhexa_2_out_2));
  Hex_Digit_Display hex_digit_display_10 (.value(showhexa_2_out_3));  // open: dp
  Hex_Digit_Display hex_digit_display_11 (.value(showhexa_2_out_4));  // open: dp
  // Probe on instruction_reg_1_opcode
  Hex_Digit_Display hex_digit_display_12 (.value(showhexa_2_out_5));  // open: dp
  Hex_Digit_Display hex_digit_display_13 (.value(showhexa_2_digit));  // open: dp
  Hex_Digit_Display hex_digit_display_14 (.value(showhexa_2_out_7));  // open: dp
  Hex_Digit_Display hex_digit_display_15 (.value(showhexa_2_out_8));  // open: dp
  Multiplexer #(.width(2)) multiplexer_48 (.in0(2'b00), .in1(2'b01), .out(multiplexer_48_out), .sel(crnt_cond_met));
  Multiplexer #(.width(2)) multiplexer_49 (.in0(2'b00), .in1(2'b10), .out(multiplexer_49_out), .sel(crnt_cond_met));
  Multiplexer #(.width(2)) multiplexer_50 (.in0(2'b01), .in1(2'b11), .out(multiplexer_50_out), .sel(crnt_cond_met));
  Multiplexer #(.width(2)) multiplexer_51 (.in0(2'b10), .in1(2'b11), .out(multiplexer_51_out), .sel(crnt_cond_met));
  Multiplexer #(.width(2)) multiplexer_52 (.in0(2'b00), .in1(2'b01), .out(multiplexer_52_out), .sel(crnt_cond_met));
  Multiplexer #(.width(2)) multiplexer_53 (.in0(2'b00), .in1(2'b10), .out(multiplexer_53_out), .sel(crnt_cond_met));
  Multiplexer #(.width(2)) multiplexer_54 (.in0(2'b01), .in1(2'b11), .out(multiplexer_54_out), .sel(crnt_cond_met));
  Multiplexer #(.width(2)) multiplexer_55 (.in0(2'b10), .in1(2'b11), .out(multiplexer_55_out), .sel(crnt_cond_met));
  Multiplexer #(.width(2)) multiplexer_56 (.in0(2'b00), .in1(2'b01), .out(multiplexer_56_out), .sel(crnt_cond_met));
  Multiplexer #(.width(2)) multiplexer_57 (.in0(2'b00), .in1(2'b10), .out(multiplexer_57_out), .sel(crnt_cond_met));
  Multiplexer #(.width(2)) multiplexer_58 (.in0(2'b01), .in1(2'b11), .out(multiplexer_58_out), .sel(crnt_cond_met));
  Multiplexer #(.width(2)) multiplexer_59 (.in0(2'b10), .in1(2'b11), .out(multiplexer_59_out), .sel(crnt_cond_met));
  Multiplexer #(.width(2)) multiplexer_60 (.in0(2'b00), .in1(2'b01), .out(multiplexer_60_out), .sel(crnt_cond_met));
  Multiplexer #(.width(2)) multiplexer_61 (.in0(2'b00), .in1(2'b10), .out(multiplexer_61_out), .sel(crnt_cond_met));
  Multiplexer #(.width(2)) multiplexer_62 (.in0(2'b01), .in1(2'b11), .out(multiplexer_62_out), .sel(crnt_cond_met));
  Multiplexer #(.width(2)) multiplexer_63 (.in0(2'b10), .in1(2'b11), .out(multiplexer_63_out), .sel(crnt_cond_met));
  Hex_Digit_Display hex_digit_display_16 (.value(showhexa_2_out_9));  // open: dp
  Multiplexer #(.width(8)) multiplexer_64 (
    .in0({8{1'b0}}), .in1({1'b0, instruction_reg_1_opcode}), .out(multiplexer_64_out), .sel(crnt_cond_met));
  Multiplexer #(.width(2)) multiplexer_65 (
    .in0(multiplexer_48_out), .in1(multiplexer_49_out), .out(multiplexer_65_out), .sel(LSBc1));
  Multiplexer #(.width(2)) multiplexer_66 (
    .in0(multiplexer_50_out), .in1(multiplexer_51_out), .out(multiplexer_66_out), .sel(LSBc1));
  Multiplexer #(.width(2)) multiplexer_67 (
    .in0(multiplexer_52_out), .in1(multiplexer_53_out), .out(multiplexer_67_out), .sel(LSBc2));
  Multiplexer #(.width(2)) multiplexer_68 (
    .in0(multiplexer_54_out), .in1(multiplexer_55_out), .out(multiplexer_68_out), .sel(LSBc2));
  Multiplexer #(.width(2)) multiplexer_69 (
    .in0(multiplexer_56_out), .in1(multiplexer_57_out), .out(multiplexer_69_out), .sel(LSBc3));
  Multiplexer #(.width(2)) multiplexer_70 (
    .in0(multiplexer_58_out), .in1(multiplexer_59_out), .out(multiplexer_70_out), .sel(LSBc3));
  Multiplexer #(.width(2)) multiplexer_71 (
    .in0(multiplexer_60_out), .in1(multiplexer_61_out), .out(multiplexer_71_out), .sel(LSBc4));
  Multiplexer #(.width(2)) multiplexer_72 (
    .in0(multiplexer_62_out), .in1(multiplexer_63_out), .out(multiplexer_72_out), .sel(LSBc4));
  Multiplexer #(.width(32)) multiplexer_73 (
    .in0(Instruction_RAM_data), .in1({32{1'b0}}), .out(multiplexer_73_out), .sel(flush));
  ROM #(.dataWidth(32)) rom_1 (
    .addr(multiplexer_64_out),
    .data({rom_1_data[31:21], dwrite_ID, rom_1_data[19:4], load_LR, pcsel, rom_1_data[0]}));
  Multiplexer #(.width(2)) multiplexer_74 (
    .in0(multiplexer_65_out), .in1(multiplexer_66_out), .out(two_bit_update_c1), .sel(MSBc1));
  Multiplexer #(.width(2)) multiplexer_75 (
    .in0(multiplexer_67_out), .in1(multiplexer_68_out), .out(two_bit_update_c2), .sel(MSBc2));
  Multiplexer #(.width(2)) multiplexer_76 (
    .in0(multiplexer_69_out), .in1(multiplexer_70_out), .out(two_bit_update_c3), .sel(MSBc3));
  Multiplexer #(.width(2)) multiplexer_77 (
    .in0(multiplexer_71_out), .in1(multiplexer_72_out), .out(two_bit_update_c4), .sel(MSBc4));
  IF_to_ID if_to_id_1 (
    .Clk(CLK), .Reset(Reset), .instruction(multiplexer_73_out), .instructionOut(if_to_id_1_instructionout));
  Multiplexer multiplexer_78 (.in0(1'b1), .in1(1'b0), .out(multiplexer_78_out), .sel(stall));
  Register #(.width(32)) register_10 (
    .D(if_to_id_1_instructionout), .en(multiplexer_78_out), .Q(IR_ID), .clk(CLK), .clr(Reset));
  Hex_Digit_Display hex_digit_display_17 (.value(showhexa_3_out_2));  // open: dp
  ShowHexa showhexa_3 (
    .Data(IR_ID), .out_3(showhexa_3_out_3), .out_4(showhexa_3_out_4), .out_5(showhexa_3_out_5),
    .Digit(showhexa_3_digit), .out_7(showhexa_3_out_7), .out_8(showhexa_3_out_8), .out_9(showhexa_3_out_9),
    .out_2(showhexa_3_out_2));
  Multiplexer multiplexer_79 (.in0(1'b1), .in1(1'b0), .out(multiplexer_79_out), .sel(stall));
  Hex_Digit_Display hex_digit_display_18 (.value(showhexa_3_out_3));  // open: dp
  Hex_Digit_Display hex_digit_display_19 (.value(showhexa_3_out_4));  // open: dp
  Hex_Digit_Display hex_digit_display_20 (.value(showhexa_3_out_5));  // open: dp
  Hex_Digit_Display hex_digit_display_21 (.value(showhexa_3_digit));  // open: dp
  Hex_Digit_Display hex_digit_display_22 (.value(showhexa_3_out_7));  // open: dp
  Hex_Digit_Display hex_digit_display_23 (.value(showhexa_3_out_8));  // open: dp
  // Probe on instruction_reg_1_immed
  Instruction_Reg instruction_reg_1 (
    .reset(Reset), .irload(multiplexer_79_out), .instruction(if_to_id_1_instructionout), .clock(CLK),
    .immed(instruction_reg_1_immed), .dregsel(instruction_reg_1_dregsel), .sregsel(ssel), .tregsel(tsel),
    .condition(instruction_reg_1_condition), .set_flags(instruction_reg_1_set_flags), .imload(imload),
    .opcode(instruction_reg_1_opcode));
  // Probe on instruction_reg_1_dregsel
  // Probe on ssel
  // Probe on tsel
  // Probe on instruction_reg_1_condition
  // Probe on instruction_reg_1_set_flags
  // Probe on imload
  // Probe on instruction_reg_1_opcode
  Hex_Digit_Display hex_digit_display_24 (.value(showhexa_3_out_9));  // open: dp
  Multiplexer #(.width(10)) multiplexer_80 (
    .in0({10{1'b0}}), .in1(instruction_reg_1_immed), .out(multiplexer_80_out), .sel(imload));
  // Probe on instruction_reg_1_condition
  // Probe on opcode_decoder_5_imm
  // Probe on opcode_decoder_5_imm
  // Probe on opcode_decoder_5_rd
  // Probe on opcode_decoder_5_rd
  // Probe on opcode_decoder_5_rs
  // Probe on opcode_decoder_5_rs
  // Probe on opcode_decoder_5_rt
  // Probe on opcode_decoder_5_rt
  // Probe on instruction_reg_1_dregsel
  // Probe on ssel
  // Probe on tsel
  Bit_Extender bit_extender_1 (.datain(multiplexer_80_out), .dataout(immed));
  OpCode_Decoder opcode_decoder_5 (
    .in_1(IR_ID), .Imm(opcode_decoder_5_imm), .Rd(opcode_decoder_5_rd), .Rs(opcode_decoder_5_rs),
    .Rt(opcode_decoder_5_rt));
  // Probe on r0
  // Probe on r1
  // Probe on r2
  // Probe on r3
  // Probe on r4
  // Probe on r5
  // Probe on r6
  // Probe on r7
  Multiplexer #(.width(3)) multiplexer_81 (.in0(instruction_reg_1_dregsel), .in1(3'b000), .out(dsel), .sel(bubble));
  Register_Bank register_bank_1 (
    .dselin(ma_to_wb_1_dregsel_out), .regval(regwrite), .dwrite(dwrite), .sselin(ma_to_wb_1_sregsel_out),
    .swrite(swrite), .tselin(ma_to_wb_1_tregsel_out), .twrite(twrite), .clock(CLK),
    .dselout(instruction_reg_1_dregsel), .Reset(Reset), .sselout(ssel), .tselout(tsel),
    .dreg(register_bank_1_dreg), .sreg(Rs), .treg(register_bank_1_treg), .r0(r0), .r1(r1), .r2(r2), .r3(r3),
    .r4(r4), .r5(r5), .r6(r6), .r7(r7));
  check_condition check_condition_1 (
    .C(C), .Z(Z), .V(V), .N(N), .condition(instruction_reg_1_condition), .cond_met(crnt_cond_met));
  Multiplexer multiplexer_82 (.in0(crnt_cond_met), .in1(1'b0), .out(cond_met), .sel(bubble));
  // Probe on register_bank_1_dreg
  // Probe on Rs
  // Probe on register_bank_1_treg
  and and_16 (and_16_out, crnt_cond_met, instruction_reg_1_set_flags);
  // Probe on ssel
  // Probe on tsel
  // Probe on imload
  // Probe on flgset
  // Probe on regwrite
  RAW_Check raw_check_1 (
    .dsel(dsel), .Clk(CLK), .Reset(Reset), .ssel(ssel), .tsel(tsel), .imload(imload), .flgset(flgset),
    .cond(cond_met), .dwrite(dwrite_ID), .sselForward(raw_check_1_sselforward),
    .tselForward(raw_check_1_tselforward), .frwrdFlags(flagsForward));
  // Probe on Rs
  // Probe on register_bank_1_treg
  xnor xnor_1 (prediction_crct, crnt_cond_met, prev_predicted_jump);
  // Probe on multiplexer_83_out
  // Probe on multiplexer_86_out
  // Probe on multiplexer_87_out
  Forwarding_Unit forwarding_unit_1 (
    .Clk(CLK), .Reset(Reset), .Rs(Rs), .Rt(register_bank_1_treg), .Rd3(multiplexer_87_out),
    .opcode(instruction_reg_1_opcode), .Rd1(multiplexer_83_out), .Rd2(multiplexer_86_out),
    .sselForward(raw_check_1_sselforward), .tselForward(raw_check_1_tselforward), .stall(stall),
    .bubble(bubble), .Rs_Out(forwarding_unit_1_rs_out), .Rt_Out(forwarding_unit_1_rt_out));
  // Probe on forwarding_unit_1_rs_out
  // Probe on forwarding_unit_1_rt_out
  // Probe on ma_to_wb_1_tregsel_out
  // Probe on ma_to_wb_1_sregsel_out
  ID_to_EX id_to_ex_1 (
    .Bubble(bubble), .Clk(CLK), .Reset(Reset), .instruction(IR_ID), .aluop(rom_1_data[10:7]),
    .negOp2(rom_1_data[11]), .rvrsOps(rom_1_data[12]), .datasel(rom_1_data[14:13]),
    .datawrite(rom_1_data[15]), .addrsel(rom_1_data[17:16]), .swrite(rom_1_data[21]),
    .twrite(rom_1_data[22]), .set_flags(and_16_out), .dwrite(dwrite_ID), .Rs(forwarding_unit_1_rs_out),
    .Rt(forwarding_unit_1_rt_out), .immed(multiplexer_80_out), .dregsel(instruction_reg_1_dregsel),
    .sregsel(ssel), .tregsel(tsel), .Rd(register_bank_1_dreg), .imload(imload), .regsrc(rom_1_data[19:18]),
    .op2sel(rom_1_data[6:5]), .datasel_out(id_to_ex_1_datasel_out), .datawrite_out(id_to_ex_1_datawrite_out),
    .addrsel_out(id_to_ex_1_addrsel_out), .dwrite_out(id_to_ex_1_dwrite_out),
    .swrite_out(id_to_ex_1_swrite_out), .twrite_out(id_to_ex_1_twrite_out), .negOp2_out(negOp2),
    .rvrsOps_out(rvrsOps), .aluop_out(aluop), .imload_out(id_to_ex_1_imload_out), .flags_set(flgset),
    .instruction_out(IR_EX), .dregselOut(id_to_ex_1_dregselout), .sregselOut(id_to_ex_1_sregselout),
    .tregselOut(id_to_ex_1_tregselout), .immedOut(id_to_ex_1_immedout), .regsrc_out(prevRegsrc),
    .Rs_Out(id_to_ex_1_rs_out), .Rt_Out(id_to_ex_1_rt_out), .op2sel_out(op2sel), .Rd_Out(id_to_ex_1_rd_out));
  // Probe on flgset
  // Probe on id_to_ex_1_dregselout
  // Probe on id_to_ex_1_sregselout
  // Probe on id_to_ex_1_tregselout
  // Probe on id_to_ex_1_rd_out
  // Probe on id_to_ex_1_rs_out
  // Probe on id_to_ex_1_rt_out
  // Probe on id_to_ex_1_immedout
  // Probe on id_to_ex_1_imload_out
  // Probe on ma_to_wb_1_dregsel_out
  ALU_Operands alu_operands_1 (
    .op2sel(op2sel), .negop2(negOp2), .rvrsOps(rvrsOps), .Rt(id_to_ex_1_rt_out),
    .immed({{22{1'b0}}, id_to_ex_1_immedout}), .Rs(id_to_ex_1_rs_out), .operand_1(alu_operands_1_operand_1),
    .operand_2(alu_operands_1_operand_2));
  // Probe on alu_operands_1_operand_1
  // Probe on alu_operands_1_operand_2
  Hex_Digit_Display hex_digit_display_25 (.value(showhexa_4_out_2));  // open: dp
  Hex_Digit_Display hex_digit_display_26 (.value(showhexa_4_out_3));  // open: dp
  ShowHexa showhexa_4 (
    .Data(IR_EX), .out_3(showhexa_4_out_3), .out_4(showhexa_4_out_4), .out_5(showhexa_4_out_5),
    .Digit(showhexa_4_digit), .out_7(showhexa_4_out_7), .out_8(showhexa_4_out_8), .out_9(showhexa_4_out_9),
    .out_2(showhexa_4_out_2));
  Hex_Digit_Display hex_digit_display_27 (.value(showhexa_4_out_4));  // open: dp
  Hex_Digit_Display hex_digit_display_28 (.value(showhexa_4_out_5));  // open: dp
  Hex_Digit_Display hex_digit_display_29 (.value(showhexa_4_digit));  // open: dp
  Hex_Digit_Display hex_digit_display_30 (.value(showhexa_4_out_7));  // open: dp
  // Probe on aluop
  Hex_Digit_Display hex_digit_display_31 (.value(showhexa_4_out_8));  // open: dp
  Hex_Digit_Display hex_digit_display_32 (.value(showhexa_4_out_9));  // open: dp
  ALU alu_1 (
    .A(alu_operands_1_operand_1), .B(alu_operands_1_operand_2), .aluop(aluop), .Result(alu_1_result),
    .Overflow(alu_1_overflow), .Carry(alu_1_carry), .Negative(alu_1_negative), .Zero(alu_1_zero));
  // Probe on alu_1_result
  Flags flags_1 (
    .flagsForward(flagsForward), .flgset(flgset), .CLK(CLK), .Reset(Reset), .N(alu_1_negative),
    .C(alu_1_carry), .Z(alu_1_zero), .V(alu_1_overflow), .N_out(N), .C_out(C), .Z_out(Z), .V_out(V));
  // Probe on opcode_decoder_6_imm
  // Probe on opcode_decoder_6_imm
  // Probe on opcode_decoder_6_rd
  // Probe on opcode_decoder_6_rd
  // Probe on opcode_decoder_6_rs
  // Probe on opcode_decoder_6_rs
  // Probe on opcode_decoder_6_rt
  // Probe on opcode_decoder_6_rt
  OpCode_Decoder opcode_decoder_6 (
    .in_1(IR_EX), .Imm(opcode_decoder_6_imm), .Rd(opcode_decoder_6_rd), .Rs(opcode_decoder_6_rs),
    .Rt(opcode_decoder_6_rt));
  Multiplexer #(.select(2), .width(32)) multiplexer_83 (
    .in0(id_to_ex_1_rs_out), .in1({{22{1'b0}}, id_to_ex_1_immedout}), .in3(alu_1_result),
    .out(multiplexer_83_out), .sel(prevRegsrc));  // open: in2
  EX_to_MA ex_to_ma_1 (
    .Clk(CLK), .Reset(Reset), .datasel(id_to_ex_1_datasel_out), .datawrite(id_to_ex_1_datawrite_out),
    .addrsel(id_to_ex_1_addrsel_out), .regsrc(prevRegsrc), .dwrite(id_to_ex_1_dwrite_out),
    .swrite(id_to_ex_1_swrite_out), .twrite(id_to_ex_1_twrite_out), .Rs(id_to_ex_1_rs_out),
    .Rt(id_to_ex_1_rt_out), .instruction(IR_EX), .immed({{22{1'b0}}, id_to_ex_1_immedout}),
    .dregsel(id_to_ex_1_dregselout), .sregsel(id_to_ex_1_sregselout), .tregsel(id_to_ex_1_tregselout),
    .Rd(id_to_ex_1_rd_out), .aluout(alu_1_result), .imload(id_to_ex_1_imload_out), .datasel_out(datasel),
    .datawrite_out(datawrite), .addrsel_out(addrsel), .dwrite_out(ex_to_ma_1_dwrite_out),
    .swrite_out(ex_to_ma_1_swrite_out), .twrite_out(ex_to_ma_1_twrite_out),
    .imload_out(ex_to_ma_1_imload_out), .Rs_Out(ex_to_ma_1_rs_out), .Rt_Out(ex_to_ma_1_rt_out),
    .instruction_out(IR_MA), .immed_Out(ex_to_ma_1_immed_out), .dregsel_Out(ex_to_ma_1_dregsel_out),
    .sregsel_Out(ex_to_ma_1_sregsel_out), .tregsel_Out(ex_to_ma_1_tregsel_out), .Rd_out(ex_to_ma_1_rd_out),
    .aluout_Out(ex_to_ma_1_aluout_out), .regsrc_out(prevRegsrc1));
  // Probe on ex_to_ma_1_dregsel_out
  // Probe on ex_to_ma_1_sregsel_out
  // Probe on ex_to_ma_1_tregsel_out
  // Probe on ex_to_ma_1_imload_out
  // Probe on ex_to_ma_1_rd_out
  // Probe on ex_to_ma_1_rs_out
  // Probe on ex_to_ma_1_rt_out
  // Probe on ex_to_ma_1_aluout_out
  // Probe on ex_to_ma_1_immed_out
  Multiplexer #(.select(2), .width(32)) multiplexer_84 (
    .in0(ex_to_ma_1_immed_out), .in1(ex_to_ma_1_aluout_out), .in2(ex_to_ma_1_rs_out),
    .out({multiplexer_84_out_2, multiplexer_84_out}), .sel(addrsel));  // open: in3
  // Probe on addrsel
  Multiplexer #(.select(2), .width(32)) multiplexer_85 (
    .in0(ex_to_ma_1_rs_out), .in1(ex_to_ma_1_rt_out), .in2(ex_to_ma_1_aluout_out), .in3(ex_to_ma_1_rd_out),
    .out(datain), .sel(datasel));
  // Probe on datasel
  Hex_Digit_Display hex_digit_display_33 (.value(showhexa_5_out_2));  // open: dp
  ShowHexa showhexa_5 (
    .Data(IR_MA), .out_3(showhexa_5_out_3), .out_4(showhexa_5_out_4), .out_5(showhexa_5_out_5),
    .Digit(showhexa_5_digit), .out_7(showhexa_5_out_7), .out_8(showhexa_5_out_8), .out_9(showhexa_5_out_9),
    .out_2(showhexa_5_out_2));
  and and_17 (and_17_out, FB_LED, datawrite);
  Button Clear (.out(Clear_out));
  Hex_Digit_Display hex_digit_display_34 (.value(showhexa_5_out_3));  // open: dp
  Hex_Digit_Display hex_digit_display_35 (.value(showhexa_5_out_4));  // open: dp
  // Probe on {multiplexer_84_out_2, multiplexer_84_out}
  // Probe on datain
  Address_Decoder ADDR_DEC (
    .Address({multiplexer_84_out_2, multiplexer_84_out}), .RAM(RAMSel), .FB_LED(FB_LED), .TTY(TTYSel),
    .output_3(ADDR_DEC_output_3));
  DotMatrix #(.inputtype("row"), .matrixcols(32), .matrixrows(16)) dotmatrix_1 (
    .row0(frame_buffer_16x32_1_out_6), .row1(frame_buffer_16x32_1_out_7), .row2(frame_buffer_16x32_1_out_8),
    .row3(frame_buffer_16x32_1_out_9), .row4(frame_buffer_16x32_1_out_10),
    .row5(frame_buffer_16x32_1_out_11), .row6(frame_buffer_16x32_1_out_12),
    .row7(frame_buffer_16x32_1_out_13), .row8(frame_buffer_16x32_1_out_14),
    .row9(frame_buffer_16x32_1_out_15), .row10(frame_buffer_16x32_1_out_16),
    .row11(frame_buffer_16x32_1_out_17), .row12(frame_buffer_16x32_1_out_18),
    .row13(frame_buffer_16x32_1_out_19), .row14(frame_buffer_16x32_1_out_20),
    .row15(frame_buffer_16x32_1_out_21));
  Frame_Buffer_16x32 frame_buffer_16x32_1 (
    .address(multiplexer_84_out), .store(and_17_out), .data(datain), .clock(CLK), .reset(Clear_out),
    .out_6(frame_buffer_16x32_1_out_6), .out_7(frame_buffer_16x32_1_out_7),
    .out_8(frame_buffer_16x32_1_out_8), .out_9(frame_buffer_16x32_1_out_9),
    .out_10(frame_buffer_16x32_1_out_10), .out_11(frame_buffer_16x32_1_out_11),
    .out_12(frame_buffer_16x32_1_out_12), .out_13(frame_buffer_16x32_1_out_13),
    .out_14(frame_buffer_16x32_1_out_14), .out_15(frame_buffer_16x32_1_out_15),
    .out_16(frame_buffer_16x32_1_out_16), .out_17(frame_buffer_16x32_1_out_17),
    .out_18(frame_buffer_16x32_1_out_18), .out_19(frame_buffer_16x32_1_out_19),
    .out_20(frame_buffer_16x32_1_out_20), .out_21(frame_buffer_16x32_1_out_21));
  Hex_Digit_Display hex_digit_display_36 (.value(showhexa_5_out_5));  // open: dp
  Hex_Digit_Display hex_digit_display_37 (.value(showhexa_5_digit));  // open: dp
  not not_13 (not_13_out, datawrite);
  Hex_Digit_Display hex_digit_display_38 (.value(showhexa_5_out_7));  // open: dp
  Hex_Digit_Display hex_digit_display_39 (.value(showhexa_5_out_8));  // open: dp
  and and_18 (and_18_out, RAMSel, datawrite);
  and and_19 (and_19_out, RAMSel, not_13_out);
  Hex_Digit_Display hex_digit_display_40 (.value(showhexa_5_out_9));  // open: dp
  RAM #(.addrWidth(16), .asyncread("true"), .dataWidth(32), .databus("bidir")) ram_11 (
    .addr({multiplexer_84_out_2[15:4], multiplexer_84_out}), .we(and_18_out), .oe(and_19_out), .clk(CLK),
    .data(ram_11_data));
  // Probe on opcode_decoder_7_rd
  // Probe on opcode_decoder_7_rd
  // Probe on opcode_decoder_7_rs
  // Probe on opcode_decoder_7_rs
  // Probe on opcode_decoder_7_rt
  // Probe on opcode_decoder_7_rt
  // Probe on opcode_decoder_7_imm
  // Probe on opcode_decoder_7_imm
  assign ram_11_data = datawrite ? datain : 32'bz;  // Controlled_Buffer controlled_buffer_1
  // Probe on datain[6:0]
  TTY #(.cols(16), .rows(4)) tty_3 (.data(datain[6:0]), .clk(CLK), .we(and_20_out), .clr(Clear_Screen_out));
  and and_20 (and_20_out, TTYSel, datawrite);
  Button Clear_Screen (.out(Clear_Screen_out));
  OpCode_Decoder opcode_decoder_7 (
    .in_1(IR_MA), .Imm(opcode_decoder_7_imm), .Rd(opcode_decoder_7_rd), .Rs(opcode_decoder_7_rs),
    .Rt(opcode_decoder_7_rt));
  Multiplexer #(.select(2), .width(32)) multiplexer_86 (
    .in0(ex_to_ma_1_rs_out), .in1(ex_to_ma_1_immed_out), .in2(ram_11_data), .in3(ex_to_ma_1_aluout_out),
    .out(multiplexer_86_out), .sel(prevRegsrc1));
  MA_to_WB ma_to_wb_1 (
    .Clk(CLK), .Reset(Reset), .regsrc(prevRegsrc1), .dwrite(ex_to_ma_1_dwrite_out),
    .swrite(ex_to_ma_1_swrite_out), .twrite(ex_to_ma_1_twrite_out), .instruction(IR_MA),
    .aluout(ex_to_ma_1_aluout_out), .Rs(ex_to_ma_1_rs_out), .immed(ex_to_ma_1_immed_out),
    .dregsel(ex_to_ma_1_dregsel_out), .sregsel(ex_to_ma_1_sregsel_out), .tregsel(ex_to_ma_1_tregsel_out),
    .operand(ram_11_data), .imload(ex_to_ma_1_imload_out), .dwrite_out(dwrite), .swrite_out(swrite),
    .twrite_out(twrite), .instruction_out(IR_WB), .aluout_Out(ma_to_wb_1_aluout_out),
    .Rs_Out(ma_to_wb_1_rs_out), .immed_Out(ma_to_wb_1_immed_out), .dregsel_Out(ma_to_wb_1_dregsel_out),
    .sregsel_Out(ma_to_wb_1_sregsel_out), .tregsel_Out(ma_to_wb_1_tregsel_out),
    .operand_Out(ma_to_wb_1_operand_out), .regsrc_out(regsrc));
  // Probe on ma_to_wb_1_dregsel_out
  // Probe on ma_to_wb_1_sregsel_out
  // Probe on ma_to_wb_1_tregsel_out
  // Probe on ma_to_wb_1_operand_out
  // Probe on ma_to_wb_1_rs_out
  // Probe on ma_to_wb_1_immed_out
  // Probe on ma_to_wb_1_aluout_out
  Multiplexer #(.select(2), .width(32)) multiplexer_87 (
    .in0(ma_to_wb_1_rs_out), .in1(ma_to_wb_1_immed_out), .in2(ma_to_wb_1_operand_out),
    .in3(ma_to_wb_1_aluout_out), .out(multiplexer_87_out), .sel(regsrc));
  Multiplexer #(.select(2), .width(32)) multiplexer_88 (
    .in0(ma_to_wb_1_rs_out), .in1(ma_to_wb_1_immed_out), .in2(ma_to_wb_1_operand_out),
    .in3(ma_to_wb_1_aluout_out), .out(regwrite), .sel(regsrc));
  // Probe on regsrc
  Hex_Digit_Display hex_digit_display_41 (.value(showhexa_6_out_2));  // open: dp
  ShowHexa showhexa_6 (
    .Data(IR_WB), .out_3(showhexa_6_out_3), .out_4(showhexa_6_out_4), .out_5(showhexa_6_out_5),
    .Digit(showhexa_6_digit), .out_7(showhexa_6_out_7), .out_8(showhexa_6_out_8), .out_9(showhexa_6_out_9),
    .out_2(showhexa_6_out_2));
  Hex_Digit_Display hex_digit_display_42 (.value(showhexa_6_out_3));  // open: dp
  Hex_Digit_Display hex_digit_display_43 (.value(showhexa_6_out_4));  // open: dp
  // Probe on opcode_decoder_8_imm
  // Probe on opcode_decoder_8_rd
  // Probe on opcode_decoder_8_rd
  // Probe on opcode_decoder_8_rs
  // Probe on opcode_decoder_8_rs
  // Probe on opcode_decoder_8_rt
  // Probe on opcode_decoder_8_rt
  Hex_Digit_Display hex_digit_display_44 (.value(showhexa_6_out_5));  // open: dp
  Hex_Digit_Display hex_digit_display_45 (.value(showhexa_6_digit));  // open: dp
  OpCode_Decoder opcode_decoder_8 (
    .in_1(IR_WB), .Imm(opcode_decoder_8_imm), .Rd(opcode_decoder_8_rd), .Rs(opcode_decoder_8_rs),
    .Rt(opcode_decoder_8_rt));
  // Probe on opcode_decoder_8_imm
  Hex_Digit_Display hex_digit_display_46 (.value(showhexa_6_out_7));  // open: dp
  Hex_Digit_Display hex_digit_display_47 (.value(showhexa_6_out_8));  // open: dp
  Hex_Digit_Display hex_digit_display_48 (.value(showhexa_6_out_9));  // open: dp

  // Other names for the same wires on the sheet: MSBc = corrPred; twoBit = MSB; br_addr[15:0] = Break_Addr;
  //   dbgadr = Stop_Addr; dbgcyc = Cycle; pcreg[15:0] = IFaddr

  // Notes on the sheet:
  //   Flags
  //   3bit GHR
  //   Debug
  //   MiMo - Microprogrammed CPU Model
  //   Imm_ID
  //   Rd_ID
  //   Rs_ID
  //   Rt_ID
  //   Address
  //   Jump outcome
  //   Jump prediction
  //   Incorrect Predictions
  //   v0 Pipelined
  //   ID
  //   previous PC+1
  //   Imm_EX
  //   Rd_EX
  //   Rs_EX
  //   Rt_EX
  //   Instruction RAM
  //   No predict
  //   (Branch not taken)
  //   Total Predictions
  //   2^2 Correlating Predictor
  //   8x2 CPT
  //   Flags
  //   Link Register
  //   8x2 LPT
  //   8x2 GPT
  //   EX
  //   1-bit
  //   1 bit prediction table
  //   2 bit prediction table
  //   Correlating Predictor using LHT
  //   Tournament Predictor
  //   2-bit
  //   Imm_MA
  //   Rd_MA
  //   Rs_MA
  //   Rt_MA
  //   Predictions Methods
  //   Correlating LHT
  //   If we previously made a prediction and it was wrong
  //   we need to flush the pipeline
  //   MA
  //   Correlating 2 by 2
  //   Imm_WB
  //   Rd_WB
  //   Rs_WB
  //   Rt_WB
  //   Tournament
  //   WB
  //   opcode
  //   IF
  //   cond_met
  //   contents of rom_1 (hex, n*v repeats v):
  //   0 100000 1c1500 1c0000 1c0080 1c1080 1c0100 1c0180 1c0200 1c0280 1c0300 1c0380 1c0400 1c0480 1c0a80
  //   80 0 380 280 1c0580 1c0600 1c0680 1c0780 1c0700 3 5 b 13 8000 180000 1a0000 190000 2e000 1e000
  //   Control ROM
  //   Not needed in this version
  //   IF
  //   ctrl signals
  //   ID
  //   Not needed in this version
  //   Imm_ID
  //   Rd_ID
  //   Rs_ID
  //   Rt_ID
  //   Registers
  //   Value in Rd
  //   Value in Rs
  //   Value in Rt
  //   regwrite from WB
  //   tsel from WB
  //   ssel from WB
  //   dsel from WB
  //   Rs
  //   Rt
  //   immed
  //   EX
  //   aluout
  //   Imm_EX
  //   Rd_EX
  //   Rs_EX
  //   Rt_EX
  //   Address
  //   Data
  //   MA
  //   Frame Buffer LED 16x32
  //   Imm_MA
  //   Rd_MA
  //   Rs_MA
  //   Rt_MA
  //   Operand RAM
  //   TTY
  //   Imm_WB
  //   Rd_WB
  //   Rs_WB
  //   Rt_WB
  //   WB
endmodule

module MiMo_Pipelined_v0 (
  input  Stop_Addr,
  input  Cycle,
  input  [15:0] Break_Addr
);

  wire ADDR_DEC_output_3, and_1_out, and_2_out, C, Clear_out, Clear_Screen_out, CLK, CLKin, cont, datawrite,
       dwrite, FB_LED, id_stage_1_cond_met, id_stage_1_set_flags, imload, instrUnload, load_LR, N, negOp2,
       not_1_out, RAMSel, Reset, rvrsOps, str_LR, swrite, TTYSel, twrite, V, Z;
  wire [1:0] addrsel, datasel, multiplexer_5_out, multiplexer_6_out, op2sel, pcsel, regsrc;
  wire [2:0] id_stage_1_dregs, id_stage_1_sregs, id_stage_1_tregs, shift_register_1_out,
       shift_register_2_out, shift_register_3_out;
  wire [3:0] aluop, showhexa_1_digit, showhexa_1_out_2, showhexa_1_out_3, showhexa_1_out_4, showhexa_1_out_5,
       showhexa_1_out_7, showhexa_1_out_8, showhexa_1_out_9, showhexa_2_digit, showhexa_2_out_2,
       showhexa_2_out_3, showhexa_2_out_4, showhexa_2_out_5, showhexa_2_out_7, showhexa_2_out_8,
       showhexa_2_out_9, showhexa_3_digit, showhexa_3_out_2, showhexa_3_out_3, showhexa_3_out_4,
       showhexa_3_out_5, showhexa_3_out_7, showhexa_3_out_8, showhexa_3_out_9, showhexa_4_digit,
       showhexa_4_out_2, showhexa_4_out_3, showhexa_4_out_4, showhexa_4_out_5, showhexa_4_out_7,
       showhexa_4_out_8, showhexa_4_out_9, showhexa_5_digit, showhexa_5_out_2, showhexa_5_out_3,
       showhexa_5_out_4, showhexa_5_out_5, showhexa_5_out_7, showhexa_5_out_8, showhexa_5_out_9;
  wire [6:0] id_stage_1_opcode;
  wire [7:0] adder_1_out, multiplexer_3_out;
  wire [9:0] ex_stage_1_immed1, immed, ma_stage_1_immed2;
  wire [15:0] counter_1_q, IFaddr;
  wire [31:0] datain, ex_stage_1_aluout, ex_stage_1_instruction2, ex_stage_1_rd1, ex_stage_1_rs1,
       ex_stage_1_rt1, frame_buffer_16x32_1_out_6, frame_buffer_16x32_1_out_7, frame_buffer_16x32_1_out_8,
       frame_buffer_16x32_1_out_9, frame_buffer_16x32_1_out_10, frame_buffer_16x32_1_out_11,
       frame_buffer_16x32_1_out_12, frame_buffer_16x32_1_out_13, frame_buffer_16x32_1_out_14,
       frame_buffer_16x32_1_out_15, frame_buffer_16x32_1_out_16, frame_buffer_16x32_1_out_17,
       frame_buffer_16x32_1_out_18, frame_buffer_16x32_1_out_19, frame_buffer_16x32_1_out_20,
       frame_buffer_16x32_1_out_21, id_stage_1_instruction1, Instruction_RAM_data, LR, ma_stage_1_addr,
       ma_stage_1_aluout1, ma_stage_1_instruction3, ma_stage_1_rs2, multiplexer_1_out, multiplexer_2_out,
       ram_1_data, register_bank_1_dreg, register_bank_1_r0, register_bank_1_r1, register_bank_1_r2,
       register_bank_1_r3, register_bank_1_r4, register_bank_1_r5, register_bank_1_r6, register_bank_1_r7,
       register_bank_1_treg, regwrite, Rs;
  wire [31:1] rom_1_data;
  wire [31:16] if_stage_1_address;

  Counter #(.max('hffff), .width(16)) counter_1 (
    .count(CLK), .Q(counter_1_q), .up(1'b1), .clk(CLK), .clr(Reset));  // open: load, D, carry
  Clock clock_1 (.out(CLKin));
  Button button_1 (.out(Reset));
  // Probe on counter_1_q
  // Probe on immed
  Multiplexer #(.width(32)) multiplexer_1 (.in0(Rs), .in1(LR), .out(multiplexer_1_out), .sel(str_LR));
  // Probe on pcsel
  LED u_N (.in(N));
  LED u_V (.in(V));
  LED u_Z (.in(Z));
  LED u_C (.in(C));
  // Probe on multiplexer_1_out
  Hex_Digit_Display hex_digit_display_1 (.value(showhexa_1_out_2));  // open: dp
  Hex_Digit_Display hex_digit_display_2 (.value(showhexa_1_out_3));  // open: dp
  ShowHexa showhexa_1 (
    .Data(multiplexer_2_out), .out_3(showhexa_1_out_3), .out_4(showhexa_1_out_4), .out_5(showhexa_1_out_5),
    .Digit(showhexa_1_digit), .out_7(showhexa_1_out_7), .out_8(showhexa_1_out_8), .out_9(showhexa_1_out_9),
    .out_2(showhexa_1_out_2));
  Hex_Digit_Display hex_digit_display_3 (.value(showhexa_2_out_2));  // open: dp
  Hex_Digit_Display hex_digit_display_4 (.value(showhexa_2_out_3));  // open: dp
  ShowHexa showhexa_2 (
    .Data({if_stage_1_address, IFaddr}), .out_3(showhexa_2_out_3), .out_4(showhexa_2_out_4),
    .out_5(showhexa_2_out_5), .Digit(showhexa_2_digit), .out_7(showhexa_2_out_7), .out_8(showhexa_2_out_8),
    .out_9(showhexa_2_out_9), .out_2(showhexa_2_out_2));
  Hex_Digit_Display hex_digit_display_5 (.value(showhexa_1_out_4));  // open: dp
  Hex_Digit_Display hex_digit_display_6 (.value(showhexa_1_out_5));  // open: dp
  Hex_Digit_Display hex_digit_display_7 (.value(showhexa_2_out_4));  // open: dp
  Hex_Digit_Display hex_digit_display_8 (.value(showhexa_2_out_5));  // open: dp
  Hex_Digit_Display hex_digit_display_9 (.value(showhexa_1_digit));  // open: dp
  Hex_Digit_Display hex_digit_display_10 (.value(showhexa_1_out_7));  // open: dp
  Hex_Digit_Display hex_digit_display_11 (.value(showhexa_2_digit));  // open: dp
  Hex_Digit_Display hex_digit_display_12 (.value(showhexa_2_out_7));  // open: dp
  Hex_Digit_Display hex_digit_display_13 (.value(showhexa_1_out_8));  // open: dp
  Hex_Digit_Display hex_digit_display_14 (.value(showhexa_1_out_9));  // open: dp
  Hex_Digit_Display hex_digit_display_15 (.value(showhexa_2_out_8));  // open: dp
  Hex_Digit_Display hex_digit_display_16 (.value(showhexa_2_out_9));  // open: dp
  IF_Stage if_stage_1 (
    .Clk(CLK), .Reset(Reset), .immed(immed), .Rs(multiplexer_1_out), .pcsel(pcsel),
    .address({if_stage_1_address, IFaddr}));
  RAM #(.addrWidth(16), .asyncread("true"), .dataWidth(32), .databus("bidir")) Instruction_RAM (
    .addr(IFaddr), .we(1'b0), .oe(1'b1), .clk(CLK), .data(Instruction_RAM_data));
  Button u_Cont (.out(cont));
  Register #(.width(32)) register_1 (.D({if_stage_1_address, IFaddr}), .en(load_LR), .Q(LR), .clk(CLK), .clr(Reset));
  // Probe on LR
  // DebugUnit debugunit_1: pin names not known; wires that end beside it: Break_Addr, IFaddr, Reset, CLKin, cont, Cycle, Stop_Addr, CLK
  Multiplexer #(.width(32)) multiplexer_2 (
    .in0(Instruction_RAM_data), .in1({32{1'b0}}), .out(multiplexer_2_out), .sel(instrUnload));
  // Probe on id_stage_1_dregs
  // Probe on id_stage_1_sregs
  // Probe on id_stage_1_tregs
  Hex_Digit_Display hex_digit_display_17 (.value(showhexa_3_out_2));  // open: dp
  Hex_Digit_Display hex_digit_display_18 (.value(showhexa_3_out_3));  // open: dp
  ShowHexa showhexa_3 (
    .Data(id_stage_1_instruction1), .out_3(showhexa_3_out_3), .out_4(showhexa_3_out_4),
    .out_5(showhexa_3_out_5), .Digit(showhexa_3_digit), .out_7(showhexa_3_out_7), .out_8(showhexa_3_out_8),
    .out_9(showhexa_3_out_9), .out_2(showhexa_3_out_2));
  Hex_Digit_Display hex_digit_display_19 (.value(showhexa_3_out_4));  // open: dp
  Hex_Digit_Display hex_digit_display_20 (.value(showhexa_3_out_5));  // open: dp
  // Probe on register_bank_1_r0
  // Probe on register_bank_1_r1
  // Probe on register_bank_1_r2
  // Probe on register_bank_1_r3
  // Probe on register_bank_1_r4
  // Probe on register_bank_1_r5
  // Probe on register_bank_1_r6
  // Probe on register_bank_1_r7
  Hex_Digit_Display hex_digit_display_21 (.value(showhexa_3_digit));  // open: dp
  Hex_Digit_Display hex_digit_display_22 (.value(showhexa_3_out_7));  // open: dp
  // Probe on id_stage_1_opcode
  Register_Bank register_bank_1 (
    .dselin(shift_register_1_out), .dwrite(dwrite), .sselin(shift_register_2_out), .swrite(swrite),
    .tselin(shift_register_3_out), .twrite(twrite), .clock(CLK), .dselout(id_stage_1_dregs), .Reset(Reset),
    .sselout(id_stage_1_sregs), .tselout(id_stage_1_tregs), .dreg(register_bank_1_dreg), .sreg(Rs),
    .treg(register_bank_1_treg), .r0(register_bank_1_r0), .r1(register_bank_1_r1), .r2(register_bank_1_r2),
    .r3(register_bank_1_r3), .r4(register_bank_1_r4), .r5(register_bank_1_r5), .r6(register_bank_1_r6),
    .r7(register_bank_1_r7));  // open: regval
  Shift_Register #(.length(3), .width(3)) shift_register_1 (
    .shift(CLK), .in(id_stage_1_dregs), .clk(CLK), .out(shift_register_1_out), .clr(Reset));  // open: load, d0, q0, d1, q1, d2, q2
  Shift_Register #(.length(3), .width(3)) shift_register_2 (
    .shift(CLK), .in(id_stage_1_sregs), .clk(CLK), .out(shift_register_2_out), .clr(Reset));  // open: load, d0, q0, d1, q1, d2, q2
  Shift_Register #(.length(3), .width(3)) shift_register_3 (
    .shift(CLK), .in(id_stage_1_tregs), .clk(CLK), .out(shift_register_3_out), .clr(Reset));  // open: load, d0, q0, d1, q1, d2, q2
  ID_Stage id_stage_1 (
    .Clk(CLK), .reset(Reset), .instruction(multiplexer_2_out), .N(N), .V(V), .Z(Z), .C(C), .immed(immed),
    .imload(imload), .dregs(id_stage_1_dregs), .sregs(id_stage_1_sregs), .tregs(id_stage_1_tregs),
    .cond_met(id_stage_1_cond_met), .set_flags(id_stage_1_set_flags), .opcode(id_stage_1_opcode),
    .instruction1(id_stage_1_instruction1));
  Hex_Digit_Display hex_digit_display_23 (.value(showhexa_3_out_8));  // open: dp
  Hex_Digit_Display hex_digit_display_24 (.value(showhexa_3_out_9));  // open: dp
  Adder adder_1 (.a({1'b0, id_stage_1_opcode}), .b(8'h1), .out(adder_1_out));  // open: cin, cout
  Multiplexer #(.width(8)) multiplexer_3 (
    .in0({8{1'b0}}), .in1(adder_1_out), .out(multiplexer_3_out), .sel(id_stage_1_cond_met));
  // Probe on immed
  ROM #(.dataWidth(32)) rom_1 (
    .addr(multiplexer_3_out), .data({rom_1_data[31:5], str_LR, load_LR, rom_1_data[2:1], instrUnload}));
  // Probe on register_bank_1_dreg
  // Probe on Rs
  // Probe on register_bank_1_treg
  // Probe on op2sel
  // Probe on aluop
  Hex_Digit_Display hex_digit_display_25 (.value(showhexa_4_out_2));  // open: dp
  ShowHexa showhexa_4 (
    .Data(ex_stage_1_instruction2), .out_3(showhexa_4_out_3), .out_4(showhexa_4_out_4),
    .out_5(showhexa_4_out_5), .Digit(showhexa_4_digit), .out_7(showhexa_4_out_7), .out_8(showhexa_4_out_8),
    .out_9(showhexa_4_out_9), .out_2(showhexa_4_out_2));
  Hex_Digit_Display hex_digit_display_26 (.value(showhexa_4_out_3));  // open: dp
  Hex_Digit_Display hex_digit_display_27 (.value(showhexa_4_out_4));  // open: dp
  Hex_Digit_Display hex_digit_display_28 (.value(showhexa_4_out_5));  // open: dp
  Hex_Digit_Display hex_digit_display_29 (.value(showhexa_4_digit));  // open: dp
  EX_Stage ex_stage_1 (
    .Clk(CLK), .flags_set(id_stage_1_set_flags), .reset(Reset), .Rd(register_bank_1_dreg), .Rs(Rs),
    .Rt(register_bank_1_treg), .op2sel(op2sel), .negOp2(negOp2), .aluop(aluop), .rvrsOps(rvrsOps),
    .immed(immed), .instruction1(id_stage_1_instruction1), .Rd1(ex_stage_1_rd1), .Rs1(ex_stage_1_rs1),
    .Rt1(ex_stage_1_rt1), .C(C), .Z(Z), .N(N), .V(V), .aluout(ex_stage_1_aluout), .immed1(ex_stage_1_immed1),
    .instruction2(ex_stage_1_instruction2));
  Hex_Digit_Display hex_digit_display_30 (.value(showhexa_4_out_7));  // open: dp
  Hex_Digit_Display hex_digit_display_31 (.value(showhexa_4_out_8));  // open: dp
  Hex_Digit_Display hex_digit_display_32 (.value(showhexa_4_out_9));  // open: dp
  // Probe on ex_stage_1_rd1
  // Probe on ex_stage_1_immed1
  // Probe on ex_stage_1_rs1
  // Probe on ex_stage_1_aluout
  Shift_Register #(.length(1), .width(4)) shift_register_4 (
    .shift(CLK), .in(rom_1_data[10:7]), .clk(CLK), .out(aluop), .clr(Reset));  // open: load, d0, q0
  Shift_Register #(.length(1)) shift_register_5 (
    .shift(CLK), .in(rom_1_data[11]), .clk(CLK), .out(negOp2), .clr(Reset));  // open: load, d0, q0
  Shift_Register #(.length(1)) shift_register_6 (
    .shift(CLK), .in(rom_1_data[12]), .clk(CLK), .out(rvrsOps), .clr(Reset));  // open: load, d0, q0
  Shift_Register #(.length(2), .width(2)) shift_register_7 (
    .shift(CLK), .in(rom_1_data[14:13]), .clk(CLK), .out(datasel), .clr(Reset));  // open: load, d0, q0, d1, q1
  Shift_Register #(.length(2)) shift_register_8 (
    .shift(CLK), .in(rom_1_data[15]), .clk(CLK), .out(datawrite), .clr(Reset));  // open: load, d0, q0, d1, q1
  Shift_Register #(.length(2), .width(2)) shift_register_9 (
    .shift(CLK), .in(rom_1_data[17:16]), .clk(CLK), .out(addrsel), .clr(Reset));  // open: load, d0, q0, d1, q1
  Shift_Register #(.length(3)) shift_register_10 (
    .shift(CLK), .in(rom_1_data[20]), .clk(CLK), .out(dwrite), .clr(Reset));  // open: load, d0, q0, d1, q1, d2, q2
  Shift_Register #(.length(3)) shift_register_11 (
    .shift(CLK), .in(rom_1_data[21]), .clk(CLK), .out(swrite), .clr(Reset));  // open: load, d0, q0, d1, q1, d2, q2
  Shift_Register #(.length(3)) shift_register_12 (
    .shift(CLK), .in(rom_1_data[22]), .clk(CLK), .out(twrite), .clr(Reset));  // open: load, d0, q0, d1, q1, d2, q2
  Multiplexer #(.select(2), .width(2)) multiplexer_4 (
    .in0({1'b0, imload}), .in1({1'b0, imload}), .in2(rom_1_data[2:1]), .in3(rom_1_data[2:1]), .out(pcsel),
    .sel(rom_1_data[2:1]));
  // Probe on ex_stage_1_rt1
  // Probe on addrsel
  // Probe on datasel
  Multiplexer #(.select(2), .width(2)) multiplexer_5 (
    .in0({1'b0, imload}), .in1({1'b0, imload}), .in2(rom_1_data[19:18]), .in3(rom_1_data[19:18]),
    .out(multiplexer_5_out), .sel(rom_1_data[19:18]));
  Hex_Digit_Display hex_digit_display_33 (.value(showhexa_5_out_2));  // open: dp
  Hex_Digit_Display hex_digit_display_34 (.value(showhexa_5_out_3));  // open: dp
  ShowHexa showhexa_5 (
    .Data(ma_stage_1_instruction3), .out_3(showhexa_5_out_3), .out_4(showhexa_5_out_4),
    .out_5(showhexa_5_out_5), .Digit(showhexa_5_digit), .out_7(showhexa_5_out_7), .out_8(showhexa_5_out_8),
    .out_9(showhexa_5_out_9), .out_2(showhexa_5_out_2));
  Multiplexer #(.select(2), .width(2)) multiplexer_6 (
    .in0({1'b0, imload}), .in1({1'b0, imload}), .in2(rom_1_data[6:5]), .in3(rom_1_data[6:5]),
    .out(multiplexer_6_out), .sel(rom_1_data[6:5]));
  Shift_Register #(.length(1), .width(2)) shift_register_13 (
    .shift(CLK), .in(multiplexer_6_out), .clk(CLK), .out(op2sel), .clr(Reset));  // open: load, d0, q0
  Shift_Register #(.length(3), .width(2)) shift_register_14 (
    .shift(CLK), .in(multiplexer_5_out), .clk(CLK), .out(regsrc), .clr(Reset));  // open: load, d0, q0, d1, q1, d2, q2
  Hex_Digit_Display hex_digit_display_35 (.value(showhexa_5_out_4));  // open: dp
  Hex_Digit_Display hex_digit_display_36 (.value(showhexa_5_out_5));  // open: dp
  Hex_Digit_Display hex_digit_display_37 (.value(showhexa_5_digit));  // open: dp
  Hex_Digit_Display hex_digit_display_38 (.value(showhexa_5_out_7));  // open: dp
  MA_Stage ma_stage_1 (
    .Clk(CLK), .reset(Reset), .immed1(ex_stage_1_immed1), .aluout(ex_stage_1_aluout), .Rd1(ex_stage_1_rd1),
    .Rs1(ex_stage_1_rs1), .Rt1(ex_stage_1_rt1), .addrsel(addrsel), .datasel(datasel),
    .instruction2(ex_stage_1_instruction2), .immed2(ma_stage_1_immed2), .aluout1(ma_stage_1_aluout1),
    .Rs2(ma_stage_1_rs2), .addr(ma_stage_1_addr), .datain(datain), .instruction3(ma_stage_1_instruction3));
  Hex_Digit_Display hex_digit_display_39 (.value(showhexa_5_out_8));  // open: dp
  Hex_Digit_Display hex_digit_display_40 (.value(showhexa_5_out_9));  // open: dp
  // Probe on ma_stage_1_immed2
  // Probe on ma_stage_1_addr
  // Probe on datain
  Address_Decoder ADDR_DEC (
    .Address(ma_stage_1_addr), .RAM(RAMSel), .FB_LED(FB_LED), .TTY(TTYSel), .output_3(ADDR_DEC_output_3));
  // Probe on ma_stage_1_aluout1
  and and_1 (and_1_out, RAMSel, datawrite);
  and and_2 (and_2_out, RAMSel, not_1_out);
  not not_1 (not_1_out, datawrite);
  // Probe on ma_stage_1_rs2
  Button Clear (.out(Clear_out));
  RAM #(.addrWidth(16), .asyncread("true"), .dataWidth(32), .databus("bidir")) ram_1 (
    .addr(ma_stage_1_addr[15:0]), .we(and_1_out), .oe(and_2_out), .clk(CLK), .data(ram_1_data));
  DotMatrix #(.inputtype("row"), .matrixcols(32), .matrixrows(16)) dotmatrix_1 (
    .row0(frame_buffer_16x32_1_out_6), .row1(frame_buffer_16x32_1_out_7), .row2(frame_buffer_16x32_1_out_8),
    .row3(frame_buffer_16x32_1_out_9), .row4(frame_buffer_16x32_1_out_10),
    .row5(frame_buffer_16x32_1_out_11), .row6(frame_buffer_16x32_1_out_12),
    .row7(frame_buffer_16x32_1_out_13), .row8(frame_buffer_16x32_1_out_14),
    .row9(frame_buffer_16x32_1_out_15), .row10(frame_buffer_16x32_1_out_16),
    .row11(frame_buffer_16x32_1_out_17), .row12(frame_buffer_16x32_1_out_18),
    .row13(frame_buffer_16x32_1_out_19), .row14(frame_buffer_16x32_1_out_20),
    .row15(frame_buffer_16x32_1_out_21));
  Frame_Buffer_16x32 frame_buffer_16x32_1 (
    .address(ma_stage_1_addr[3:0]), .store(1'b1), .data(datain), .clock(CLK), .reset(Clear_out),
    .out_6(frame_buffer_16x32_1_out_6), .out_7(frame_buffer_16x32_1_out_7),
    .out_8(frame_buffer_16x32_1_out_8), .out_9(frame_buffer_16x32_1_out_9),
    .out_10(frame_buffer_16x32_1_out_10), .out_11(frame_buffer_16x32_1_out_11),
    .out_12(frame_buffer_16x32_1_out_12), .out_13(frame_buffer_16x32_1_out_13),
    .out_14(frame_buffer_16x32_1_out_14), .out_15(frame_buffer_16x32_1_out_15),
    .out_16(frame_buffer_16x32_1_out_16), .out_17(frame_buffer_16x32_1_out_17),
    .out_18(frame_buffer_16x32_1_out_18), .out_19(frame_buffer_16x32_1_out_19),
    .out_20(frame_buffer_16x32_1_out_20), .out_21(frame_buffer_16x32_1_out_21));
  assign ram_1_data = datawrite ? datain : 32'bz;  // Controlled_Buffer controlled_buffer_1
  // Probe on regsrc
  // Probe on datain[6:0]
  TTY #(.cols(16), .rows(4)) tty_1 (.data(datain[6:0]), .clk(CLK), .we(1'b1), .clr(Clear_Screen_out));
  Button Clear_Screen (.out(Clear_Screen_out));
  // Probe on regwrite
  WB_Stage wb_stage_1 (
    .Clk(CLK), .reset(Reset), .immed2(ma_stage_1_immed2), .aluout1(ma_stage_1_aluout1), .Rs2(ma_stage_1_rs2),
    .operand(ram_1_data), .regsrc(regsrc), .regwrite(regwrite));

  // Other names for the same wires on the sheet: br_addr[15:0] = Break_Addr; dbgadr = Stop_Addr; dbgcyc = Cycle

  // Notes on the sheet:
  //   Flags
  //   Instruction going to ID
  //   Address
  //   MiMo - Microprogrammed CPU Model
  //   Link Register
  //   Debug
  //   Instruction RAM
  //   v0 Pipelined
  //   Instruction going to EX
  //   Registers
  //   opcode
  //   1st address is reserved
  //   cond_met
  //   contents of rom_1 (hex, n*v repeats v):
  //   4 100004 1c1504 1c0004 1c0084 1c1084 1c0104 1c0184 1c0204 1c0284 1c0304 1c0384 1c0404 1c0484 1c0a84
  //   84 4 384 284 1c0584 1c0604 1c0684 1c0784 1c0704 1 7 9 180004 8004 4 11
  //   Value in Rd
  //   Value in Rs
  //   Value in Rt
  //   Control ROM
  //   Instruction going to MA
  //   IF
  //   EX
  //   MA
  //   WB
  //   Instruction going to WB
  //   Operand RAM
  //   Frame Buffer LED 16x32
  //   TTY
endmodule

module IF_to_ID (
  input  Clk,
  input  Reset,
  input  [31:0] instruction,
  output [31:0] instructionOut
);

  Register #(.width(32)) register_1 (.D(instruction), .en(Clk), .clk(Clk), .clr(Reset));  // open: Q

  assign instructionOut = instruction;
endmodule

module ID_to_EX (
  input  Clk,
  input  Reset,
  input  Bubble,
  input  [9:0] immed,
  input  [2:0] dregsel,
  input  [2:0] sregsel,
  input  [2:0] tregsel,
  input  [31:0] Rd,
  input  [31:0] Rs,
  input  [31:0] Rt,
  input  set_flags,
  input  [31:0] instruction,
  input  imload,
  input  [1:0] op2sel,
  input  [3:0] aluop,
  input  negOp2,
  input  rvrsOps,
  input  [1:0] datasel,
  input  datawrite,
  input  [1:0] addrsel,
  input  [1:0] regsrc,
  input  dwrite,
  input  swrite,
  input  twrite,
  output [9:0] immedOut,
  output [2:0] dregselOut,
  output [2:0] sregselOut,
  output [2:0] tregselOut,
  output [31:0] Rd_Out,
  output [31:0] Rs_Out,
  output [31:0] Rt_Out,
  output flags_set,
  output [31:0] instruction_out,
  output imload_out,
  output [1:0] op2sel_out,
  output [3:0] aluop_out,
  output negOp2_out,
  output rvrsOps_out,
  output [1:0] datasel_out,
  output datawrite_out,
  output [1:0] addrsel_out,
  output [1:0] regsrc_out,
  output dwrite_out,
  output swrite_out,
  output twrite_out
);

  wire multiplexer_1_out;
  wire [1:0] multiplexer_7_out, multiplexer_8_out;
  wire [2:0] multiplexer_4_out, multiplexer_5_out, multiplexer_6_out;
  wire [9:0] multiplexer_3_out;
  wire [31:0] multiplexer_2_out;

  Multiplexer multiplexer_1 (.in0(set_flags), .in1(1'b0), .out(multiplexer_1_out), .sel(Bubble));
  Multiplexer #(.width(32)) multiplexer_2 (.in0(instruction), .in1({32{1'b0}}), .out(multiplexer_2_out), .sel(Bubble));
  Shift_Register #(.length(1), .width(4)) shift_register_1 (
    .shift(Clk), .in(aluop), .clk(Clk), .out(aluop_out), .clr(Reset));  // open: load, d0, q0
  Shift_Register #(.length(1)) shift_register_2 (
    .shift(Clk), .in(negOp2), .clk(Clk), .out(negOp2_out), .clr(Reset));  // open: load, d0, q0
  Shift_Register #(.length(1)) shift_register_3 (
    .shift(Clk), .in(rvrsOps), .clk(Clk), .out(rvrsOps_out), .clr(Reset));  // open: load, d0, q0
  Shift_Register #(.length(1), .width(2)) shift_register_4 (
    .shift(Clk), .in(datasel), .clk(Clk), .out(datasel_out), .clr(Reset));  // open: load, d0, q0
  Shift_Register #(.length(1)) shift_register_5 (
    .shift(Clk), .in(datawrite), .clk(Clk), .out(datawrite_out), .clr(Reset));  // open: load, d0, q0
  Shift_Register #(.length(1), .width(2)) shift_register_6 (
    .shift(Clk), .in(addrsel), .clk(Clk), .out(addrsel_out), .clr(Reset));  // open: load, d0, q0
  Shift_Register #(.length(1)) shift_register_7 (
    .shift(Clk), .in(dwrite), .clk(Clk), .out(dwrite_out), .clr(Reset));  // open: load, d0, q0
  Shift_Register #(.length(1)) shift_register_8 (
    .shift(Clk), .in(swrite), .clk(Clk), .out(swrite_out), .clr(Reset));  // open: load, d0, q0
  Shift_Register #(.length(1)) shift_register_9 (
    .shift(Clk), .in(twrite), .clk(Clk), .out(twrite_out), .clr(Reset));  // open: load, d0, q0
  Multiplexer #(.width(10)) multiplexer_3 (.in0(immed), .in1({10{1'b0}}), .out(multiplexer_3_out), .sel(Bubble));
  Multiplexer #(.width(3)) multiplexer_4 (.in0(dregsel), .in1(3'b000), .out(multiplexer_4_out), .sel(Bubble));
  Multiplexer #(.width(3)) multiplexer_5 (.in0(sregsel), .in1(3'b000), .out(multiplexer_5_out), .sel(Bubble));
  Multiplexer #(.width(3)) multiplexer_6 (.in0(tregsel), .in1(3'b000), .out(multiplexer_6_out), .sel(Bubble));
  Shift_Register #(.length(1)) shift_register_10 (
    .shift(Clk), .in(imload), .clk(Clk), .out(imload_out), .clr(Reset));  // open: load, d0, q0
  Register #(.width(10)) register_1 (.D(multiplexer_3_out), .en(Clk), .Q(immedOut), .clk(Clk), .clr(Reset));
  Register #(.width(3)) register_2 (.D(multiplexer_4_out), .en(Clk), .Q(dregselOut), .clk(Clk), .clr(Reset));
  Register #(.width(3)) register_3 (.D(multiplexer_5_out), .en(Clk), .Q(sregselOut), .clk(Clk), .clr(Reset));
  Register #(.width(3)) register_4 (.D(multiplexer_6_out), .en(Clk), .Q(tregselOut), .clk(Clk), .clr(Reset));
  Register #(.width(1)) register_5 (.D(multiplexer_1_out), .en(Clk), .Q(flags_set), .clk(Clk), .clr(Reset));
  Register #(.width(32)) register_6 (.D(multiplexer_2_out), .en(Clk), .Q(instruction_out), .clk(Clk), .clr(Reset));
  Multiplexer #(.select(2), .width(2)) multiplexer_7 (
    .in0({1'b0, imload}), .in1({1'b0, imload}), .in2(regsrc), .in3(regsrc), .out(multiplexer_7_out),
    .sel(regsrc));
  Register #(.width(32)) register_7 (.D(Rd), .en(Clk), .Q(Rd_Out), .clk(Clk), .clr(Reset));
  Register #(.width(32)) register_8 (.D(Rs), .en(Clk), .Q(Rs_Out), .clk(Clk), .clr(Reset));
  Register #(.width(32)) register_9 (.D(Rt), .en(Clk), .Q(Rt_Out), .clk(Clk), .clr(Reset));
  Multiplexer #(.select(2), .width(2)) multiplexer_8 (
    .in0({1'b0, imload}), .in1({1'b0, imload}), .in2(op2sel), .in3(op2sel), .out(multiplexer_8_out),
    .sel(op2sel));
  Shift_Register #(.length(1), .width(2)) shift_register_11 (
    .shift(Clk), .in(multiplexer_7_out), .clk(Clk), .out(regsrc_out), .clr(Reset));  // open: load, d0, q0
  Shift_Register #(.length(1), .width(2)) shift_register_12 (
    .shift(Clk), .in(multiplexer_8_out), .clk(Clk), .out(op2sel_out), .clr(Reset));  // open: load, d0, q0
endmodule

module EX_to_MA (
  input  Clk,
  input  Reset,
  input  [31:0] immed,
  input  [2:0] dregsel,
  input  [2:0] sregsel,
  input  [2:0] tregsel,
  input  [31:0] Rd,
  input  [31:0] Rs,
  input  [31:0] Rt,
  input  [31:0] aluout,
  input  [31:0] instruction,
  input  imload,
  input  [1:0] datasel,
  input  datawrite,
  input  [1:0] addrsel,
  input  [1:0] regsrc,
  input  dwrite,
  input  swrite,
  input  twrite,
  output [31:0] immed_Out,
  output [2:0] dregsel_Out,
  output [2:0] sregsel_Out,
  output [2:0] tregsel_Out,
  output [31:0] Rd_out,
  output [31:0] Rs_Out,
  output [31:0] Rt_Out,
  output [31:0] aluout_Out,
  output [31:0] instruction_out,
  output imload_out,
  output [1:0] datasel_out,
  output datawrite_out,
  output [1:0] addrsel_out,
  output [1:0] regsrc_out,
  output dwrite_out,
  output swrite_out,
  output twrite_out
);

  wire [1:0] multiplexer_1_out;

  Shift_Register #(.length(1), .width(2)) shift_register_1 (
    .shift(Clk), .in(datasel), .clk(Clk), .out(datasel_out), .clr(Reset));  // open: load, d0, q0
  Shift_Register #(.length(1)) shift_register_2 (
    .shift(Clk), .in(datawrite), .clk(Clk), .out(datawrite_out), .clr(Reset));  // open: load, d0, q0
  Shift_Register #(.length(1), .width(2)) shift_register_3 (
    .shift(Clk), .in(addrsel), .clk(Clk), .out(addrsel_out), .clr(Reset));  // open: load, d0, q0
  Shift_Register #(.length(1)) shift_register_4 (
    .shift(Clk), .in(dwrite), .clk(Clk), .out(dwrite_out), .clr(Reset));  // open: load, d0, q0
  Shift_Register #(.length(1)) shift_register_5 (
    .shift(Clk), .in(swrite), .clk(Clk), .out(swrite_out), .clr(Reset));  // open: load, d0, q0
  Shift_Register #(.length(1)) shift_register_6 (
    .shift(Clk), .in(twrite), .clk(Clk), .out(twrite_out), .clr(Reset));  // open: load, d0, q0
  Shift_Register #(.length(1)) shift_register_7 (
    .shift(Clk), .in(imload), .clk(Clk), .out(imload_out), .clr(Reset));  // open: load, d0, q0
  Register #(.width(32)) register_1 (.D(immed), .en(Clk), .Q(immed_Out), .clk(Clk), .clr(Reset));
  Register #(.width(3)) register_2 (.D(dregsel), .en(Clk), .Q(dregsel_Out), .clk(Clk), .clr(Reset));
  Register #(.width(3)) register_3 (.D(sregsel), .en(Clk), .Q(sregsel_Out), .clk(Clk), .clr(Reset));
  Register #(.width(3)) register_4 (.D(tregsel), .en(Clk), .Q(tregsel_Out), .clk(Clk), .clr(Reset));
  Register #(.width(32)) register_5 (.D(Rd), .en(Clk), .Q(Rd_out), .clk(Clk), .clr(Reset));
  Register #(.width(32)) register_6 (.D(Rs), .en(Clk), .Q(Rs_Out), .clk(Clk), .clr(Reset));
  Register #(.width(32)) register_7 (.D(Rt), .en(Clk), .Q(Rt_Out), .clk(Clk), .clr(Reset));
  Register #(.width(32)) register_8 (.D(aluout), .en(Clk), .Q(aluout_Out), .clk(Clk), .clr(Reset));
  Register #(.width(32)) register_9 (.D(instruction), .en(Clk), .Q(instruction_out), .clk(Clk), .clr(Reset));
  Multiplexer #(.select(2), .width(2)) multiplexer_1 (
    .in0({1'b0, imload}), .in1({1'b0, imload}), .in2(regsrc), .in3(regsrc), .out(multiplexer_1_out),
    .sel(regsrc));
  Shift_Register #(.length(1), .width(2)) shift_register_8 (
    .shift(Clk), .in(multiplexer_1_out), .clk(Clk), .out(regsrc_out), .clr(Reset));  // open: load, d0, q0
endmodule

module MA_to_WB (
  input  Clk,
  input  Reset,
  input  [31:0] immed,
  input  [2:0] dregsel,
  input  [2:0] sregsel,
  input  [2:0] tregsel,
  input  [31:0] operand,
  input  [31:0] Rs,
  input  [31:0] aluout,
  input  [31:0] instruction,
  input  imload,
  input  [1:0] regsrc,
  input  dwrite,
  input  swrite,
  input  twrite,
  output [31:0] immed_Out,
  output [2:0] dregsel_Out,
  output [2:0] sregsel_Out,
  output [2:0] tregsel_Out,
  output [31:0] operand_Out,
  output [31:0] Rs_Out,
  output [31:0] aluout_Out,
  output [31:0] instruction_out,
  output [1:0] regsrc_out,
  output dwrite_out,
  output swrite_out,
  output twrite_out
);

  wire [1:0] multiplexer_1_out;

  Shift_Register #(.length(1)) shift_register_1 (
    .shift(Clk), .in(dwrite), .clk(Clk), .out(dwrite_out), .clr(Reset));  // open: load, d0, q0
  Shift_Register #(.length(1)) shift_register_2 (
    .shift(Clk), .in(swrite), .clk(Clk), .out(swrite_out), .clr(Reset));  // open: load, d0, q0
  Shift_Register #(.length(1)) shift_register_3 (
    .shift(Clk), .in(twrite), .clk(Clk), .out(twrite_out), .clr(Reset));  // open: load, d0, q0
  Register #(.width(32)) register_1 (.D(aluout), .en(Clk), .Q(aluout_Out), .clk(Clk), .clr(Reset));
  Register #(.width(32)) register_2 (.D(instruction), .en(Clk), .Q(instruction_out), .clk(Clk), .clr(Reset));
  Register #(.width(32)) register_3 (.D(immed), .en(Clk), .Q(immed_Out), .clk(Clk), .clr(Reset));
  Register #(.width(3)) register_4 (.D(dregsel), .en(Clk), .Q(dregsel_Out), .clk(Clk), .clr(Reset));
  Register #(.width(3)) register_5 (.D(sregsel), .en(Clk), .Q(sregsel_Out), .clk(Clk), .clr(Reset));
  Register #(.width(3)) register_6 (.D(tregsel), .en(Clk), .Q(tregsel_Out), .clk(Clk), .clr(Reset));
  Register #(.width(32)) register_7 (.D(operand), .en(Clk), .Q(operand_Out), .clk(Clk), .clr(Reset));
  Register #(.width(32)) register_8 (.D(Rs), .en(Clk), .Q(Rs_Out), .clk(Clk), .clr(Reset));
  Multiplexer #(.select(2), .width(2)) multiplexer_1 (
    .in0({1'b0, imload}), .in1({1'b0, imload}), .in2(regsrc), .in3(regsrc), .out(multiplexer_1_out),
    .sel(regsrc));
  Shift_Register #(.length(1), .width(2)) shift_register_4 (
    .shift(Clk), .in(multiplexer_1_out), .clk(Clk), .out(regsrc_out), .clr(Reset));  // open: load, d0, q0
endmodule

module IF_Stage (
  input  Clk,
  input  Reset,
  input  [9:0] immed,
  input  [31:0] Rs,
  input  [1:0] pcsel,
  output [31:0] address
);

  // PC pc_1: pin names not known; wires that end beside it: 1'b1, Clk

  // Notes on the sheet:
  //   PC
endmodule

module ID_Stage (
  input  Clk,
  input  reset,
  input  [31:0] instruction,
  input  N,
  input  V,
  input  Z,
  input  C,
  output [9:0] immed,
  output imload,
  output [2:0] dregs,
  output [2:0] sregs,
  output [2:0] tregs,
  output cond_met,
  output set_flags,
  output [6:0] opcode,
  output [31:0] instruction1
);

  wire instruction_reg_1_set_flags;
  wire [3:0] instruction_reg_1_condition;
  wire [9:0] instruction_reg_1_immed;

  Instruction_Reg instruction_reg_1 (
    .reset(reset), .instruction(instruction), .clock(Clk), .immed(instruction_reg_1_immed), .dregsel(dregs),
    .sregsel(sregs), .tregsel(tregs), .condition(instruction_reg_1_condition),
    .set_flags(instruction_reg_1_set_flags), .imload(imload), .opcode(opcode));  // open: irload
  Multiplexer #(.width(10)) multiplexer_1 (.in0({10{1'b0}}), .in1(instruction_reg_1_immed), .out(immed), .sel(imload));
  // Probe on instruction_reg_1_condition
  // check_condition check_condition_1: pin names not known; wires that end beside it: C, Z, V, N, instruction_reg_1_condition, cond_met
  and and_1 (set_flags, cond_met, instruction_reg_1_set_flags);
  Register #(.width(32)) register_1 (.D(instruction), .en(Clk), .Q(instruction1), .clk(Clk), .clr(reset));

  // Notes on the sheet:
  //   Flags
endmodule

module EX_Stage (
  input  Clk,
  input  flags_set,
  input  reset,
  input  [31:0] Rd,
  input  [31:0] Rs,
  input  [31:0] Rt,
  input  [1:0] op2sel,
  input  negOp2,
  input  [3:0] aluop,
  input  rvrsOps,
  input  [9:0] immed,
  input  [31:0] instruction1,
  output [31:0] Rd1,
  output [31:0] Rs1,
  output [31:0] Rt1,
  output C,
  output Z,
  output N,
  output V,
  output [31:0] aluout,
  output [9:0] immed1,
  output [31:0] instruction2
);

  wire alu_1_p4, alu_1_p5, alu_1_p6, alu_1_p7, flgset;
  wire [31:0] multiplexer_1_out, multiplexer_2_out, multiplexer_3_out, multiplexer_4_out, not_1_out;

  Register #(.width(1)) register_1 (.D(flags_set), .en(Clk), .Q(flgset), .clk(Clk), .clr(reset));
  Register #(.width(32)) register_2 (.D(Rs), .en(Clk), .Q(Rs1), .clk(Clk), .clr(reset));
  Register #(.width(32)) register_3 (.D(Rt), .en(Clk), .Q(Rt1), .clk(Clk), .clr(reset));
  Register #(.width(10)) register_4 (.D(immed), .en(Clk), .Q(immed1), .clk(Clk), .clr(reset));
  Register #(.width(32)) register_5 (.D(instruction1), .en(Clk), .Q(instruction2), .clk(Clk), .clr(reset));
  Register #(.width(32)) register_6 (.D(Rd), .en(Clk), .Q(Rd1), .clk(Clk), .clr(reset));
  Multiplexer #(.select(2), .width(32)) multiplexer_1 (
    .in0(Rt1), .in1({{22{1'b0}}, immed1}), .in2({32{1'b0}}), .in3(32'h1), .out(multiplexer_1_out),
    .sel(op2sel));
  Multiplexer #(.width(32)) multiplexer_2 (
    .in0(multiplexer_1_out), .in1(not_1_out), .out(multiplexer_2_out), .sel(negOp2));
  assign not_1_out = ~multiplexer_1_out;  // NOT_Gate not_1, 32 bits wide
  Multiplexer #(.width(32)) multiplexer_3 (.in0(Rs1), .in1(multiplexer_2_out), .out(multiplexer_3_out), .sel(rvrsOps));
  Multiplexer #(.width(32)) multiplexer_4 (.in0(multiplexer_2_out), .in1(Rs1), .out(multiplexer_4_out), .sel(rvrsOps));
  // ALU alu_1: pin names not known; wires that end beside it: multiplexer_3_out, multiplexer_4_out, aluop, alu_1_p4, alu_1_p5, alu_1_p6, alu_1_p7, aluout
  Register #(.width(1)) register_7 (.D(alu_1_p4), .en(flgset), .Q(C), .clk(Clk), .clr(reset));
  Register #(.width(1)) register_8 (.D(alu_1_p5), .en(flgset), .Q(Z), .clk(Clk), .clr(reset));
  Register #(.width(1)) register_9 (.D(alu_1_p6), .en(flgset), .Q(N), .clk(Clk), .clr(reset));
  Register #(.width(1)) register_10 (.D(alu_1_p7), .en(flgset), .Q(V), .clk(Clk), .clr(reset));

  // Notes on the sheet:
  //   Here the set_flags is directly taken form the previous stage
  //   ALU
endmodule

module MA_Stage (
  input  Clk,
  input  reset,
  input  [9:0] immed1,
  input  [31:0] aluout,
  input  [31:0] Rd1,
  input  [31:0] Rs1,
  input  [31:0] Rt1,
  input  [1:0] addrsel,
  input  [1:0] datasel,
  input  [31:0] instruction2,
  output [9:0] immed2,
  output [31:0] aluout1,
  output [31:0] Rs2,
  output [31:0] addr,
  output [31:0] datain,
  output [31:0] instruction3
);

  wire [31:0] register_2_q, register_3_q;

  Register #(.width(32)) register_1 (.D(aluout), .en(Clk), .Q(aluout1), .clk(Clk), .clr(reset));
  Register #(.width(32)) register_2 (.D(Rd1), .en(Clk), .Q(register_2_q), .clk(Clk), .clr(reset));
  Register #(.width(32)) register_3 (.D(Rt1), .en(Clk), .Q(register_3_q), .clk(Clk), .clr(reset));
  Register #(.width(10)) register_4 (.D(immed1), .en(Clk), .Q(immed2), .clk(Clk), .clr(reset));
  Register #(.width(32)) register_5 (.D(Rs1), .en(Clk), .Q(Rs2), .clk(Clk), .clr(reset));
  Register #(.width(32)) register_6 (.D(instruction2), .en(Clk), .Q(instruction3), .clk(Clk), .clr(reset));
  Multiplexer #(.select(2), .width(32)) multiplexer_1 (
    .in0({{22{1'b0}}, immed2}), .in1(aluout1), .in2(Rs2), .out(addr), .sel(addrsel));  // open: in3
  Multiplexer #(.select(2), .width(32)) multiplexer_2 (
    .in0(register_2_q), .in1(register_3_q), .in2(aluout1), .out(datain), .sel(datasel));  // open: in3
endmodule

module WB_Stage (
  input  Clk,
  input  reset,
  input  [9:0] immed2,
  input  [31:0] aluout1,
  input  [31:0] Rs2,
  input  [31:0] operand,
  input  [1:0] regsrc,
  output [31:0] regwrite
);

  wire [9:0] register_1_q;
  wire [31:0] register_2_q, register_3_q, register_4_q;

  Register #(.width(10)) register_1 (.D(immed2), .en(Clk), .Q(register_1_q), .clk(Clk), .clr(reset));
  Register #(.width(32)) register_2 (.D(operand), .en(Clk), .Q(register_2_q), .clk(Clk), .clr(reset));
  Register #(.width(32)) register_3 (.D(aluout1), .en(Clk), .Q(register_3_q), .clk(Clk), .clr(reset));
  Register #(.width(32)) register_4 (.D(Rs2), .en(Clk), .Q(register_4_q), .clk(Clk), .clr(reset));
  Multiplexer #(.select(2), .width(32)) multiplexer_1 (
    .in0(register_4_q), .in1({{22{1'b0}}, register_1_q}), .in2(register_2_q), .in3(register_3_q),
    .out(regwrite), .sel(regsrc));
endmodule

module check_condition (
  input  C,
  input  Z,
  input  V,
  input  N,
  input  [3:0] condition,
  output cond_met
);

  wire and_1_out, and_2_out, and_3_out, and_4_out, and_5_out, and_6_out, and_7_out, and_8_out, and_9_out,
       and_10_out, and_11_out, and_12_out, and_13_out, and_14_out, and_15_out, and_16_out, and_17_out,
       and_18_out, decoder_1_out1, decoder_1_out2, decoder_1_out3, decoder_1_out4, decoder_1_out5,
       decoder_1_out6, decoder_1_out7, decoder_1_out8, decoder_1_out9, decoder_1_out10, decoder_1_out11,
       decoder_1_out12, decoder_1_out13, decoder_1_out14, decoder_1_out15, not_1_out, not_2_out, not_3_out,
       not_4_out, not_5_out, not_6_out, not_7_out, or_1_out, xnor_1_out, xnor_2_out, xor_1_out, xor_2_out;

  Decoder #(.enable("false"), .select(4)) decoder_1 (
    .out1(decoder_1_out1), .out2(decoder_1_out2), .out3(decoder_1_out3), .out4(decoder_1_out4),
    .out5(decoder_1_out5), .out6(decoder_1_out6), .out7(decoder_1_out7), .out8(decoder_1_out8),
    .out9(decoder_1_out9), .out10(decoder_1_out10), .out11(decoder_1_out11), .out12(decoder_1_out12),
    .out13(decoder_1_out13), .out14(decoder_1_out14), .out15(decoder_1_out15), .sel(condition));  // open: out0
  LED led_1 (.in(decoder_1_out10));
  LED led_2 (.in(decoder_1_out11));
  LED led_3 (.in(decoder_1_out12));
  LED led_4 (.in(decoder_1_out13));
  LED led_5 (.in(decoder_1_out14));
  LED led_6 (.in(decoder_1_out15));
  LED led_7 (.in(C));
  LED led_8 (.in(Z));
  LED led_9 (.in(V));
  LED led_10 (.in(decoder_1_out2));
  LED led_11 (.in(decoder_1_out3));
  LED led_12 (.in(decoder_1_out4));
  LED led_13 (.in(decoder_1_out5));
  LED led_14 (.in(decoder_1_out6));
  LED led_15 (.in(decoder_1_out7));
  LED led_16 (.in(decoder_1_out8));
  LED led_17 (.in(decoder_1_out9));
  and and_1 (and_1_out, decoder_1_out10, not_1_out);
  not not_1 (not_1_out, Z);
  and and_2 (and_2_out, decoder_1_out10, C);
  and and_3 (and_3_out, decoder_1_out11, not_2_out);
  not not_2 (not_2_out, C);
  and and_4 (and_4_out, decoder_1_out11, Z);
  xnor xnor_1 (xnor_1_out, N, V);
  xor xor_1 (xor_1_out, N, V);
  not not_3 (not_3_out, Z);
  xnor xnor_2 (xnor_2_out, N, V);
  xor xor_2 (xor_2_out, N, V);
  LED led_18 (.in(N));
  LED led_19 (.in(decoder_1_out1));
  and and_5 (and_5_out, decoder_1_out2, Z);
  and and_6 (and_6_out, decoder_1_out3, not_4_out);
  not not_4 (not_4_out, Z);
  and and_7 (and_7_out, decoder_1_out4, C);
  and and_8 (and_8_out, decoder_1_out5, not_5_out);
  not not_5 (not_5_out, C);
  and and_9 (and_9_out, decoder_1_out6, N);
  and and_10 (and_10_out, decoder_1_out7, not_6_out);
  not not_6 (not_6_out, N);
  and and_11 (and_11_out, decoder_1_out8, V);
  and and_12 (and_12_out, decoder_1_out9, not_7_out);
  not not_7 (not_7_out, V);
  and and_13 (and_13_out, and_1_out, and_2_out);
  and and_14 (and_14_out, and_3_out, and_4_out);
  and and_15 (and_15_out, decoder_1_out12, xnor_1_out);
  and and_16 (and_16_out, decoder_1_out13, xor_1_out);
  and and_17 (and_17_out, decoder_1_out14, not_3_out, xnor_2_out);
  and and_18 (and_18_out, decoder_1_out15, or_1_out);
  or or_1 (or_1_out, Z, xor_2_out);
  or or_2 (cond_met, decoder_1_out1, and_5_out, and_6_out, and_7_out, and_8_out, and_9_out, and_10_out, and_11_out, and_12_out, and_13_out, and_14_out, and_15_out, and_16_out, and_17_out, and_18_out);
  LED led_20 (.in(cond_met));

  // Notes on the sheet:
  //   Flags
  //   HI
  //   LS
  //   GE
  //   LT
  //   GT
  //   LE
  //   AL (Always)
  //   EQ
  //   NE
  //   CS
  //   CC
  //   MI
  //   PL
  //   VS
  //   VC
endmodule

module Instruction_Reg (
  input  [31:0] instruction,
  input  reset,
  input  clock,
  input  irload,
  output [9:0] immed,
  output [2:0] dregsel,
  output [2:0] sregsel,
  output [2:0] tregsel,
  output [3:0] condition,
  output set_flags,
  output imload,
  output [6:0] opcode
);

  Register #(.width(32)) register_1 (
    .D(instruction), .en(irload),
    .Q({opcode, imload, set_flags, condition, tregsel, sregsel, dregsel, immed}), .clk(clock), .clr(reset));
  // Probe on immed
  // Probe on dregsel
  // Probe on sregsel
  // Probe on tregsel
  // Probe on condition
  LED led_1 (.in(set_flags));
  LED led_2 (.in(imload));
  // Probe on nothing

  // Notes on the sheet:
  //   IR Logic
endmodule

module Register_Bank (
  input  [31:0] regval,
  input  Reset,
  input  clock,
  input  [2:0] dselout,
  input  [2:0] sselout,
  input  [2:0] tselout,
  input  dwrite,
  input  swrite,
  input  twrite,
  input  [2:0] dselin,
  input  [2:0] sselin,
  input  [2:0] tselin,
  output [31:0] r0,
  output [31:0] r1,
  output [31:0] r2,
  output [31:0] r3,
  output [31:0] r4,
  output [31:0] r5,
  output [31:0] r6,
  output [31:0] r7,
  output [31:0] dreg,
  output [31:0] sreg,
  output [31:0] treg
);

  wire demultiplexer_1_out0, demultiplexer_1_out1, demultiplexer_1_out2, demultiplexer_1_out3,
       demultiplexer_1_out4, demultiplexer_1_out5, demultiplexer_1_out6, demultiplexer_1_out7;

  Demultiplexer #(.select(3)) demultiplexer_1 (
    .out0(demultiplexer_1_out0), .out1(demultiplexer_1_out1), .out2(demultiplexer_1_out2),
    .out3(demultiplexer_1_out3), .out4(demultiplexer_1_out4), .out5(demultiplexer_1_out5),
    .out6(demultiplexer_1_out6), .out7(demultiplexer_1_out7), .in(dwrite), .sel(dselin));
  Demultiplexer #(.select(3)) demultiplexer_2 (
    .out0(demultiplexer_1_out0), .out1(demultiplexer_1_out1), .out2(demultiplexer_1_out2),
    .out3(demultiplexer_1_out3), .out4(demultiplexer_1_out4), .out5(demultiplexer_1_out5),
    .out6(demultiplexer_1_out6), .out7(demultiplexer_1_out7), .in(swrite), .sel(sselin));
  Demultiplexer #(.select(3)) demultiplexer_3 (
    .out0(demultiplexer_1_out0), .out1(demultiplexer_1_out1), .out2(demultiplexer_1_out2),
    .out3(demultiplexer_1_out3), .out4(demultiplexer_1_out4), .out5(demultiplexer_1_out5),
    .out6(demultiplexer_1_out6), .out7(demultiplexer_1_out7), .in(twrite), .sel(tselin));
  Register #(.width(32)) register_1 (.D(regval), .en(demultiplexer_1_out0), .Q(r0), .clk(clock), .clr(Reset));
  Register #(.width(32)) register_2 (.D(regval), .en(demultiplexer_1_out1), .Q(r1), .clk(clock), .clr(Reset));
  Register #(.width(32)) register_3 (.D(regval), .en(demultiplexer_1_out2), .Q(r2), .clk(clock), .clr(Reset));
  Register #(.width(32)) register_4 (.D(regval), .en(demultiplexer_1_out3), .Q(r3), .clk(clock), .clr(Reset));
  Register #(.width(32)) register_5 (.D(regval), .en(demultiplexer_1_out4), .Q(r4), .clk(clock), .clr(Reset));
  Register #(.width(32)) register_6 (.D(regval), .en(demultiplexer_1_out5), .Q(r5), .clk(clock), .clr(Reset));
  Register #(.width(32)) register_7 (.D(regval), .en(demultiplexer_1_out6), .Q(r6), .clk(clock), .clr(Reset));
  Register #(.width(32)) register_8 (.D(regval), .en(demultiplexer_1_out7), .Q(r7), .clk(clock), .clr(Reset));
  Multiplexer #(.select(3), .width(32)) multiplexer_1 (
    .in0(r0), .in1(r1), .in2(r2), .in3(r3), .in4(r4), .in5(r5), .in6(r6), .in7(r7), .out(dreg), .sel(dselout));
  Multiplexer #(.select(3), .width(32)) multiplexer_2 (
    .in0(r0), .in1(r1), .in2(r2), .in3(r3), .in4(r4), .in5(r5), .in6(r6), .in7(r7), .out(sreg), .sel(sselout));
  Multiplexer #(.select(3), .width(32)) multiplexer_3 (
    .in0(r0), .in1(r1), .in2(r2), .in3(r3), .in4(r4), .in5(r5), .in6(r6), .in7(r7), .out(treg), .sel(tselout));

  // Notes on the sheet:
  //   Register File
endmodule

module ALU (
  input  [31:0] A,
  input  [31:0] B,
  input  [3:0] aluop,
  output Overflow,
  output Carry,
  output Zero,
  output Negative,
  output [31:0] Result
);

  wire adder_1_cout, and_2_out, and_3_out, or_3_out, subtractor_1_bout, xnor_1_out, xnor_2_out, xor_2_out,
       xor_3_out;
  wire [15:0] decoder_1_out0;
  wire [31:0] adder_1_out, and_1_out, divider_1_out, divider_1_rem, multiplier_1_out, nand_1_out, nor_1_out,
       not_1_out, or_1_out, shifter_1_out, shifter_2_out, shifter_3_out, shifter_4_out, shifter_5_out,
       subtractor_1_out, xor_1_out;

  Adder #(.width(32)) adder_1 (.a(A), .b(B), .out(adder_1_out), .cin(1'b0), .cout(adder_1_cout));
  Subtractor #(.width(32)) subtractor_1 (.a(A), .b(B), .out(subtractor_1_out), .bin(1'b0), .bout(subtractor_1_bout));
  Multiplier #(.width(32)) multiplier_1 (.a(A), .b(B), .out(multiplier_1_out), .cin({32{1'b0}}));  // open: cout
  Divider #(.width(32)) divider_1 (.a(A), .b(B), .out(divider_1_out), .upper({32{1'b0}}), .rem(divider_1_rem));
  assign and_1_out = A & B;  // AND_Gate and_1, 32 bits wide
  assign or_1_out = A | B;  // OR_Gate or_1, 32 bits wide
  assign xor_1_out = A ^ B;  // XOR_Gate xor_1, 32 bits wide
  assign nand_1_out = ~(A & B);  // NAND_Gate nand_1, 32 bits wide
  assign nor_1_out = ~(A | B);  // NOR_Gate nor_1, 32 bits wide
  assign not_1_out = ~A;  // NOT_Gate not_1, 32 bits wide
  Shifter #(.width(32)) shifter_1 (.in(A), .\dist (B[4:0]), .out(shifter_1_out));
  Shifter #(.shift("lr"), .width(32)) shifter_2 (.in(A), .\dist (B[4:0]), .out(shifter_2_out));
  Shifter #(.shift("ar"), .width(32)) shifter_3 (.in(A), .\dist (B[4:0]), .out(shifter_3_out));
  Shifter #(.shift("rl"), .width(32)) shifter_4 (.in(A), .\dist (B[4:0]), .out(shifter_4_out));
  Shifter #(.shift("rr"), .width(32)) shifter_5 (.in(A), .\dist (B[4:0]), .out(shifter_5_out));
  xor xor_2 (xor_2_out, B[31], A[31]);
  and and_2 (and_2_out, xor_2_out, xnor_1_out);
  xnor xnor_1 (xnor_1_out, B[31], subtractor_1_out[31]);
  xnor xnor_2 (xnor_2_out, B[31], A[31]);
  xor xor_3 (xor_3_out, A[31], adder_1_out[31]);
  Multiplexer #(.select(4), .width(32)) multiplexer_1 (
    .in0(adder_1_out), .in1(subtractor_1_out), .in2(multiplier_1_out), .in3(divider_1_out),
    .in4(divider_1_rem), .in5(and_1_out), .in6(or_1_out), .in7(xor_1_out), .in8(nand_1_out), .in9(nor_1_out),
    .in10(not_1_out), .in11(shifter_1_out), .in12(shifter_2_out), .in13(shifter_3_out), .in14(shifter_4_out),
    .in15(shifter_5_out), .out({Negative, Result[30:0]}), .sel(aluop));
  and and_3 (and_3_out, xnor_2_out, xor_3_out);
  or or_2 (Overflow, and_2_out, and_3_out);
  Multiplexer #(.select(4)) multiplexer_2 (
    .in0(adder_1_cout), .in1(subtractor_1_bout), .in2(1'b0), .in3(1'b0), .in4(1'b0), .in5(1'b0), .in6(1'b0),
    .in7(1'b0), .in8(1'b0), .in9(1'b0), .in10(1'b0), .in11(1'b0), .in12(1'b0), .in13(1'b0), .in14(1'b0),
    .in15(1'b0), .out(Carry), .sel(aluop));
  or or_3 (or_3_out, Result[0], Result[1], Result[2], Result[3], Result[4], Result[5], Result[6], Result[7], Result[8], Result[9], Result[10], Result[11], Result[12], Result[13], Result[14], Result[15], Result[16], Result[17], Result[18], Result[19], Result[20], Result[21], Result[22], Result[23], Result[24], Result[25], Result[26], Result[27], Result[28], Result[29], Result[30], Negative);
  Decoder #(.enable("false"), .select(4)) decoder_1 (
    .out0(decoder_1_out0[0]), .out1(decoder_1_out0[1]), .out2(decoder_1_out0[2]), .out3(decoder_1_out0[3]),
    .out4(decoder_1_out0[4]), .out5(decoder_1_out0[5]), .out6(decoder_1_out0[6]), .out7(decoder_1_out0[7]),
    .out8(decoder_1_out0[8]), .out9(decoder_1_out0[9]), .out10(decoder_1_out0[10]),
    .out11(decoder_1_out0[11]), .out12(decoder_1_out0[12]), .out13(decoder_1_out0[13]),
    .out14(decoder_1_out0[14]), .out15(decoder_1_out0[15]), .sel(aluop));
  not not_2 (Zero, or_3_out);
  LED led_1 (.in(decoder_1_out0[0]));
  LED led_2 (.in(decoder_1_out0[1]));
  LED led_3 (.in(decoder_1_out0[2]));
  LED led_4 (.in(decoder_1_out0[3]));
  LED led_5 (.in(decoder_1_out0[4]));
  LED led_6 (.in(decoder_1_out0[5]));
  LED led_7 (.in(decoder_1_out0[6]));
  LED led_8 (.in(decoder_1_out0[7]));
  LED led_9 (.in(decoder_1_out0[8]));
  LED led_10 (.in(decoder_1_out0[9]));
  LED led_11 (.in(decoder_1_out0[10]));
  LED led_12 (.in(decoder_1_out0[11]));
  LED led_13 (.in(decoder_1_out0[12]));
  LED led_14 (.in(decoder_1_out0[13]));
  LED led_15 (.in(decoder_1_out0[14]));
  LED led_16 (.in(decoder_1_out0[15]));

  assign Result[31] = Negative;

  // Notes on the sheet:
  //   32-bit ALU
  //   B MSB
  //   A MSB
  //   B MSB
  //   A MSB
  //   A MSB != B MSB?
  //   A MSB = B MSB?
  //   B MSB = output MSB
  //   A/B MSB != output MSB
  //   ADD
  //   SUB
  //   MUL
  //   DIV
  //   REM
  //   AND
  //   OR
  //   XOR
  //   NAND
  //   NOR
  //   NOT
  //   LOGICAL LEFT
  //   LOGICAL RIGHT
  //   ARITHMETIC RIGHT
  //   ROTATE LEFT
  //   ROTATE RIGHT
endmodule

module PC (
  input  flush,
  input  should_predict,
  input  [31:0] imreg,
  input  pcload,
  input  clock,
  input  reset,
  input  [1:0] pcsel,
  output [31:0] prev_pc,
  output [31:0] pcout
);

  wire [31:0] adder_1_out, adder_2_out, multiplexer_1_out, multiplexer_2_out, subtractor_1_out;

  Adder #(.width(32)) adder_1 (.a(multiplexer_2_out), .b(32'h1), .out(adder_1_out));  // open: cin, cout
  Subtractor #(.width(32)) subtractor_1 (.a(imreg), .b(multiplexer_2_out), .out(subtractor_1_out));  // open: bin, bout
  Adder #(.width(32)) adder_2 (.a(multiplexer_2_out), .b(subtractor_1_out), .out(adder_2_out));  // open: cin, cout
  Multiplexer #(.select(2), .width(32)) multiplexer_1 (
    .in0(adder_1_out), .in1(imreg), .in2(adder_2_out), .out(multiplexer_1_out), .sel(pcsel));  // open: in3
  LED led_1 (.in(pcload));
  LED led_2 (.in(flush));
  Register #(.width(32)) register_1 (.D(multiplexer_1_out), .en(pcload), .Q(pcout), .clk(clock), .clr(reset));
  Multiplexer #(.width(32)) multiplexer_2 (.in0(pcout), .in1(prev_pc), .out(multiplexer_2_out), .sel(flush));
  Register #(.width(32)) register_2 (.D(pcout), .en(should_predict), .Q(prev_pc), .clk(clock), .clr(reset));
  LED led_3 (.in(should_predict));

  // Notes on the sheet:
  //   PC Logic
endmodule
module ShowHexa (
  input  [31:0] Data,
  output [3:0] out_2,
  output [3:0] out_3,
  output [3:0] out_4,
  output [3:0] out_5,
  output [3:0] Digit,
  output [3:0] out_7,
  output [3:0] out_8,
  output [3:0] out_9
);


  assign Digit = Data[15:12];
  assign out_2 = Data[31:28];
  assign out_3 = Data[27:24];
  assign out_4 = Data[23:20];
  assign out_5 = Data[19:16];
  assign out_7 = Data[11:8];
  assign out_8 = Data[7:4];
  assign out_9 = Data[3:0];
endmodule

module Frame_Buffer_16x32 (
  input  [3:0] address,
  input  store,
  input  [31:0] data,
  input  clock,
  input  reset,
  output [31:0] out_6,
  output [31:0] out_7,
  output [31:0] out_8,
  output [31:0] out_9,
  output [31:0] out_10,
  output [31:0] out_11,
  output [31:0] out_12,
  output [31:0] out_13,
  output [31:0] out_14,
  output [31:0] out_15,
  output [31:0] out_16,
  output [31:0] out_17,
  output [31:0] out_18,
  output [31:0] out_19,
  output [31:0] out_20,
  output [31:0] out_21
);

  wire demultiplexer_1_out0, demultiplexer_1_out1, demultiplexer_1_out2, demultiplexer_1_out3,
       demultiplexer_1_out4, demultiplexer_1_out5, demultiplexer_1_out6, demultiplexer_1_out7,
       demultiplexer_1_out8, demultiplexer_1_out9, demultiplexer_1_out10, demultiplexer_1_out11,
       demultiplexer_1_out12, demultiplexer_1_out13, demultiplexer_1_out14, demultiplexer_1_out15;

  Demultiplexer #(.select(4)) demultiplexer_1 (
    .out0(demultiplexer_1_out0), .out1(demultiplexer_1_out1), .out2(demultiplexer_1_out2),
    .out3(demultiplexer_1_out3), .out4(demultiplexer_1_out4), .out5(demultiplexer_1_out5),
    .out6(demultiplexer_1_out6), .out7(demultiplexer_1_out7), .out8(demultiplexer_1_out8),
    .out9(demultiplexer_1_out9), .out10(demultiplexer_1_out10), .out11(demultiplexer_1_out11),
    .out12(demultiplexer_1_out12), .out13(demultiplexer_1_out13), .out14(demultiplexer_1_out14),
    .out15(demultiplexer_1_out15), .in(store), .sel(address));
  Register #(.width(32)) register_1 (.D(data), .en(demultiplexer_1_out0), .Q(out_6), .clk(clock), .clr(reset));
  Register #(.width(32)) register_2 (.D(data), .en(demultiplexer_1_out1), .Q(out_7), .clk(clock), .clr(reset));
  Register #(.width(32)) register_3 (.D(data), .en(demultiplexer_1_out2), .Q(out_8), .clk(clock), .clr(reset));
  Register #(.width(32)) register_4 (.D(data), .en(demultiplexer_1_out3), .Q(out_9), .clk(clock), .clr(reset));
  Register #(.width(32)) register_5 (.D(data), .en(demultiplexer_1_out4), .Q(out_10), .clk(clock), .clr(reset));
  Register #(.width(32)) register_6 (.D(data), .en(demultiplexer_1_out5), .Q(out_11), .clk(clock), .clr(reset));
  Register #(.width(32)) register_7 (.D(data), .en(demultiplexer_1_out6), .Q(out_12), .clk(clock), .clr(reset));
  Register #(.width(32)) register_8 (.D(data), .en(demultiplexer_1_out7), .Q(out_13), .clk(clock), .clr(reset));
  Register #(.width(32)) register_9 (.D(data), .en(demultiplexer_1_out8), .Q(out_14), .clk(clock), .clr(reset));
  Register #(.width(32)) register_10 (.D(data), .en(demultiplexer_1_out9), .Q(out_15), .clk(clock), .clr(reset));
  Register #(.width(32)) register_11 (.D(data), .en(demultiplexer_1_out10), .Q(out_16), .clk(clock), .clr(reset));
  Register #(.width(32)) register_12 (.D(data), .en(demultiplexer_1_out11), .Q(out_17), .clk(clock), .clr(reset));
  Register #(.width(32)) register_13 (.D(data), .en(demultiplexer_1_out12), .Q(out_18), .clk(clock), .clr(reset));
  Register #(.width(32)) register_14 (.D(data), .en(demultiplexer_1_out13), .Q(out_19), .clk(clock), .clr(reset));
  Register #(.width(32)) register_15 (.D(data), .en(demultiplexer_1_out14), .Q(out_20), .clk(clock), .clr(reset));
  Register #(.width(32)) register_16 (.D(data), .en(demultiplexer_1_out15), .Q(out_21), .clk(clock), .clr(reset));
endmodule

module Address_Decoder (
  input  [31:0] Address,
  output RAM,
  output FB_LED,
  output TTY,
  output output_3
);

  Decoder #(.enable("false"), .select(2)) decoder_1 (
    .out0(RAM), .out1(FB_LED), .out2(TTY), .out3(output_3), .sel(Address[31:30]));
endmodule

module DebugUnit (
  input  reset,
  input  \continue ,
  input  clock,
  input  [15:0] IFaddr,
  input  [15:0] break_addr,
  input  break_on_addr,
  input  break_on_cycle,
  output clock_out
);

  wire and_1_out, and_2_out, nor_1_out, nor_2_out, or_1_out, shift_register_1_out, shift_register_1_q0;
  wire [15:0] xor_1_out;

  Shift_Register #(.length(2), .trigger("falling")) shift_register_1 (
    .in(\continue ), .clk(clock), .out(shift_register_1_out), .clr(reset), .q0(shift_register_1_q0));  // open: shift, load, d0, d1, q1
  assign xor_1_out = IFaddr ^ break_addr;  // XOR_Gate xor_1, 16 bits wide
  LED Addr (.in(break_on_addr));
  and and_1 (and_1_out, ~shift_register_1_out, shift_register_1_q0);  // AND_Gate
  nor nor_1 (nor_1_out, xor_1_out[15], xor_1_out[14], xor_1_out[13], xor_1_out[12], xor_1_out[11], xor_1_out[10], xor_1_out[9], xor_1_out[8], xor_1_out[6], xor_1_out[5], xor_1_out[4], xor_1_out[3], xor_1_out[2], xor_1_out[1], xor_1_out[0], xor_1_out[7]);
  and and_2 (and_2_out, nor_1_out, break_on_addr);
  LED Cycle (.in(break_on_cycle));
  nor nor_2 (nor_2_out, and_2_out, break_on_cycle);
  or or_1 (or_1_out, and_1_out, nor_2_out);
  LED Pass (.in(or_1_out));
  and and_3 (clock_out, clock, or_1_out);

  // Notes on the sheet:
  //   Breaks on PC = break_addr
  //   Breaks on each clock pulse
  //   Makes sure the 'continue' button only
  //   lets through 1 clock pulse, until you let go
  //   and press it again.
  //   Outputs 1 only on first cycle (shift bits are unequal).
  //   Debug Unit
  //   IF address = break_addr?
endmodule

module OpCode_Decoder (
  input  [31:0] in_1,
  output [9:0] Imm,
  output [2:0] Rd,
  output [2:0] Rs,
  output [2:0] Rt
);

  wire comparator_1_eq, comparator_2_eq, comparator_3_eq, comparator_3_gt, comparator_3_lt, or_1_out,
       or_2_out, or_3_out;
  wire [6:0] multiplexer_1_out;
  wire [31:0] decoder_1_out0;

  LED led_1 (.in(in_1[23]));
  LED led_2 (.in(in_1[24]));
  Comparator #(.width(7)) comparator_1 (.a(in_1[31:25]), .b(7'b0100000), .eq(comparator_1_eq));  // open: gt, lt
  Comparator #(.width(7)) comparator_2 (.a(in_1[31:25]), .b(7'b0100001), .eq(comparator_2_eq));  // open: gt, lt
  Comparator #(.width(4)) comparator_3 (
    .a(in_1[22:19]), .b(4'b0001), .gt(comparator_3_gt), .eq(comparator_3_eq), .lt(comparator_3_lt));
  LED led_3 (.in(comparator_3_eq));
  Multiplexer #(.width(7)) multiplexer_1 (.in0(in_1[31:25]), .in1(7'b0011100), .out(multiplexer_1_out), .sel(or_1_out));
  or or_1 (or_1_out, comparator_1_eq, comparator_2_eq);
  or or_2 (or_2_out, comparator_3_gt, comparator_3_lt);
  LED led_4 (.in(or_2_out));
  Decoder #(.enable("false"), .select(5)) decoder_1 (
    .out0(decoder_1_out0[0]), .out1(decoder_1_out0[1]), .out2(decoder_1_out0[2]), .out3(decoder_1_out0[3]),
    .out4(decoder_1_out0[4]), .out5(decoder_1_out0[5]), .out6(decoder_1_out0[6]), .out7(decoder_1_out0[7]),
    .out8(decoder_1_out0[8]), .out9(decoder_1_out0[9]), .out10(decoder_1_out0[10]),
    .out11(decoder_1_out0[11]), .out12(decoder_1_out0[12]), .out13(decoder_1_out0[13]),
    .out14(decoder_1_out0[14]), .out15(decoder_1_out0[15]), .out16(decoder_1_out0[16]),
    .out17(decoder_1_out0[17]), .out18(decoder_1_out0[18]), .out19(decoder_1_out0[19]),
    .out20(decoder_1_out0[20]), .out21(decoder_1_out0[21]), .out22(decoder_1_out0[22]),
    .out23(decoder_1_out0[23]), .out24(decoder_1_out0[24]), .out25(decoder_1_out0[25]),
    .out26(decoder_1_out0[26]), .out27(decoder_1_out0[27]), .out28(decoder_1_out0[28]),
    .out29(decoder_1_out0[29]), .out30(decoder_1_out0[30]), .out31(decoder_1_out0[31]),
    .sel(multiplexer_1_out[4:0]));
  LED led_5 (.in(decoder_1_out0[0]));
  LED led_6 (.in(decoder_1_out0[1]));
  LED led_7 (.in(decoder_1_out0[2]));
  LED led_8 (.in(decoder_1_out0[3]));
  LED led_9 (.in(decoder_1_out0[4]));
  LED led_10 (.in(decoder_1_out0[5]));
  LED led_11 (.in(decoder_1_out0[6]));
  LED led_12 (.in(decoder_1_out0[7]));
  LED led_13 (.in(decoder_1_out0[8]));
  LED led_14 (.in(decoder_1_out0[9]));
  LED led_15 (.in(decoder_1_out0[10]));
  LED led_16 (.in(decoder_1_out0[11]));
  LED led_17 (.in(decoder_1_out0[12]));
  LED led_18 (.in(decoder_1_out0[13]));
  LED led_19 (.in(decoder_1_out0[14]));
  LED led_20 (.in(decoder_1_out0[15]));
  LED led_21 (.in(decoder_1_out0[16]));
  LED led_22 (.in(decoder_1_out0[17]));
  LED led_23 (.in(decoder_1_out0[18]));
  LED led_24 (.in(decoder_1_out0[19]));
  LED led_25 (.in(decoder_1_out0[20]));
  LED led_26 (.in(decoder_1_out0[21]));
  LED led_27 (.in(decoder_1_out0[22]));
  LED led_28 (.in(decoder_1_out0[23]));
  LED led_29 (.in(decoder_1_out0[24]));
  LED led_30 (.in(decoder_1_out0[25]));
  LED led_31 (.in(decoder_1_out0[26]));
  LED led_32 (.in(decoder_1_out0[27]));
  LED led_33 (.in(decoder_1_out0[28]));
  or or_3 (or_3_out, decoder_1_out0[29], decoder_1_out0[30], decoder_1_out0[31]);
  LED led_34 (.in(or_3_out));

  assign Imm = in_1[9:0];
  assign Rd = in_1[12:10];
  assign Rs = in_1[15:13];
  assign Rt = in_1[18:16];

  // Notes on the sheet:
  //   SetFlags
  //   Immediate
  //   NOP 
  //   RTS
  //   MOV Rd, Rs/#Imm
  //   MVN Rd, Rs/#Imm
  //   ADD Rd, Rs, Rt/#imm 
  //   SUB Rd, Rs, Rt/#imm 
  //   RSB Rd, Rs, Rt/#Imm
  //   MUL Rd, Rs, Rt/#Imm
  //   DIV Rd, Rs, Rt/#Imm
  //   REM Rd, Rs, Rt/#Imm
  //   AND Rd, Rs, Rt/#Imm
  //   ORR Rd, Rs, Rt/#Imm
  //   EOR Rd, Rs, Rt/#Imm
  //   NAND Rd, Rs, Rt/#Imm
  //   NOR Rd, Rs, Rt/#Imm
  //   BIC Rd, Rs, Rt/#Imm
  //   CMP Rs, Rt/#Imm
  //   CMN Rs, Rt/#Imm
  //   TST Rs, Rt/#Imm
  //   TEQ Rs, Rt/#Imm
  //   LSL Rd, Rs, Rt/#Imm
  //   LSR Rd, Rs, Rt/#Imm
  //   ASR Rd, Rs, Rt/#Imm
  //   ROR Rd, Rs, Rt/#Imm
  //   ROL Rd, Rs, Rt/#Imm
  //   J Rs/#Imm/Label
  //   B Rs/#Imm/Label
  //   BL Label
  //   STR  Rd, #Imm
  //   No operation
  //   LDR  Rd, #Imm
  //   LDR [Rs]
  //   LDR [Rs, Rt/#imm]
  //   Rd <- Rs
  //   Rd <- !Rs
  //   Rd <- Rs + Rt
  //   Rd <- Rs - Rt
  //   Rd <- Rt - Rs
  //   Rd <- Rs * Rt
  //   Rd <- Rs / Rt
  //   Rd <- Rs % Rt
  //   Rd <- Rs AND Rt
  //   Rd <- Rs OR Rt
  //   Rd <- Rs XOR Rt
  //   Rd <- Rs NAND Rt
  //   Rd <- Rs NOR Rt
  //   Rd <- Rs AND !Rt
  //   Rd <- Rs << Rt
  //   Rd <- Rs >> Rt
  //   Rd <- Rs rolled right by Rt bits
  //   Rd <- Rs rolled left by Rt bits
  //   PC <- Rs/#Imm
  //   PC <- PC + Rs/#Imm
  //   Jump to subroutine
  //   Return from subroutine
  //   M[#Imm] <- Rd
  //   Rd <- M[#Imm]
  //   Rd <- M[Rs]
  //   Rd <- M[Rs + Rt/#Imm]
  //   Rs - Rt, then set flags, result isn't saved
  //   Rs + Rt, then set flags, result isn't saved
  //   Rs XOR Rt, then set flags, result isn't saved
  //   Rs AND Rt, then set flags, result isn't saved
  //   Rd <- Rs >> Rt (filled bits are the sign bit)
endmodule

module Flags (
  input  flgset,
  input  CLK,
  input  Reset,
  input  flagsForward,
  input  C,
  input  Z,
  input  N,
  input  V,
  output C_out,
  output Z_out,
  output N_out,
  output V_out
);

  wire register_1_q, register_2_q, register_3_q, register_4_q;

  LED led_1 (.in(flagsForward));
  LED led_2 (.in(flgset));
  Register #(.width(1)) register_1 (.D(C), .en(flgset), .Q(register_1_q), .clk(CLK), .clr(Reset));
  Register #(.width(1)) register_2 (.D(Z), .en(flgset), .Q(register_2_q), .clk(CLK), .clr(Reset));
  Register #(.width(1)) register_3 (.D(N), .en(flgset), .Q(register_3_q), .clk(CLK), .clr(Reset));
  Register #(.width(1)) register_4 (.D(V), .en(flgset), .Q(register_4_q), .clk(CLK), .clr(Reset));
  Multiplexer multiplexer_1 (.in0(register_1_q), .in1(C), .out(C_out), .sel(flagsForward));
  Multiplexer multiplexer_2 (.in0(register_2_q), .in1(Z), .out(Z_out), .sel(flagsForward));
  Multiplexer multiplexer_3 (.in0(register_3_q), .in1(N), .out(N_out), .sel(flagsForward));
  Multiplexer multiplexer_4 (.in0(register_4_q), .in1(V), .out(V_out), .sel(flagsForward));
  LED led_3 (.in(C_out));
  LED led_4 (.in(Z_out));
  LED led_5 (.in(N_out));
  LED led_6 (.in(V_out));
endmodule

module ALU_Operands (
  input  [1:0] op2sel,
  input  negop2,
  input  rvrsOps,
  input  [31:0] Rs,
  input  [31:0] Rt,
  input  [31:0] immed,
  output [31:0] operand_1,
  output [31:0] operand_2
);

  wire decoder_1_out0, decoder_1_out1, decoder_1_out2, decoder_1_out3, multiplexer_2_out, multiplexer_4_out,
       multiplexer_5_out, multiplexer_6_out, multiplexer_7_out, multiplexer_10_out, multiplexer_11_out,
       multiplexer_12_out, multiplexer_13_out, multiplexer_14_out;
  wire [31:0] multiplexer_1_out, multiplexer_3_out, not_1_out;

  Multiplexer #(.select(2), .width(32)) multiplexer_1 (
    .in0(Rt), .in1(immed), .in2({32{1'b0}}), .in3(32'h1), .out(multiplexer_1_out), .sel(op2sel));
  // Probe on op2sel
  Decoder #(.enable("false"), .select(2)) decoder_1 (
    .out0(decoder_1_out0), .out1(decoder_1_out1), .out2(decoder_1_out2), .out3(decoder_1_out3), .sel(op2sel));
  assign not_1_out = ~multiplexer_1_out;  // NOT_Gate not_1, 32 bits wide
  Multiplexer multiplexer_2 (.in0(1'b1), .in1(1'b0), .out(multiplexer_2_out), .sel(rvrsOps));
  Multiplexer #(.width(32)) multiplexer_3 (
    .in0(multiplexer_1_out), .in1(not_1_out), .out(multiplexer_3_out), .sel(negop2));
  Multiplexer multiplexer_4 (.in0(1'b0), .in1(decoder_1_out0), .out(multiplexer_4_out), .sel(rvrsOps));
  Multiplexer multiplexer_5 (.in0(1'b0), .in1(decoder_1_out1), .out(multiplexer_5_out), .sel(rvrsOps));
  Multiplexer multiplexer_6 (.in0(1'b0), .in1(decoder_1_out2), .out(multiplexer_6_out), .sel(rvrsOps));
  Multiplexer multiplexer_7 (.in0(1'b0), .in1(decoder_1_out3), .out(multiplexer_7_out), .sel(rvrsOps));
  Multiplexer #(.width(32)) multiplexer_8 (.in0(Rs), .in1(multiplexer_3_out), .out(operand_1), .sel(rvrsOps));
  Multiplexer #(.width(32)) multiplexer_9 (.in0(multiplexer_3_out), .in1(Rs), .out(operand_2), .sel(rvrsOps));
  LED led_1 (.in(multiplexer_2_out));
  LED led_2 (.in(multiplexer_4_out));
  LED led_3 (.in(multiplexer_5_out));
  LED led_4 (.in(multiplexer_6_out));
  LED led_5 (.in(multiplexer_7_out));
  Multiplexer multiplexer_10 (.in0(1'b0), .in1(1'b1), .out(multiplexer_10_out), .sel(rvrsOps));
  Multiplexer multiplexer_11 (.in0(decoder_1_out0), .in1(1'b0), .out(multiplexer_11_out), .sel(rvrsOps));
  Multiplexer multiplexer_12 (.in0(decoder_1_out1), .in1(1'b0), .out(multiplexer_12_out), .sel(rvrsOps));
  Multiplexer multiplexer_13 (.in0(decoder_1_out2), .in1(1'b0), .out(multiplexer_13_out), .sel(rvrsOps));
  Multiplexer multiplexer_14 (.in0(decoder_1_out3), .in1(1'b0), .out(multiplexer_14_out), .sel(rvrsOps));
  LED led_6 (.in(multiplexer_10_out));
  LED led_7 (.in(multiplexer_11_out));
  LED led_8 (.in(multiplexer_12_out));
  LED led_9 (.in(multiplexer_13_out));
  LED led_10 (.in(multiplexer_14_out));

  // Notes on the sheet:
  //   Operand 1
  //   Rs
  //   Rt
  //   immed
  //   const0
  //   const1
  //   Operand 2
  //   Rs
  //   Rt
  //   immed
  //   const0
  //   const1
endmodule

module RAW_Check (
  input  Clk,
  input  Reset,
  input  [2:0] ssel,
  input  [2:0] tsel,
  input  imload,
  input  [2:0] dsel,
  input  cond,
  input  flgset,
  input  dwrite,
  output [1:0] sselForward,
  output frwrdFlags,
  output [1:0] tselForward
);

  wire and_1_out, and_2_out, and_3_out, and_5_out, and_6_out, and_8_out, and_9_out, comparator_1_eq,
       comparator_2_eq, comparator_3_eq, comparator_4_eq, comparator_5_eq, comparator_6_eq, not_1_out,
       not_2_out, not_3_out, not_4_out, not_5_out, not_6_out, not_7_out, not_8_out, not_9_out, prevCond,
       prevCond1, prevCond2, prevDWrite, prevDWrite1, prevDWrite2;
  wire [2:0] and_4_out, and_7_out, prevRd, prevRd1, prevRd2;

  Register #(.width(1)) register_1 (.D(cond), .en(1'b1), .Q(prevCond), .clk(Clk), .clr(Reset));
  // Probe on prevCond
  Register #(.width(1)) register_2 (.D(dwrite), .en(1'b1), .Q(prevDWrite), .clk(Clk), .clr(Reset));
  // Probe on prevDWrite
  Register #(.width(3)) register_3 (.D(dsel), .en(1'b1), .Q(prevRd), .clk(Clk), .clr(Reset));
  // Probe on prevRd
  Register #(.width(1)) register_4 (.D(prevCond), .en(1'b1), .Q(prevCond1), .clk(Clk), .clr(Reset));
  Register #(.width(1)) register_5 (.D(prevDWrite), .en(1'b1), .Q(prevDWrite1), .clk(Clk), .clr(Reset));
  Register #(.width(3)) register_6 (.D(prevRd), .en(1'b1), .Q(prevRd1), .clk(Clk), .clr(Reset));
  Register #(.width(3)) register_7 (.D(prevRd1), .en(1'b1), .Q(prevRd2), .clk(Clk), .clr(Reset));
  // Probe on prevRd1
  Register #(.width(1)) register_8 (.D(prevCond1), .en(1'b1), .Q(prevCond2), .clk(Clk), .clr(Reset));
  // Probe on prevCond2
  // Probe on prevCond1
  Register #(.width(1)) register_9 (.D(prevDWrite1), .en(1'b1), .Q(prevDWrite2), .clk(Clk), .clr(Reset));
  // Probe on prevDWrite2
  // Probe on prevDWrite1
  // Probe on prevRd2
  Comparator #(.mode("unsigned"), .width(3)) comparator_1 (.a(prevRd), .b(tsel), .eq(comparator_1_eq));  // open: gt, lt
  Comparator #(.mode("unsigned"), .width(3)) comparator_2 (
    .a(prevRd1), .b(tsel), .eq(comparator_2_eq));  // open: gt, lt
  Comparator #(.mode("unsigned"), .width(3)) comparator_3 (
    .a(prevRd2), .b(tsel), .eq(comparator_3_eq));  // open: gt, lt
  Comparator #(.mode("unsigned"), .width(3)) comparator_4 (.a(prevRd), .b(ssel), .eq(comparator_4_eq));  // open: gt, lt
  Comparator #(.mode("unsigned"), .width(3)) comparator_5 (
    .a(prevRd1), .b(ssel), .eq(comparator_5_eq));  // open: gt, lt
  Comparator #(.mode("unsigned"), .width(3)) comparator_6 (
    .a(prevRd2), .b(ssel), .eq(comparator_6_eq));  // open: gt, lt
  and and_1 (and_1_out, comparator_1_eq, not_1_out);
  not not_1 (not_1_out, imload);
  and and_2 (and_2_out, comparator_2_eq, not_2_out);
  not not_2 (not_2_out, imload);
  and and_3 (and_3_out, comparator_3_eq, not_3_out);
  not not_3 (not_3_out, imload);
  and and_4 (and_4_out[0], comparator_4_eq, prevDWrite, prevCond);
  and and_5 (and_5_out, comparator_5_eq, prevDWrite1, prevCond1);
  and and_6 (and_6_out, comparator_6_eq, prevDWrite2, prevCond2);
  and and_7 (and_7_out[0], and_1_out, prevDWrite, prevCond);
  and and_8 (and_8_out, and_2_out, prevDWrite1, prevCond1);
  and and_9 (and_9_out, and_3_out, prevDWrite2, prevCond2);
  not not_4 (not_4_out, and_4_out[0]);
  not not_5 (not_5_out, and_4_out[0]);
  not not_6 (not_6_out, and_7_out[0]);
  not not_7 (not_7_out, and_7_out[0]);
  and and_10 (and_4_out[1], not_4_out, and_5_out);
  and and_11 (and_7_out[1], not_6_out, and_8_out);
  not not_8 (not_8_out, and_4_out[1]);
  and and_12 (and_4_out[2], not_8_out, not_5_out, and_6_out);
  not not_9 (not_9_out, and_7_out[1]);
  and and_13 (and_7_out[2], not_9_out, not_7_out, and_9_out);
  Multiplexer #(.select(3), .width(2)) multiplexer_1 (
    .in0(2'b00), .in1(2'b01), .in2(2'b10), .in4(2'b11), .out(sselForward), .sel(and_4_out));  // open: in3, in5, in6, in7
  Multiplexer #(.select(3), .width(2)) multiplexer_2 (
    .in0(2'b00), .in1(2'b01), .in2(2'b10), .in4(2'b11), .out(tselForward), .sel(and_7_out));  // open: in3, in5, in6, in7

  assign frwrdFlags = flgset;

  // Other names for the same wires on the sheet: Rs[2:0] = ssel; Rt[2:0] = tsel

  // Notes on the sheet:
  //   - the condition for the given previous instruction is met
  //   - the dwrite signal for the given previous instruction is equal to 1
  //   ((Rd = Rs) OR (Rd = Rt AND imload=0)) AND dwrite=1 AND cond_met = 1 
  //   2. The flags were set in the previous instruction, so they have not been saved yet (flgset=1)
  //   Read After Write (RAW) occurs under multiple conditions for any of the 3 previous instructions:
  //   1. The destination register in any of the 3 previous instructions is the same register used for the second or third register in the current instruction, while
endmodule

module Forwarding_Unit (
  input  Clk,
  input  [1:0] sselForward,
  input  Reset,
  input  [1:0] tselForward,
  input  [6:0] opcode,
  input  [31:0] Rs,
  input  [31:0] Rt,
  input  [31:0] Rd1,
  input  [31:0] Rd2,
  input  [31:0] Rd3,
  output stall,
  output bubble,
  output [31:0] Rs_Out,
  output [31:0] Rt_Out
);

  wire comparator_1_gt, comparator_2_eq, comparator_3_eq, decoder_1_out0, decoder_1_out1, decoder_1_out2,
       decoder_1_out3, decoder_2_out0, decoder_2_out1, decoder_2_out2, decoder_2_out3, or_1_out;
  wire [6:0] register_1_q;
  wire [31:0] multiplexer_1_out, multiplexer_2_out;

  Register #(.width(7)) register_1 (.D(opcode), .en(Clk), .Q(register_1_q), .clk(Clk), .clr(Reset));
  Multiplexer #(.width(32)) multiplexer_1 (.in0(Rs), .in1({32{1'b0}}), .out(multiplexer_1_out), .sel(bubble));
  Multiplexer #(.width(32)) multiplexer_2 (.in0(Rt), .in1({32{1'b0}}), .out(multiplexer_2_out), .sel(bubble));
  Comparator #(.width(7)) comparator_1 (.a(register_1_q), .b(7'b0011100), .gt(comparator_1_gt));  // open: eq, lt
  Comparator #(.width(2)) comparator_2 (.a(2'b01), .b(sselForward), .eq(comparator_2_eq));  // open: gt, lt
  Comparator #(.width(2)) comparator_3 (.a(2'b01), .b(tselForward), .eq(comparator_3_eq));  // open: gt, lt
  Multiplexer #(.select(2), .width(32)) multiplexer_3 (
    .in0(multiplexer_1_out), .in1(Rd1), .in2(Rd2), .in3(Rd3), .out(Rs_Out), .sel(sselForward));
  Multiplexer #(.select(2), .width(32)) multiplexer_4 (
    .in0(multiplexer_2_out), .in1(Rd1), .in2(Rd2), .in3(Rd3), .out(Rt_Out), .sel(tselForward));
  and and_1 (bubble, comparator_1_gt, or_1_out);
  or or_1 (or_1_out, comparator_2_eq, comparator_3_eq);
  Decoder #(.enable("false"), .select(2)) decoder_1 (
    .out0(decoder_1_out0), .out1(decoder_1_out1), .out2(decoder_1_out2), .out3(decoder_1_out3),
    .sel(sselForward));
  Decoder #(.enable("false"), .select(2)) decoder_2 (
    .out0(decoder_2_out0), .out1(decoder_2_out1), .out2(decoder_2_out2), .out3(decoder_2_out3),
    .sel(tselForward));
  LED led_1 (.in(decoder_1_out0));
  LED led_2 (.in(decoder_1_out1));
  LED led_3 (.in(decoder_1_out2));
  LED led_4 (.in(decoder_1_out3));
  LED led_5 (.in(decoder_2_out0));
  LED led_6 (.in(decoder_2_out1));
  LED led_7 (.in(decoder_2_out2));
  LED led_8 (.in(decoder_2_out3));

  assign stall = bubble;

  // Notes on the sheet:
  //   If the previous instruction is ldr, we need to stall for 1 cycle
  //   ID
  //   EX
  //   MA
  //   WB
  //   ID
  //   EX
  //   MA
  //   WB
endmodule

module Bit_Extender (
  input  [9:0] datain,
  output [31:0] dataout
);

  Multiplexer #(.width(22)) multiplexer_1 (.in0({22{1'b0}}), .in1({22{1'b1}}), .out(dataout[31:10]), .sel(datain[9]));

  assign dataout[9:0] = datain;
endmodule

module LHT (
  input  clk,
  input  reset,
  input  store,
  input  data_in,
  input  [2:0] address,
  output [2:0] r0,
  output [2:0] r1,
  output [2:0] r2,
  output [2:0] r3,
  output [2:0] lpt_addr,
  output [2:0] r4,
  output [2:0] r5,
  output [2:0] r6,
  output [2:0] r7
);

  wire and_1_out, and_2_out, and_3_out, and_4_out, and_5_out, and_6_out, and_7_out, and_8_out,
       decoder_1_out0, decoder_1_out1, decoder_1_out2, decoder_1_out3, decoder_1_out4, decoder_1_out5,
       decoder_1_out6, decoder_1_out7;

  Decoder #(.enable("false"), .select(3)) decoder_1 (
    .out0(decoder_1_out0), .out1(decoder_1_out1), .out2(decoder_1_out2), .out3(decoder_1_out3),
    .out4(decoder_1_out4), .out5(decoder_1_out5), .out6(decoder_1_out6), .out7(decoder_1_out7), .sel(address));
  and and_1 (and_1_out, store, decoder_1_out0);
  and and_2 (and_2_out, store, decoder_1_out1);
  and and_3 (and_3_out, store, decoder_1_out2);
  and and_4 (and_4_out, store, decoder_1_out3);
  and and_5 (and_5_out, store, decoder_1_out4);
  and and_6 (and_6_out, store, decoder_1_out5);
  and and_7 (and_7_out, store, decoder_1_out6);
  and and_8 (and_8_out, store, decoder_1_out7);
  Shift_Register #(.length(3)) shift_register_1 (
    .shift(and_1_out), .in(data_in), .clk(clk), .out(r0[0]), .clr(reset), .q0(r0[2]), .q1(r0[1]));  // open: load, d0, d1, d2, q2
  Shift_Register #(.length(3)) shift_register_2 (
    .shift(and_2_out), .in(data_in), .clk(clk), .out(r1[0]), .clr(reset), .q0(r1[2]), .q1(r1[1]));  // open: load, d0, d1, d2, q2
  Shift_Register #(.length(3)) shift_register_3 (
    .shift(and_3_out), .in(data_in), .clk(clk), .out(r2[0]), .clr(reset), .q0(r2[2]), .q1(r2[1]));  // open: load, d0, d1, d2, q2
  Shift_Register #(.length(3)) shift_register_4 (
    .shift(and_4_out), .in(data_in), .clk(clk), .out(r3[0]), .clr(reset), .q0(r3[2]), .q1(r3[1]));  // open: load, d0, d1, d2, q2
  Shift_Register #(.length(3)) shift_register_5 (
    .shift(and_5_out), .in(data_in), .clk(clk), .out(r4[0]), .clr(reset), .q0(r4[2]), .q1(r4[1]));  // open: load, d0, d1, d2, q2
  Shift_Register #(.length(3)) shift_register_6 (
    .shift(and_6_out), .in(data_in), .clk(clk), .out(r5[0]), .clr(reset), .q0(r5[2]), .q1(r5[1]));  // open: load, d0, d1, d2, q2
  Shift_Register #(.length(3)) shift_register_7 (
    .shift(and_7_out), .in(data_in), .clk(clk), .out(r6[0]), .clr(reset), .q0(r6[2]), .q1(r6[1]));  // open: load, d0, d1, d2, q2
  Shift_Register #(.length(3)) shift_register_8 (
    .shift(and_8_out), .in(data_in), .clk(clk), .out(r7[0]), .clr(reset), .q0(r7[2]), .q1(r7[1]));  // open: load, d0, d1, d2, q2
  Multiplexer #(.select(3), .width(3)) multiplexer_1 (
    .in0(r0), .in1(r1), .in2(r2), .in3(r3), .in4(r4), .in5(r5), .in6(r6), .in7(r7), .out(lpt_addr),
    .sel(address));

  // Notes on the sheet:
  //   8x3 LHT
endmodule

module PC_Prediction_Logic (
  input  [1:0] pcsel,
  input  [1:0] pcsel_IF,
  input  [31:0] immed,
  input  should_predict,
  input  prev_shld_predict,
  input  [31:0] immed_IF,
  input  predicted_jump,
  input  prev_predicted_jump,
  input  flush,
  output [31:0] immed_out,
  output [1:0] pcsel_out
);

  wire and_1_out;
  wire [1:0] multiplexer_1_out, multiplexer_2_out, multiplexer_4_out, multiplexer_5_out;

  and and_1 (and_1_out, should_predict, predicted_jump);
  Multiplexer #(.width(2)) multiplexer_1 (.in0(2'b00), .in1(pcsel_IF), .out(multiplexer_1_out), .sel(predicted_jump));
  Multiplexer #(.width(2)) multiplexer_2 (.in0(pcsel), .in1(2'b00), .out(multiplexer_2_out), .sel(prev_shld_predict));
  Multiplexer #(.width(32)) multiplexer_3 (.in0(immed), .in1(immed_IF), .out(immed_out), .sel(and_1_out));
  Multiplexer #(.width(2)) multiplexer_4 (
    .in0(multiplexer_2_out), .in1(multiplexer_1_out), .out(multiplexer_4_out), .sel(should_predict));
  Multiplexer #(.width(2)) multiplexer_5 (.in0(pcsel), .in1(2'b00), .out(multiplexer_5_out), .sel(prev_predicted_jump));
  Multiplexer #(.width(2)) multiplexer_6 (
    .in0(multiplexer_4_out), .in1(multiplexer_5_out), .out(pcsel_out), .sel(flush));

  // Notes on the sheet:
  //   A change in the PC is predicted
  //   pcsel value of instruction in IF stage
  //   pcsel value of instruction in ID stage
  //   pcsel = pc (pc + 1)
  //   A prediction is needed for the instruction in IF stage
  //   pcsel = pc (pc + 1)
  //   - Normally the immediate value is taken from the instruction in the ID stage
  //   - Normally the pcsel control signal is taken from the instruction in the ID stage
  //   - When we predict a change in PC for an instruction, we must use that instruction's immediate value
  //   - When we predict a change in PC for an instruction, we must use that instruction's pcsel value
  //   - The prediction is made in the IF stage, so we must extract the pcsel value from the instruction in the IF stage
  //   A change in PC was predicted for instruction in IF stage
  //   Scenario 2 (prev_shld_predict = 1): A prediction was made, pcsel of instruction in ID stage was already used,
  //   A prediction was needed for the instruction in ID stage
  //   - The prediction is made in the IF stage, so we must extract the immediate value from the instruction in the IF stage
  //   Scenario 1 (prev_shld_predict = 0): No prediction was made, so pcsel is taken normally from instruction in ID stage
  //   immed of instruction currently in IF stage
  //   so we need  to take the next instruction in line(pc + 1), otherwise we enter an infinite loop
  //   immed of instruction currently in ID stage
  //   A prediction is needed for the instruction in IF stage
  //   pcsel value of instruction in ID stage
  //   pcsel = pc (pc + 1)
  //   Opposite pcsel value of our prediction
  //   pcsel value derived from previous logic when no flush is needed
  //   A change in PC was predicted for instruction in ID stage
  //   - If a change of PC was predicted for instruction in ID stage, then we take pc + 1
  //   - If no change in PC was predicted, then we take pcsel of instruction in ID stage
  //   The prediction for the instruction in ID stage was incorrect, so a flush of the pipeline is needed
endmodule

module Instruction_prediction_unit (
  input  Clk,
  input  Reset,
  input  [31:0] instruction,
  input  stall,
  output [31:0] immed_IF,
  output uncond,
  output prev_uncond,
  output should_predict,
  output prev_shld_predict,
  output [1:0] pcsel_IF,
  output str_LR
);

  wire and_1_out, comparator_1_eq, comparator_2_gt, comparator_3_lt, comparator_4_eq, not_1_out;

  Comparator #(.mode("unsigned"), .width(4)) comparator_1 (
    .a(instruction[22:19]), .b(4'b0001), .eq(comparator_1_eq));  // open: gt, lt
  Comparator #(.mode("unsigned"), .width(7)) comparator_2 (
    .a(instruction[31:25]), .b(7'b0010111), .gt(comparator_2_gt));  // open: eq, lt
  Comparator #(.mode("unsigned"), .width(7)) comparator_3 (
    .a(instruction[31:25]), .b(7'b0011100), .lt(comparator_3_lt));  // open: gt, eq
  not not_1 (not_1_out, stall);
  Comparator #(.mode("unsigned"), .width(7)) comparator_4 (
    .a(instruction[31:25]), .b(7'b0011001), .eq(comparator_4_eq));  // open: gt, lt
  Comparator #(.mode("unsigned"), .width(7)) comparator_5 (
    .a(instruction[31:25]), .b(7'b0011011), .eq(str_LR));  // open: gt, lt
  Bit_Extender bit_extender_1 (.datain(instruction[9:0]), .dataout(immed_IF));
  and and_1 (and_1_out, comparator_2_gt, comparator_3_lt);
  and and_2 (should_predict, and_1_out, not_1_out);
  Multiplexer #(.width(2)) multiplexer_1 (.in0(2'b01), .in1(2'b10), .out(pcsel_IF), .sel(comparator_4_eq));
  and and_3 (uncond, comparator_1_eq, should_predict);
  Register #(.width(1)) register_1 (.D(should_predict), .en(Clk), .Q(prev_shld_predict), .clk(Clk), .clr(Reset));
  Register #(.width(1)) register_2 (.D(uncond), .en(Clk), .Q(prev_uncond), .clk(Clk), .clr(Reset));

  // Notes on the sheet:
  //   is unconditional?
  //   is branch / jump command?
  //   is branch?
  //   is rts?
  //   is branch / jump command?
  //   If the instruction is an unconditional branch/jump, a change in PC should always be made right away
  //   pcsel = pc + immed
  //   pcsel = immed
  //   If a prediction is made and a change in the PC is needed, we must use the immediate value of the instruction in the IF stage
  //   We derive the value of pcsel by checking if the instruction is a branch
  //   in branch instructions
  //   in jump instructions
  //   If the instruction is rts (return from subroutine), the str_LR control signal is activated 
  //   This signal loads the value in the Link register inside the immediate port of the PC
  //   If the instruction is a branch or jump and not stall is active, a prediction should be made
  //   If a prediction is made and a change in the PC is needed, we must use the pcsel value of the instruction in the IF stage
endmodule
