// Logisim project mimo_32bit_v1.circ as structural Verilog: 21 circuits, main circuit MiMo_Pipelined_v0
module MiMo_Pipelined_v0 (
  input  [1:0] imload,
  input  [1:0] op2sel,
  output [1:0] out_3
);

  wire C, CLK, datawrite, dwrite, id_stage_1_cond_met, id_stage_1_set_flags, imload_t, instrUnload, N,
       negOp2, not_1_out, Reset, rvrsOps, swrite, twrite, V, Z;
  wire [1:0] addrsel, datasel, multiplexer_4_out, multiplexer_5_out, op2sel_t, pcsel, regsrc;
  wire [2:0] id_stage_1_dregs, id_stage_1_sregs, id_stage_1_tregs, shift_register_1_out,
       shift_register_2_out, shift_register_3_out;
  wire [3:0] aluop, showhexa_1_digit, showhexa_1_out_2, showhexa_1_out_3, showhexa_1_out_4, showhexa_1_out_5,
       showhexa_1_out_7, showhexa_1_out_8, showhexa_1_out_9, showhexa_2_digit, showhexa_2_out_2,
       showhexa_2_out_3, showhexa_2_out_4, showhexa_2_out_5, showhexa_2_out_7, showhexa_2_out_8,
       showhexa_2_out_9, showhexa_3_digit, showhexa_3_out_2, showhexa_3_out_3, showhexa_3_out_4,
       showhexa_3_out_5, showhexa_3_out_7, showhexa_3_out_8, showhexa_3_out_9, showhexa_4_digit,
       showhexa_4_out_2, showhexa_4_out_3, showhexa_4_out_4, showhexa_4_out_5, showhexa_4_out_7,
       showhexa_4_out_8, showhexa_4_out_9, showhexa_5_digit, showhexa_5_out_2, showhexa_5_out_3,
       showhexa_5_out_4, showhexa_5_out_5, showhexa_5_out_7, showhexa_5_out_8, showhexa_5_out_9;
  wire [6:0] id_stage_1_opcode;
  wire [7:0] adder_1_out, multiplexer_2_out;
  wire [9:0] ex_stage_1_immed1, immed, immed3, ma_stage_1_immed2;
  wire [31:0] aluout2, ex_stage_1_aluout, ex_stage_1_instruction2, ex_stage_1_rd1, ex_stage_1_rs1,
       ex_stage_1_rt1, id_stage_1_instruction1, if_stage_1_address, Instruction_RAM_data, ma_stage_1_addr,
       ma_stage_1_aluout1, ma_stage_1_datain, ma_stage_1_instruction3, ma_stage_1_rs2, multiplexer_1_out,
       ram_1_data, register_bank_1_dreg, register_bank_1_r0, register_bank_1_r1, register_bank_1_r2,
       register_bank_1_r3, register_bank_1_r4, register_bank_1_r5, register_bank_1_r6, register_bank_1_r7,
       register_bank_1_treg, regwrite, Rs, Rs3;
  wire [31:1] rom_1_data;

  Clock clock_1 (.out(CLK));
  Button button_1 (.out(Reset));
  Hex_Digit_Display hex_digit_display_1 (.value(showhexa_1_out_2));  // open: dp
  ShowHexa showhexa_1 (
    .Data(if_stage_1_address), .out_3(showhexa_1_out_3), .out_4(showhexa_1_out_4), .out_5(showhexa_1_out_5),
    .Digit(showhexa_1_digit), .out_7(showhexa_1_out_7), .out_8(showhexa_1_out_8), .out_9(showhexa_1_out_9),
    .out_2(showhexa_1_out_2));
  // Probe on immed
  Hex_Digit_Display hex_digit_display_2 (.value(showhexa_2_out_2));  // open: dp
  Hex_Digit_Display hex_digit_display_3 (.value(showhexa_2_out_3));  // open: dp
  ShowHexa showhexa_2 (
    .Data(multiplexer_1_out), .out_3(showhexa_2_out_3), .out_4(showhexa_2_out_4), .out_5(showhexa_2_out_5),
    .Digit(showhexa_2_digit), .out_7(showhexa_2_out_7), .out_8(showhexa_2_out_8), .out_9(showhexa_2_out_9),
    .out_2(showhexa_2_out_2));
  Hex_Digit_Display hex_digit_display_4 (.value(showhexa_1_out_3));  // open: dp
  Hex_Digit_Display hex_digit_display_5 (.value(showhexa_1_out_4));  // open: dp
  Hex_Digit_Display hex_digit_display_6 (.value(showhexa_2_out_4));  // open: dp
  Hex_Digit_Display hex_digit_display_7 (.value(showhexa_2_out_5));  // open: dp
  Hex_Digit_Display hex_digit_display_8 (.value(showhexa_1_out_5));  // open: dp
  Hex_Digit_Display hex_digit_display_9 (.value(showhexa_1_digit));  // open: dp
  Hex_Digit_Display hex_digit_display_10 (.value(showhexa_2_digit));  // open: dp
  Hex_Digit_Display hex_digit_display_11 (.value(showhexa_2_out_7));  // open: dp
  Hex_Digit_Display hex_digit_display_12 (.value(showhexa_1_out_7));  // open: dp
  Hex_Digit_Display hex_digit_display_13 (.value(showhexa_1_out_8));  // open: dp
  IF_Stage if_stage_1 (.Clk(CLK), .Reset(Reset), .immed3(immed), .Rs3(Rs), .pcsel(pcsel), .address(if_stage_1_address));
  Hex_Digit_Display hex_digit_display_14 (.value(showhexa_2_out_8));  // open: dp
  Hex_Digit_Display hex_digit_display_15 (.value(showhexa_2_out_9));  // open: dp
  Hex_Digit_Display hex_digit_display_16 (.value(showhexa_1_out_9));  // open: dp
  RAM #(.addrWidth(16), .asyncread("true"), .dataWidth(32), .databus("bidir")) Instruction_RAM (
    .addr(if_stage_1_address[15:0]), .we(1'b0), .oe(1'b1), .clk(CLK), .data(Instruction_RAM_data));
  Multiplexer #(.width(32)) multiplexer_1 (
    .in0(Instruction_RAM_data), .in1({32{1'b0}}), .out(multiplexer_1_out), .sel(instrUnload));
  // Probe on id_stage_1_dregs
  // Probe on id_stage_1_sregs
  Hex_Digit_Display hex_digit_display_17 (.value(showhexa_3_out_2));  // open: dp
  Hex_Digit_Display hex_digit_display_18 (.value(showhexa_3_out_3));  // open: dp
  ShowHexa showhexa_3 (
    .Data(id_stage_1_instruction1), .out_3(showhexa_3_out_3), .out_4(showhexa_3_out_4),
    .out_5(showhexa_3_out_5), .Digit(showhexa_3_digit), .out_7(showhexa_3_out_7), .out_8(showhexa_3_out_8),
    .out_9(showhexa_3_out_9), .out_2(showhexa_3_out_2));
  Hex_Digit_Display hex_digit_display_19 (.value(showhexa_3_out_4));  // open: dp
  Hex_Digit_Display hex_digit_display_20 (.value(showhexa_3_out_5));  // open: dp
  Hex_Digit_Display hex_digit_display_21 (.value(showhexa_3_digit));  // open: dp
  Hex_Digit_Display hex_digit_display_22 (.value(showhexa_3_out_7));  // open: dp
  // Probe on id_stage_1_opcode
  Register_Bank register_bank_1 (
    .dselin(shift_register_1_out), .regval(regwrite), .dwrite(dwrite), .sselin(shift_register_2_out),
    .swrite(swrite), .tselin(shift_register_3_out), .twrite(twrite), .clock(CLK), .dselout(id_stage_1_dregs),
    .Reset(Reset), .sselout(id_stage_1_sregs), .tselout(id_stage_1_tregs), .dreg(register_bank_1_dreg),
    .sreg(Rs), .treg(register_bank_1_treg), .r0(register_bank_1_r0), .r1(register_bank_1_r1),
    .r2(register_bank_1_r2), .r3(register_bank_1_r3), .r4(register_bank_1_r4), .r5(register_bank_1_r5),
    .r6(register_bank_1_r6), .r7(register_bank_1_r7));
  Shift_Register #(.length(3), .width(3)) shift_register_1 (
    .shift(CLK), .in(id_stage_1_dregs), .clk(CLK), .out(shift_register_1_out), .clr(Reset));  // open: load, d0, q0, d1, q1, d2, q2
  Shift_Register #(.length(3), .width(3)) shift_register_2 (
    .shift(CLK), .in(id_stage_1_sregs), .clk(CLK), .out(shift_register_2_out), .clr(Reset));  // open: load, d0, q0, d1, q1, d2, q2
  Shift_Register #(.length(3), .width(3)) shift_register_3 (
    .shift(CLK), .in(id_stage_1_sregs), .clk(CLK), .out(shift_register_3_out), .clr(Reset));  // open: load, d0, q0, d1, q1, d2, q2
  ID_Stage id_stage_1 (
    .Clk(CLK), .reset(Reset), .instruction(multiplexer_1_out), .N(N), .V(V), .Z(Z), .C(C), .immed(immed),
    .imload(imload_t), .dregs(id_stage_1_dregs), .sregs(id_stage_1_sregs), .tregs(id_stage_1_tregs),
    .cond_met(id_stage_1_cond_met), .set_flags(id_stage_1_set_flags), .opcode(id_stage_1_opcode),
    .instruction1(id_stage_1_instruction1));
  Hex_Digit_Display hex_digit_display_23 (.value(showhexa_3_out_8));  // open: dp
  Hex_Digit_Display hex_digit_display_24 (.value(showhexa_3_out_9));  // open: dp
  // Probe on register_bank_1_r0
  Adder adder_1 (.a({1'b0, id_stage_1_opcode}), .b(8'h1), .out(adder_1_out));  // open: cin, cout
  // Probe on register_bank_1_r1
  // Probe on op2sel_t
  // Probe on immed
  Multiplexer #(.width(8)) multiplexer_2 (
    .in0({8{1'b0}}), .in1(adder_1_out), .out(multiplexer_2_out), .sel(id_stage_1_cond_met));
  // Probe on Rs
  // Probe on register_bank_1_dreg
  Hex_Digit_Display hex_digit_display_25 (.value(showhexa_4_out_2));  // open: dp
  ShowHexa showhexa_4 (
    .Data(ex_stage_1_instruction2), .out_3(showhexa_4_out_3), .out_4(showhexa_4_out_4),
    .out_5(showhexa_4_out_5), .Digit(showhexa_4_digit), .out_7(showhexa_4_out_7), .out_8(showhexa_4_out_8),
    .out_9(showhexa_4_out_9), .out_2(showhexa_4_out_2));
  ROM #(.dataWidth(32)) rom_1 (.addr(multiplexer_2_out), .data({rom_1_data, instrUnload}));
  // Probe on register_bank_1_r2
  Hex_Digit_Display hex_digit_display_26 (.value(showhexa_4_out_3));  // open: dp
  Hex_Digit_Display hex_digit_display_27 (.value(showhexa_4_out_4));  // open: dp
  // Probe on register_bank_1_r3
  Hex_Digit_Display hex_digit_display_28 (.value(showhexa_4_out_5));  // open: dp
  Hex_Digit_Display hex_digit_display_29 (.value(showhexa_4_digit));  // open: dp
  // Probe on register_bank_1_r4
  EX_Stage ex_stage_1 (
    .Clk(CLK), .flags_set(id_stage_1_set_flags), .reset(Reset), .Rd(register_bank_1_dreg), .Rs(Rs),
    .Rt(register_bank_1_treg), .op2sel(op2sel_t), .negOp2(negOp2), .aluop(aluop), .rvrsOps(rvrsOps),
    .immed(immed), .instruction1(id_stage_1_instruction1), .Rd1(ex_stage_1_rd1), .Rs1(ex_stage_1_rs1),
    .Rt1(ex_stage_1_rt1), .C(C), .Z(Z), .N(N), .V(V), .aluout(ex_stage_1_aluout), .immed1(ex_stage_1_immed1),
    .instruction2(ex_stage_1_instruction2));
  Hex_Digit_Display hex_digit_display_30 (.value(showhexa_4_out_7));  // open: dp
  Hex_Digit_Display hex_digit_display_31 (.value(showhexa_4_out_8));  // open: dp
  // Probe on {rom_1_data, instrUnload}
  // Probe on register_bank_1_r5
  // Probe on ex_stage_1_rd1
  Hex_Digit_Display hex_digit_display_32 (.value(showhexa_4_out_9));  // open: dp
  // Probe on register_bank_1_r6
  // Probe on ex_stage_1_aluout
  // Probe on register_bank_1_r7
  Hex_Digit_Display hex_digit_display_33 (.value(showhexa_5_out_2));  // open: dp
  Hex_Digit_Display hex_digit_display_34 (.value(showhexa_5_out_3));  // open: dp
  ShowHexa showhexa_5 (
    .Data(ma_stage_1_instruction3), .out_3(showhexa_5_out_3), .out_4(showhexa_5_out_4),
    .out_5(showhexa_5_out_5), .Digit(showhexa_5_digit), .out_7(showhexa_5_out_7), .out_8(showhexa_5_out_8),
    .out_9(showhexa_5_out_9), .out_2(showhexa_5_out_2));
  Hex_Digit_Display hex_digit_display_35 (.value(showhexa_5_out_4));  // open: dp
  Hex_Digit_Display hex_digit_display_36 (.value(showhexa_5_out_5));  // open: dp
  Hex_Digit_Display hex_digit_display_37 (.value(showhexa_5_digit));  // open: dp
  Hex_Digit_Display hex_digit_display_38 (.value(showhexa_5_out_7));  // open: dp
  MA_Stage ma_stage_1 (
    .Clk(CLK), .reset(Reset), .immed1(ex_stage_1_immed1), .aluout(ex_stage_1_aluout), .Rd1(ex_stage_1_rd1),
    .Rs1(ex_stage_1_rs1), .Rt1(ex_stage_1_rt1), .addrsel(addrsel), .datasel(datasel),
    .instruction2(ex_stage_1_instruction2), .immed2(ma_stage_1_immed2), .aluout1(ma_stage_1_aluout1),
    .Rs2(ma_stage_1_rs2), .addr(ma_stage_1_addr), .datain(ma_stage_1_datain),
    .instruction3(ma_stage_1_instruction3));
  Hex_Digit_Display hex_digit_display_39 (.value(showhexa_5_out_8));  // open: dp
  Hex_Digit_Display hex_digit_display_40 (.value(showhexa_5_out_9));  // open: dp
  // Probe on rom_1_data[2:1]
  Shift_Register #(.length(1), .width(4)) shift_register_4 (
    .shift(CLK), .in(rom_1_data[8:5]), .clk(CLK), .out(aluop), .clr(Reset));  // open: load, d0, q0
  Shift_Register #(.length(1)) shift_register_5 (
    .shift(CLK), .in(rom_1_data[9]), .clk(CLK), .out(negOp2), .clr(Reset));  // open: load, d0, q0
  Shift_Register #(.length(1)) shift_register_6 (
    .shift(CLK), .in(rom_1_data[10]), .clk(CLK), .out(rvrsOps), .clr(Reset));  // open: load, d0, q0
  Shift_Register #(.length(2), .width(2)) shift_register_7 (
    .shift(CLK), .in(rom_1_data[12:11]), .clk(CLK), .out(datasel), .clr(Reset));  // open: load, d0, q0, d1, q1
  Shift_Register #(.length(2)) shift_register_8 (
    .shift(CLK), .in(rom_1_data[13]), .clk(CLK), .out(datawrite), .clr(Reset));  // open: load, d0, q0, d1, q1
  Shift_Register #(.length(2), .width(2)) shift_register_9 (
    .shift(CLK), .in(rom_1_data[15:14]), .clk(CLK), .out(addrsel), .clr(Reset));  // open: load, d0, q0, d1, q1
  Shift_Register #(.length(3)) shift_register_10 (
    .shift(CLK), .in(rom_1_data[18]), .clk(CLK), .out(dwrite), .clr(Reset));  // open: load, d0, q0, d1, q1, d2, q2
  Shift_Register #(.length(3)) shift_register_11 (
    .shift(CLK), .in(rom_1_data[19]), .clk(CLK), .out(swrite), .clr(Reset));  // open: load, d0, q0, d1, q1, d2, q2
  Shift_Register #(.length(3)) shift_register_12 (
    .shift(CLK), .in(rom_1_data[20]), .clk(CLK), .out(twrite), .clr(Reset));  // open: load, d0, q0, d1, q1, d2, q2
  Multiplexer #(.select(2), .width(2)) multiplexer_3 (
    .in0({1'b0, imload_t}), .in1({1'b0, imload_t}), .in2(rom_1_data[2:1]), .in3(rom_1_data[2:1]),
    .out(pcsel), .sel(rom_1_data[2:1]));
  not not_1 (not_1_out, datawrite);
  Multiplexer #(.select(2), .width(2)) multiplexer_4 (
    .in0({1'b0, imload_t}), .in1({1'b0, imload_t}), .in2(rom_1_data[17:16]), .in3(rom_1_data[17:16]),
    .out(multiplexer_4_out), .sel(rom_1_data[17:16]));
  RAM #(.addrWidth(16), .asyncread("true"), .dataWidth(32), .databus("bidir")) ram_1 (
    .addr(ma_stage_1_addr[15:0]), .we(datawrite), .oe(not_1_out), .clk(CLK), .data(ram_1_data));
  Multiplexer #(.select(2), .width(2)) multiplexer_5 (
    .in0({1'b0, imload_t}), .in1({1'b0, imload_t}), .in2(rom_1_data[4:3]), .in3(rom_1_data[4:3]),
    .out(multiplexer_5_out), .sel(rom_1_data[4:3]));
  Shift_Register #(.length(1), .width(2)) shift_register_13 (
    .shift(CLK), .in(multiplexer_5_out), .clk(CLK), .out(op2sel_t), .clr(Reset));  // open: load, d0, q0
  Shift_Register #(.length(3), .width(2)) shift_register_14 (
    .shift(CLK), .in(multiplexer_4_out), .clk(CLK), .out(regsrc), .clr(Reset));  // open: load, d0, q0, d1, q1, d2, q2
  assign ram_1_data = datawrite ? ma_stage_1_datain : 32'bz;  // Controlled_Buffer controlled_buffer_1
  Multiplexer #(.select(2), .width(2)) multiplexer_6 (
    .in0(imload), .in1(imload), .in2(op2sel), .in3(op2sel), .out(out_3), .sel(op2sel));
  WB_Stage wb_stage_1 (
    .Clk(CLK), .reset(Reset), .immed2(ma_stage_1_immed2), .aluout1(ma_stage_1_aluout1), .Rs2(ma_stage_1_rs2),
    .operand(ram_1_data), .regsrc(regsrc), .immed3(immed3), .aluout2(aluout2), .Rs3(Rs3), .regwrite(regwrite));

  // Notes on the sheet:
  //   Instruction going to ID
  //   Address
  //   MiMo - Microprogrammed CPU Model
  //   Instruction RAM
  //   v0 Pipelined
  //   Instruction going to EX
  //   Registers
  //   opcode
  //   1st address is reserved
  //   cond_met
  //   contents of rom_1 (hex, n*v repeats v):
  //   4 40004 70544 70004 70024 70424 70044 70064 70084 700a4 700c4 700e4 70104 70124 702a4 24 4 e4 a4
  //   70164 70184 701a4 701e4 701c4 1 7 0 60004 2004 4
  //   Control ROM
  //   Instruction going to MA
  //   Instruction going to WB
  //   IF
  //   EX
  //   MA
  //   WB
  //   (add address decoder later on here)
  //   Operand RAM
endmodule

module IF_Stage (
  input  Clk,
  input  Reset,
  input  [9:0] immed3,
  input  [31:0] Rs3,
  input  [1:0] pcsel,
  output [31:0] address
);

  PC Instruction_PC (
    .imreg({{22{1'b0}}, immed3}), .sreg(Rs3), .pcsel(pcsel), .pcload(1'b1), .clock(Clk), .reset(Reset),
    .pcout(address));
  Register #(.width(32)) register_1 (.en(Clk), .clk(Clk), .clr(Reset));  // open: D, Q

  // Notes on the sheet:
  //   PC
endmodule

module ID_Stage (
  input  Clk,
  input  reset,
  input  [31:0] instruction,
  input  N,
  input  V,
  input  Z,
  input  C,
  output [9:0] immed,
  output imload,
  output [2:0] dregs,
  output [2:0] sregs,
  output [2:0] tregs,
  output cond_met,
  output set_flags,
  output [6:0] opcode,
  output [31:0] instruction1
);

  wire new_instruction_reg_1_set_flags;
  wire [3:0] new_instruction_reg_1_condition;
  wire [9:0] new_instruction_reg_1_immed;

  New_Instruction_Reg new_instruction_reg_1 (
    .instruction(instruction), .reset(reset), .clock(Clk), .immed(new_instruction_reg_1_immed),
    .dregsel(dregs), .sregsel(sregs), .tregsel(tregs), .condition(new_instruction_reg_1_condition),
    .set_flags(new_instruction_reg_1_set_flags), .imload(imload), .opcode(opcode));
  Multiplexer #(.width(10)) multiplexer_1 (
    .in0({10{1'b0}}), .in1(new_instruction_reg_1_immed), .out(immed), .sel(imload));
  // Probe on new_instruction_reg_1_condition
  New_Immediate_reg new_immediate_reg_1 (
    .DataIn(new_instruction_reg_1_immed), .IMLoad(imload), .CLKin(Clk), .reset(reset));  // open: ImmOut
  check_condition check_condition_1 (
    .C(C), .Z(Z), .V(V), .N(N), .condition(new_instruction_reg_1_condition), .cond_met(cond_met));
  and and_1 (set_flags, cond_met, new_instruction_reg_1_set_flags);
  Register #(.width(32)) register_1 (.D(instruction), .en(Clk), .Q(instruction1), .clk(Clk), .clr(reset));

  // Notes on the sheet:
  //   Flags
endmodule

module EX_Stage (
  input  Clk,
  input  flags_set,
  input  reset,
  input  [31:0] Rd,
  input  [31:0] Rs,
  input  [31:0] Rt,
  input  [1:0] op2sel,
  input  negOp2,
  input  [3:0] aluop,
  input  rvrsOps,
  input  [9:0] immed,
  input  [31:0] instruction1,
  output [31:0] Rd1,
  output [31:0] Rs1,
  output [31:0] Rt1,
  output C,
  output Z,
  output N,
  output V,
  output [31:0] aluout,
  output [9:0] immed1,
  output [31:0] instruction2
);

  wire alu_1_carry, alu_1_negative, alu_1_overflow, alu_1_zero;
  wire [31:0] multiplexer_1_out, multiplexer_2_out, multiplexer_3_out, multiplexer_4_out, not_1_out;

  Register #(.width(32)) register_1 (.D(Rs), .en(Clk), .Q(Rs1), .clk(Clk), .clr(reset));
  Register #(.width(32)) register_2 (.D(Rt), .en(Clk), .Q(Rt1), .clk(Clk), .clr(reset));
  Register #(.width(10)) register_3 (.D(immed), .en(Clk), .Q(immed1), .clk(Clk), .clr(reset));
  Register #(.width(32)) register_4 (.D(instruction1), .en(Clk), .Q(instruction2), .clk(Clk), .clr(reset));
  Register #(.width(32)) register_5 (.D(Rd), .en(Clk), .Q(Rd1), .clk(Clk), .clr(reset));
  Multiplexer #(.select(2), .width(32)) multiplexer_1 (
    .in0(Rt1), .in1({{22{1'b0}}, immed1}), .in2({32{1'b0}}), .in3(32'h1), .out(multiplexer_1_out),
    .sel(op2sel));
  Multiplexer #(.width(32)) multiplexer_2 (
    .in0(multiplexer_1_out), .in1(not_1_out), .out(multiplexer_2_out), .sel(negOp2));
  assign not_1_out = ~multiplexer_1_out;  // NOT_Gate not_1, 32 bits wide
  Multiplexer #(.width(32)) multiplexer_3 (.in0(Rs1), .in1(multiplexer_2_out), .out(multiplexer_3_out), .sel(rvrsOps));
  Multiplexer #(.width(32)) multiplexer_4 (.in0(multiplexer_2_out), .in1(Rs1), .out(multiplexer_4_out), .sel(rvrsOps));
  ALU alu_1 (
    .A(multiplexer_3_out), .B(multiplexer_4_out), .aluop(aluop), .Result(aluout), .Overflow(alu_1_overflow),
    .Carry(alu_1_carry), .Negative(alu_1_negative), .Zero(alu_1_zero));
  Register #(.width(1)) register_6 (.D(alu_1_carry), .en(flags_set), .Q(C), .clk(Clk), .clr(reset));
  Register #(.width(1)) register_7 (.D(alu_1_zero), .en(flags_set), .Q(Z), .clk(Clk), .clr(reset));
  Register #(.width(1)) register_8 (.D(alu_1_negative), .en(flags_set), .Q(N), .clk(Clk), .clr(reset));
  Register #(.width(1)) register_9 (.D(alu_1_overflow), .en(flags_set), .Q(V), .clk(Clk), .clr(reset));

  // Other names for the same wires on the sheet: flgset = flags_set

  // Notes on the sheet:
  //   Here the set_flags is directly taken form the previos stage
  //   ALU
endmodule

module MA_Stage (
  input  Clk,
  input  reset,
  input  [9:0] immed1,
  input  [31:0] aluout,
  input  [31:0] Rd1,
  input  [31:0] Rs1,
  input  [31:0] Rt1,
  input  [1:0] addrsel,
  input  [1:0] datasel,
  input  [31:0] instruction2,
  output [9:0] immed2,
  output [31:0] aluout1,
  output [31:0] Rs2,
  output [31:0] addr,
  output [31:0] datain,
  output [31:0] instruction3
);

  wire [31:0] register_2_q, register_3_q;

  Register #(.width(32)) register_1 (.D(aluout), .en(Clk), .Q(aluout1), .clk(Clk), .clr(reset));
  Register #(.width(32)) register_2 (.D(Rd1), .en(Clk), .Q(register_2_q), .clk(Clk), .clr(reset));
  Register #(.width(32)) register_3 (.D(Rt1), .en(Clk), .Q(register_3_q), .clk(Clk), .clr(reset));
  Register #(.width(10)) register_4 (.D(immed1), .en(Clk), .Q(immed2), .clk(Clk), .clr(reset));
  Register #(.width(32)) register_5 (.D(Rs1), .en(Clk), .Q(Rs2), .clk(Clk), .clr(reset));
  Register #(.width(32)) register_6 (.D(instruction2), .en(Clk), .Q(instruction3), .clk(Clk), .clr(reset));
  Multiplexer #(.select(2), .width(32)) multiplexer_1 (
    .in0({{22{1'b0}}, immed2}), .in1(aluout1), .in2(Rs2), .out(addr), .sel(addrsel));  // open: in3
  Multiplexer #(.select(2), .width(32)) multiplexer_2 (
    .in0(register_2_q), .in1(register_3_q), .in2(aluout1), .out(datain), .sel(datasel));  // open: in3
endmodule

module WB_Stage (
  input  Clk,
  input  reset,
  input  [9:0] immed2,
  input  [31:0] aluout1,
  input  [31:0] Rs2,
  input  [31:0] operand,
  input  [1:0] regsrc,
  output [9:0] immed3,
  output [31:0] aluout2,
  output [31:0] Rs3,
  output [31:0] regwrite
);

  wire [31:0] register_2_q;

  Register #(.width(10)) register_1 (.D(immed2), .en(Clk), .Q(immed3), .clk(Clk), .clr(reset));
  Register #(.width(32)) register_2 (.D(operand), .en(Clk), .Q(register_2_q), .clk(Clk), .clr(reset));
  Register #(.width(32)) register_3 (.D(aluout1), .en(Clk), .Q(aluout2), .clk(Clk), .clr(reset));
  Register #(.width(32)) register_4 (.D(Rs2), .en(Clk), .Q(Rs3), .clk(Clk), .clr(reset));
  Multiplexer #(.select(2), .width(32)) multiplexer_1 (
    .in0(Rs3), .in1({{22{1'b0}}, immed3}), .in2(register_2_q), .in3(aluout2), .out(regwrite), .sel(regsrc));
endmodule

// address
module MiMo_v05 (
  input  Cycle,
  input  Stop,
  input  Instr,
  input  [15:0] Addr,
  output [7:0] ucounter
);

  wire ADDR_DEC_output_3, alu_1_overflow, and_1_out, and_2_out, c, CLK, CLKIN, cont, FB_LED,
       multiplexer_2_out, n, Ncmd, not_1_out, or_1_out, RAMSel, reset, TTYSel, twrite, z;
  wire [1:0] addrsel, cond;
  wire [2:0] dregs, sregs, tregs;
  wire [3:0] aluop, icycles, showhexa_1_digit, showhexa_1_out_2, showhexa_1_out_3, showhexa_1_out_4,
       showhexa_1_out_5, showhexa_1_out_7, showhexa_1_out_8, showhexa_1_out_9, showhexa_2_digit,
       showhexa_2_out_2, showhexa_2_out_3, showhexa_2_out_4, showhexa_2_out_5, showhexa_2_out_7,
       showhexa_2_out_8, showhexa_2_out_9;
  wire [6:0] opcode;
  wire [7:0] adder_1_out, multiplexer_1_out, multiplexer_3_out;
  wire [15:0] cmds, cycles, DROM;
  wire [31:0] address, aluout, data, dreg, immed, irreg, multiplexer_5_out, multiplexer_6_out,
       multiplexer_7_out, pcreg, registerfile_1_r0, registerfile_1_r1, registerfile_1_r2, registerfile_1_r3,
       registerfile_1_r4, registerfile_1_r5, registerfile_1_r6, registerfile_1_r7, sreg, treg;
  wire [31:4] CROM;

  Hex_Digit_Display hex_digit_display_1 (.value(showhexa_1_out_2));  // open: dp
  ShowHexa showhexa_1 (
    .Data(address), .out_3(showhexa_1_out_3), .out_4(showhexa_1_out_4), .out_5(showhexa_1_out_5),
    .Digit(showhexa_1_digit), .out_7(showhexa_1_out_7), .out_8(showhexa_1_out_8), .out_9(showhexa_1_out_9),
    .out_2(showhexa_1_out_2));
  nor nor_1 (Ncmd, ucounter[0], ucounter[1], ucounter[2], ucounter[3], ucounter[5], ucounter[6], ucounter[7], ucounter[4]);
  Hex_Digit_Display hex_digit_display_2 (.value(showhexa_1_out_4));  // open: dp
  Hex_Digit_Display hex_digit_display_3 (.value(showhexa_1_out_3));  // open: dp
  RAM #(.addrWidth(16), .asyncread("true"), .dataWidth(32), .databus("bidir")) ram_1 (
    .addr(address[15:0]), .we(and_2_out), .oe(and_1_out), .clk(CLK), .data(data));
  and and_1 (and_1_out, RAMSel, not_1_out);
  not not_1 (not_1_out, CROM[6]);
  and and_2 (and_2_out, RAMSel, CROM[6]);
  Address_Decoder ADDR_DEC (
    .Address(address), .RAM(RAMSel), .FB_LED(FB_LED), .TTY(TTYSel), .output_3(ADDR_DEC_output_3));
  // Probe on ucounter
  // Probe on ucounter
  Register Microcounter (.D(adder_1_out), .Q(ucounter), .clk(CLK), .clr(reset));  // open: en
  Hex_Digit_Display hex_digit_display_4 (.value(showhexa_1_out_5));  // open: dp
  Hex_Digit_Display hex_digit_display_5 (.value(showhexa_1_digit));  // open: dp
  ROM #(.dataWidth(32)) rom_1 (.addr(ucounter), .data({CROM[31:19], cond, CROM[16:9], addrsel, CROM[6:4], aluop}));
  ROM #(.dataWidth(16)) rom_2 (.addr(ucounter), .data(DROM));
  Hex_Digit_Display hex_digit_display_6 (.value(showhexa_1_out_7));  // open: dp
  Hex_Digit_Display hex_digit_display_7 (.value(showhexa_1_out_8));  // open: dp
  // Probe on opcode
  Hex_Digit_Display hex_digit_display_8 (.value(showhexa_1_out_9));  // open: dp
  or or_1 (or_1_out, c, z);
  // Probe on cond
  Clock SysClk (.out(CLKIN));
  Hex_Digit_Display hex_digit_display_9 (.value(showhexa_2_out_2));  // open: dp
  Hex_Digit_Display hex_digit_display_10 (.value(showhexa_2_out_3));  // open: dp
  ShowHexa showhexa_2 (
    .Data(data), .out_3(showhexa_2_out_3), .out_4(showhexa_2_out_4), .out_5(showhexa_2_out_5),
    .Digit(showhexa_2_digit), .out_7(showhexa_2_out_7), .out_8(showhexa_2_out_8), .out_9(showhexa_2_out_9),
    .out_2(showhexa_2_out_2));
  Hex_Digit_Display hex_digit_display_11 (.value(showhexa_2_out_4));  // open: dp
  Hex_Digit_Display hex_digit_display_12 (.value(showhexa_2_out_5));  // open: dp
  // Probe on DROM[7:0]
  Multiplexer #(.width(8)) multiplexer_1 (
    .in0(DROM[7:0]), .in1(DROM[15:8]), .out(multiplexer_1_out), .sel(multiplexer_2_out));
  // Probe on DROM[15:8]
  Multiplexer #(.select(2)) multiplexer_2 (
    .in0(c), .in1(or_1_out), .in2(z), .in3(n), .out(multiplexer_2_out), .sel(cond));
  Multiplexer #(.width(8)) multiplexer_3 (
    .in0({8{1'b0}}), .in1({1'b0, opcode}), .out(multiplexer_3_out), .sel(CROM[19]));
  // Probe on address
  Hex_Digit_Display hex_digit_display_13 (.value(showhexa_2_digit));  // open: dp
  Hex_Digit_Display hex_digit_display_14 (.value(showhexa_2_out_7));  // open: dp
  // Probe on adder_1_out
  Adder adder_1 (.a(multiplexer_1_out), .b(multiplexer_3_out), .out(adder_1_out));  // open: cin, cout
  Multiplexer #(.select(2), .width(32)) multiplexer_4 (
    .in0(pcreg), .in1(immed), .in2(aluout), .in3(sreg), .out(address), .sel(addrsel));
  // Probe on addrsel
  Hex_Digit_Display hex_digit_display_15 (.value(showhexa_2_out_8));  // open: dp
  Hex_Digit_Display hex_digit_display_16 (.value(showhexa_2_out_9));  // open: dp
  assign data = CROM[6] ? multiplexer_5_out : 32'bz;  // Controlled_Buffer controlled_buffer_1
  Multiplexer #(.select(2), .width(32)) multiplexer_5 (
    .in0(pcreg), .in1(dreg), .in2(treg), .in3(aluout), .out(multiplexer_5_out), .sel(CROM[21:20]));
  // Probe on CROM[21:20]
  // Probe on ucounter
  // Probe on CROM[21:20]
  LED led_1 (.in(CROM[22]));
  // Probe on data
  // Probe on cond
  LED led_2 (.in(CROM[19]));
  Counters counters_1 (
    .new_ucounter(adder_1_out), .reset(reset), .clock(CLK), .cmds(cmds), .cycles(cycles), .icycles(icycles));
  // Probe on pcreg
  PC pc_1 (
    .imreg(immed), .sreg(sreg), .pcsel(CROM[10:9]), .pcload(CROM[11]), .clock(CLK), .reset(reset),
    .pcout(pcreg));
  ImmediateReg immediatereg_1 (.IMLoad(CROM[14]), .CLKin(CLK), .DataIn(data), .ImmOut(immed));
  InstructionReg instructionreg_1 (
    .reset(reset), .irload(CROM[13]), .instruction(data), .clock(CLK), .dregsel(dregs), .sregsel(sregs),
    .tregsel(tregs), .opcode(opcode), .Instruction_register_Content(irreg));
  // Probe on irreg
  // Probe on opcode
  // Probe on CROM[16:15]
  LED led_3 (.in(CROM[14]));
  // Probe on multiplexer_6_out
  Multiplexer #(.select(2), .width(32)) multiplexer_6 (
    .in0(data), .in1(immed), .in2(aluout), .in3(sreg), .out(multiplexer_6_out), .sel(CROM[16:15]));
  // Probe on CROM[16:15]
  // Probe on {CROM[31:19], cond, CROM[16:9], addrsel, CROM[6:4], aluop}
  LED led_4 (.in(CROM[12]));
  LED led_5 (.in(CROM[13]));
  // Probe on registerfile_1_r0
  // Probe on registerfile_1_r1
  // Probe on registerfile_1_r2
  // Probe on registerfile_1_r3
  // Probe on registerfile_1_r4
  // Probe on registerfile_1_r5
  // Probe on registerfile_1_r6
  // Probe on registerfile_1_r7
  Registerfile registerfile_1 (
    .dsel(dregs), .regval(multiplexer_6_out), .dwrite(CROM[12]), .ssel(sregs), .swrite(CROM[22]),
    .tsel(tregs), .twrite(twrite), .clock(CLK), .Reset(reset), .dreg(dreg), .sreg(sreg), .treg(treg),
    .r0(registerfile_1_r0), .r1(registerfile_1_r1), .r2(registerfile_1_r2), .r3(registerfile_1_r3),
    .r4(registerfile_1_r4), .r5(registerfile_1_r5), .r6(registerfile_1_r6), .r7(registerfile_1_r7));
  // Probe on tregs
  // Probe on sregs
  // Probe on dregs
  // Probe on CROM[10:9]
  LED led_6 (.in(CROM[11]));
  // Probe on dreg
  // Probe on sreg
  // Probe on treg
  // Probe on addrsel
  LED led_7 (.in(CROM[6]));
  // Probe on sreg
  // Probe on multiplexer_7_out
  Multiplexer #(.select(2), .width(32)) multiplexer_7 (
    .in0(treg), .in1(immed), .in2({32{1'b0}}), .in3(32'h1), .out(multiplexer_7_out), .sel(CROM[5:4]));
  // Probe on CROM[5:4]
  // Probe on DROM
  // Probe on CROM[5:4]
  ALU alu_1 (
    .A(sreg), .B(multiplexer_7_out), .aluop(aluop), .Result(aluout), .Overflow(alu_1_overflow), .Carry(c),
    .Negative(n), .Zero(z));
  // Probe on aluop
  // Probe on aluop
  Button u_Reset (.out(reset));
  // Probe on opcode
  // Probe on tregs
  // Probe on address
  // Probe on pcreg
  // Probe on irreg
  // Probe on immed
  // Probe on aluout
  // Probe on icycles
  // Probe on irreg
  // Probe on sregs
  // Probe on dregs
  LED New_CMD (.in(Ncmd));
  // Probe on cycles
  LED u_C (.in(c));
  LED u_Z (.in(z));
  LED u_N (.in(n));
  Button u_Cont (.out(cont));
  // Probe on data
  // Probe on cmds

  // Other names for the same wires on the sheet: CROM (some bits) = {cond, addrsel, aluop}; op2sel[1:0] = CROM[5:4];
  //   datawrite = CROM[6]; pcsel[1:0] = CROM[10:9]; pcload = CROM[11]; dwrite = CROM[12]; irload = CROM[13];
  //   imload = CROM[14]; regsrc[1:0] = CROM[16:15]; indexsel = CROM[19]; datasel[1:0] = CROM[21:20];
  //   swrite = CROM[22]; dbgadr = Stop; dbgcyc = Cycle; dbgins = Instr; MicroPC[7:0] = ucounter

  // Notes on the sheet:
  //   Based on: http://minnie.tuhs.org/Programs/UcodeCPU/index.html
  //   v05: Migration to EVO, Debug, Counters, ImmReg Units
  //   Address BUS
  //   RAM
  //   Control ROM
  //   Address of third uinstruction is "opcode+2"
  //   contents of rom_1 (hex, n*v repeats v):
  //   2000 80800 11000 39*0 4000 22*0 1000 0 4000 62*0 40021 1000c0 800 a00
  //   contents of rom_2 (hex, n*v repeats v):
  //   101 202 40*0 8282 22*0 8484 0 8383 62*0 8485 8484
  //   MiMo - Microprogrammed CPU Model
  //   Microcode Control Unit
  //   Decision ROM
  //   Data BUS
  //   v0.5 OR EVO
  //   Quick tips:
  //   Use ctrl+t to manually toggle global clock signal
  //   Use Simulate->Ticks Enabled for automatic clock signal
  //   ImmReg
  //   PC
  //   InsReg
  //   Micro Instruction
  //   Registers
  //   ALU
  //   Instruction:
  //   Spec. Registers
  //   Debug
  //   Address, Data Bus
  //   Status
  //   Flags
endmodule

module New_Instruction_Reg (
  input  [31:0] instruction,
  input  reset,
  input  clock,
  output [9:0] immed,
  output [2:0] dregsel,
  output [2:0] sregsel,
  output [2:0] tregsel,
  output [3:0] condition,
  output set_flags,
  output imload,
  output [6:0] opcode
);

  Register #(.width(32)) register_1 (
    .D(instruction), .en(1'b1), .Q({opcode, imload, set_flags, condition, tregsel, sregsel, dregsel, immed}),
    .clk(clock), .clr(reset));

  // Notes on the sheet:
  //   IR Logic
endmodule

module New_Immediate_reg (
  input  [9:0] DataIn,
  input  IMLoad,
  input  CLKin,
  input  reset,
  output [9:0] ImmOut
);

  Register #(.width(10)) register_1 (.D(DataIn), .en(IMLoad), .Q(ImmOut), .clk(CLKin), .clr(reset));
  // Probe on ImmOut
endmodule

module check_condition (
  input  C,
  input  Z,
  input  V,
  input  N,
  input  [3:0] condition,
  output cond_met
);

  wire and_1_out, and_2_out, and_3_out, and_4_out, and_5_out, and_6_out, and_7_out, and_8_out, and_9_out,
       and_10_out, and_11_out, and_12_out, and_13_out, and_14_out, and_15_out, and_16_out, and_17_out,
       and_18_out, decoder_1_out1, decoder_1_out2, decoder_1_out3, decoder_1_out4, decoder_1_out5,
       decoder_1_out6, decoder_1_out7, decoder_1_out8, decoder_1_out9, decoder_1_out10, decoder_1_out11,
       decoder_1_out12, decoder_1_out13, decoder_1_out14, decoder_1_out15, not_1_out, not_2_out, not_3_out,
       not_4_out, not_5_out, not_6_out, not_7_out, xnor_1_out, xnor_2_out, xor_1_out, xor_2_out;

  Decoder #(.enable("false"), .select(4)) decoder_1 (
    .out1(decoder_1_out1), .out2(decoder_1_out2), .out3(decoder_1_out3), .out4(decoder_1_out4),
    .out5(decoder_1_out5), .out6(decoder_1_out6), .out7(decoder_1_out7), .out8(decoder_1_out8),
    .out9(decoder_1_out9), .out10(decoder_1_out10), .out11(decoder_1_out11), .out12(decoder_1_out12),
    .out13(decoder_1_out13), .out14(decoder_1_out14), .out15(decoder_1_out15), .sel(condition));  // open: out0
  and and_1 (and_1_out, decoder_1_out10, not_1_out);
  not not_1 (not_1_out, Z);
  and and_2 (and_2_out, decoder_1_out10, C);
  and and_3 (and_3_out, decoder_1_out11, not_2_out);
  not not_2 (not_2_out, C);
  and and_4 (and_4_out, decoder_1_out11, Z);
  xnor xnor_1 (xnor_1_out, N, V);
  xor xor_1 (xor_1_out, N, V);
  not not_3 (not_3_out, Z);
  xnor xnor_2 (xnor_2_out, N, V);
  xor xor_2 (xor_2_out, N, V);
  and and_5 (and_5_out, decoder_1_out2, Z);
  and and_6 (and_6_out, decoder_1_out3, not_4_out);
  not not_4 (not_4_out, Z);
  and and_7 (and_7_out, decoder_1_out4, C);
  and and_8 (and_8_out, decoder_1_out5, not_5_out);
  not not_5 (not_5_out, C);
  and and_9 (and_9_out, decoder_1_out6, N);
  and and_10 (and_10_out, decoder_1_out7, not_6_out);
  not not_6 (not_6_out, N);
  and and_11 (and_11_out, decoder_1_out8, V);
  and and_12 (and_12_out, decoder_1_out9, not_7_out);
  not not_7 (not_7_out, V);
  and and_13 (and_13_out, and_1_out, and_2_out);
  and and_14 (and_14_out, and_3_out, and_4_out);
  and and_15 (and_15_out, decoder_1_out12, xnor_1_out);
  and and_16 (and_16_out, decoder_1_out13, xor_1_out);
  and and_17 (and_17_out, decoder_1_out14, not_3_out, xnor_2_out);
  and and_18 (and_18_out, decoder_1_out15, Z, xor_2_out);
  or or_1 (cond_met, decoder_1_out1, and_5_out, and_6_out, and_7_out, and_8_out, and_9_out, and_10_out, and_11_out, and_12_out, and_13_out, and_14_out, and_15_out, and_16_out, and_17_out, and_18_out);

  // Notes on the sheet:
  //   Flags
  //   HI
  //   LS
  //   GE
  //   LT
  //   GT
  //   AL (Always)
  //   EQ
  //   NE
  //   CS
  //   CC
  //   MI
  //   PL
  //   VS
  //   VC
  //   LE
endmodule

module Register_Bank (
  input  [31:0] regval,
  input  Reset,
  input  clock,
  input  [2:0] dselout,
  input  [2:0] sselout,
  input  [2:0] tselout,
  input  dwrite,
  input  swrite,
  input  twrite,
  input  [2:0] dselin,
  input  [2:0] sselin,
  input  [2:0] tselin,
  output [31:0] r0,
  output [31:0] r1,
  output [31:0] r2,
  output [31:0] r3,
  output [31:0] r4,
  output [31:0] r5,
  output [31:0] r6,
  output [31:0] r7,
  output [31:0] dreg,
  output [31:0] sreg,
  output [31:0] treg
);

  wire demultiplexer_1_out0, demultiplexer_1_out1, demultiplexer_1_out2, demultiplexer_1_out3,
       demultiplexer_1_out4, demultiplexer_1_out5, demultiplexer_1_out6, demultiplexer_1_out7;

  Demultiplexer #(.select(3)) demultiplexer_1 (
    .out0(demultiplexer_1_out0), .out1(demultiplexer_1_out1), .out2(demultiplexer_1_out2),
    .out3(demultiplexer_1_out3), .out4(demultiplexer_1_out4), .out5(demultiplexer_1_out5),
    .out6(demultiplexer_1_out6), .out7(demultiplexer_1_out7), .in(dwrite), .sel(dselin));
  Demultiplexer #(.select(3)) demultiplexer_2 (
    .out0(demultiplexer_1_out0), .out1(demultiplexer_1_out1), .out2(demultiplexer_1_out2),
    .out3(demultiplexer_1_out3), .out4(demultiplexer_1_out4), .out5(demultiplexer_1_out5),
    .out6(demultiplexer_1_out6), .out7(demultiplexer_1_out7), .in(swrite), .sel(sselin));
  Demultiplexer #(.select(3)) demultiplexer_3 (
    .out0(demultiplexer_1_out0), .out1(demultiplexer_1_out1), .out2(demultiplexer_1_out2),
    .out3(demultiplexer_1_out3), .out4(demultiplexer_1_out4), .out5(demultiplexer_1_out5),
    .out6(demultiplexer_1_out6), .out7(demultiplexer_1_out7), .in(twrite), .sel(tselin));
  Register #(.width(32)) register_1 (.D(regval), .en(demultiplexer_1_out0), .Q(r0), .clk(clock), .clr(Reset));
  Register #(.width(32)) register_2 (.D(regval), .en(demultiplexer_1_out1), .Q(r1), .clk(clock), .clr(Reset));
  Register #(.width(32)) register_3 (.D(regval), .en(demultiplexer_1_out2), .Q(r2), .clk(clock), .clr(Reset));
  Register #(.width(32)) register_4 (.D(regval), .en(demultiplexer_1_out3), .Q(r3), .clk(clock), .clr(Reset));
  Register #(.width(32)) register_5 (.D(regval), .en(demultiplexer_1_out4), .Q(r4), .clk(clock), .clr(Reset));
  Register #(.width(32)) register_6 (.D(regval), .en(demultiplexer_1_out5), .Q(r5), .clk(clock), .clr(Reset));
  Register #(.width(32)) register_7 (.D(regval), .en(demultiplexer_1_out6), .Q(r6), .clk(clock), .clr(Reset));
  Register #(.width(32)) register_8 (.D(regval), .en(demultiplexer_1_out7), .Q(r7), .clk(clock), .clr(Reset));
  Multiplexer #(.select(3), .width(32)) multiplexer_1 (
    .in0(r0), .in1(r1), .in2(r2), .in3(r3), .in4(r4), .in5(r5), .in6(r6), .in7(r7), .out(dreg), .sel(dselout));
  Multiplexer #(.select(3), .width(32)) multiplexer_2 (
    .in0(r0), .in1(r1), .in2(r2), .in3(r3), .in4(r4), .in5(r5), .in6(r6), .in7(r7), .out(sreg), .sel(sselout));
  Multiplexer #(.select(3), .width(32)) multiplexer_3 (
    .in0(r0), .in1(r1), .in2(r2), .in3(r3), .in4(r4), .in5(r5), .in6(r6), .in7(r7), .out(treg), .sel(tselout));

  // Notes on the sheet:
  //   Register File
endmodule

module ALU (
  input  [31:0] A,
  input  [31:0] B,
  input  [3:0] aluop,
  output Overflow,
  output Carry,
  output Zero,
  output Negative,
  output [31:0] Result
);

  wire adder_1_cout, and_2_out, and_3_out, or_3_out, subtractor_1_bout, xnor_1_out, xnor_2_out, xor_2_out,
       xor_3_out;
  wire [31:0] adder_1_out, and_1_out, divider_1_out, divider_1_rem, multiplier_1_out, nand_1_out, nor_1_out,
       not_1_out, or_1_out, shifter_1_out, shifter_2_out, shifter_3_out, shifter_4_out, shifter_5_out,
       subtractor_1_out, xor_1_out;

  Adder #(.width(32)) adder_1 (.a(A), .b(B), .out(adder_1_out), .cin(1'b0), .cout(adder_1_cout));
  Subtractor #(.width(32)) subtractor_1 (.a(A), .b(B), .out(subtractor_1_out), .bin(1'b0), .bout(subtractor_1_bout));
  Multiplier #(.width(32)) multiplier_1 (.a(A), .b(B), .out(multiplier_1_out), .cin({32{1'b0}}));  // open: cout
  Divider #(.width(32)) divider_1 (.a(A), .b(B), .out(divider_1_out), .upper({32{1'b0}}), .rem(divider_1_rem));
  assign and_1_out = A & B;  // AND_Gate and_1, 32 bits wide
  assign or_1_out = A | B;  // OR_Gate or_1, 32 bits wide
  assign xor_1_out = A ^ B;  // XOR_Gate xor_1, 32 bits wide
  assign nand_1_out = ~(A & B);  // NAND_Gate nand_1, 32 bits wide
  assign nor_1_out = ~(A | B);  // NOR_Gate nor_1, 32 bits wide
  assign not_1_out = ~A;  // NOT_Gate not_1, 32 bits wide
  Shifter #(.width(32)) shifter_1 (.in(A), .\dist (B[4:0]), .out(shifter_1_out));
  Shifter #(.shift("lr"), .width(32)) shifter_2 (.in(A), .\dist (B[4:0]), .out(shifter_2_out));
  Shifter #(.shift("ar"), .width(32)) shifter_3 (.in(A), .\dist (B[4:0]), .out(shifter_3_out));
  Shifter #(.shift("rl"), .width(32)) shifter_4 (.in(A), .\dist (B[4:0]), .out(shifter_4_out));
  Shifter #(.shift("rr"), .width(32)) shifter_5 (.in(A), .\dist (B[4:0]), .out(shifter_5_out));
  xor xor_2 (xor_2_out, B[31], A[31]);
  and and_2 (and_2_out, xor_2_out, xnor_1_out);
  xnor xnor_1 (xnor_1_out, B[31], subtractor_1_out[31]);
  xnor xnor_2 (xnor_2_out, B[31], A[31]);
  xor xor_3 (xor_3_out, A[31], adder_1_out[31]);
  Multiplexer #(.select(4), .width(32)) multiplexer_1 (
    .in0(adder_1_out), .in1(subtractor_1_out), .in2(multiplier_1_out), .in3(divider_1_out),
    .in4(divider_1_rem), .in5(and_1_out), .in6(or_1_out), .in7(xor_1_out), .in8(nand_1_out), .in9(nor_1_out),
    .in10(not_1_out), .in11(shifter_1_out), .in12(shifter_2_out), .in13(shifter_3_out), .in14(shifter_4_out),
    .in15(shifter_5_out), .out({Negative, Result[30:0]}), .sel(aluop));
  and and_3 (and_3_out, xnor_2_out, xor_3_out);
  or or_2 (Overflow, and_2_out, and_3_out);
  Multiplexer #(.select(4)) multiplexer_2 (
    .in0(adder_1_cout), .in1(subtractor_1_bout), .in2(1'b0), .in3(1'b0), .in4(1'b0), .in5(1'b0), .in6(1'b0),
    .in7(1'b0), .in8(1'b0), .in9(1'b0), .in10(1'b0), .in11(1'b0), .in12(1'b0), .in13(1'b0), .in14(1'b0),
    .in15(1'b0), .out(Carry), .sel(aluop));
  or or_3 (or_3_out, Result[0], Result[1], Result[2], Result[3], Result[4], Result[5], Result[6], Result[7], Result[8], Result[9], Result[10], Result[11], Result[12], Result[13], Result[14], Result[15], Result[16], Result[17], Result[18], Result[19], Result[20], Result[21], Result[22], Result[23], Result[24], Result[25], Result[26], Result[27], Result[28], Result[29], Result[30], Negative);
  not not_2 (Zero, or_3_out);

  assign Result[31] = Negative;

  // Notes on the sheet:
  //   32-bit ALU
  //   B MSB
  //   A MSB
  //   B MSB
  //   A MSB
  //   A MSB != B MSB?
  //   A MSB = B MSB?
  //   B MSB = output MSB
  //   A/B MSB != output MSB
endmodule

module InstructionReg (
  input  [31:0] instruction,
  input  reset,
  input  clock,
  input  irload,
  output [2:0] dregsel,
  output [2:0] sregsel,
  output [2:0] tregsel,
  output [6:0] opcode,
  output [31:0] Instruction_register_Content
);

  Register #(.width(32)) register_1 (
    .D(instruction), .en(irload),
    .Q({Instruction_register_Content[31:19], dregsel, Instruction_register_Content[15:0]}), .clk(clock),
    .clr(reset));

  assign Instruction_register_Content[18:16] = dregsel;
  assign opcode = Instruction_register_Content[31:25];
  assign sregsel = Instruction_register_Content[21:19];
  assign tregsel = Instruction_register_Content[24:22];

  // Notes on the sheet:
  //   IR Logic
endmodule

module Registerfile (
  input  [31:0] regval,
  input  Reset,
  input  clock,
  input  dwrite,
  input  swrite,
  input  twrite,
  input  [2:0] dsel,
  input  [2:0] ssel,
  input  [2:0] tsel,
  output [31:0] r0,
  output [31:0] r1,
  output [31:0] r2,
  output [31:0] r3,
  output [31:0] r4,
  output [31:0] r5,
  output [31:0] r6,
  output [31:0] r7,
  output [31:0] dreg,
  output [31:0] sreg,
  output [31:0] treg
);

  wire demultiplexer_1_out0, demultiplexer_1_out1, demultiplexer_1_out2, demultiplexer_1_out3,
       demultiplexer_1_out4, demultiplexer_1_out5, demultiplexer_1_out6, demultiplexer_1_out7;

  Demultiplexer #(.select(3)) demultiplexer_1 (
    .out0(demultiplexer_1_out0), .out1(demultiplexer_1_out1), .out2(demultiplexer_1_out2),
    .out3(demultiplexer_1_out3), .out4(demultiplexer_1_out4), .out5(demultiplexer_1_out5),
    .out6(demultiplexer_1_out6), .out7(demultiplexer_1_out7), .in(dwrite), .sel(dsel));
  Demultiplexer #(.select(3)) demultiplexer_2 (
    .out0(demultiplexer_1_out0), .out1(demultiplexer_1_out1), .out2(demultiplexer_1_out2),
    .out3(demultiplexer_1_out3), .out4(demultiplexer_1_out4), .out5(demultiplexer_1_out5),
    .out6(demultiplexer_1_out6), .out7(demultiplexer_1_out7), .in(swrite), .sel(ssel));
  Demultiplexer #(.select(3)) demultiplexer_3 (
    .out0(demultiplexer_1_out0), .out1(demultiplexer_1_out1), .out2(demultiplexer_1_out2),
    .out3(demultiplexer_1_out3), .out4(demultiplexer_1_out4), .out5(demultiplexer_1_out5),
    .out6(demultiplexer_1_out6), .out7(demultiplexer_1_out7), .in(twrite), .sel(tsel));
  Register #(.width(32)) register_1 (.D(regval), .en(demultiplexer_1_out0), .Q(r0), .clk(clock), .clr(Reset));
  Register #(.width(32)) register_2 (.D(regval), .en(demultiplexer_1_out1), .Q(r1), .clk(clock), .clr(Reset));
  Register #(.width(32)) register_3 (.D(regval), .en(demultiplexer_1_out2), .Q(r2), .clk(clock), .clr(Reset));
  Register #(.width(32)) register_4 (.D(regval), .en(demultiplexer_1_out3), .Q(r3), .clk(clock), .clr(Reset));
  Register #(.width(32)) register_5 (.D(regval), .en(demultiplexer_1_out4), .Q(r4), .clk(clock), .clr(Reset));
  Register #(.width(32)) register_6 (.D(regval), .en(demultiplexer_1_out5), .Q(r5), .clk(clock), .clr(Reset));
  Register #(.width(32)) register_7 (.D(regval), .en(demultiplexer_1_out6), .Q(r6), .clk(clock), .clr(Reset));
  Register #(.width(32)) register_8 (.D(regval), .en(demultiplexer_1_out7), .Q(r7), .clk(clock), .clr(Reset));
  Multiplexer #(.select(3), .width(32)) multiplexer_1 (
    .in0(r0), .in1(r1), .in2(r2), .in3(r3), .in4(r4), .in5(r5), .in6(r6), .in7(r7), .out(dreg), .sel(dsel));
  Multiplexer #(.select(3), .width(32)) multiplexer_2 (
    .in0(r0), .in1(r1), .in2(r2), .in3(r3), .in4(r4), .in5(r5), .in6(r6), .in7(r7), .out(sreg), .sel(ssel));
  Multiplexer #(.select(3), .width(32)) multiplexer_3 (
    .in0(r0), .in1(r1), .in2(r2), .in3(r3), .in4(r4), .in5(r5), .in6(r6), .in7(r7), .out(treg), .sel(tsel));

  // Notes on the sheet:
  //   Register File
endmodule

module PC (
  input  [31:0] imreg,
  input  pcload,
  input  clock,
  input  reset,
  input  [1:0] pcsel,
  input  [31:0] sreg,
  output [31:0] pcout
);

  wire [31:0] adder_1_out, adder_2_out, multiplexer_1_out;

  Adder #(.width(32)) adder_1 (.a(pcout), .b(32'h1), .out(adder_1_out));  // open: cin, cout
  Adder #(.width(32)) adder_2 (.a(pcout), .b(imreg), .out(adder_2_out));  // open: cin, cout
  Multiplexer #(.select(2), .width(32)) multiplexer_1 (
    .in0(sreg), .in1(imreg), .in2(adder_1_out), .in3(adder_2_out), .out(multiplexer_1_out), .sel(pcsel));
  Register #(.width(32)) register_1 (.D(multiplexer_1_out), .en(pcload), .Q(pcout), .clk(clock), .clr(reset));

  // Notes on the sheet:
  //   PC Logic
endmodule

module ShowHexa (
  input  [31:0] Data,
  output [3:0] out_2,
  output [3:0] out_3,
  output [3:0] out_4,
  output [3:0] out_5,
  output [3:0] Digit,
  output [3:0] out_7,
  output [3:0] out_8,
  output [3:0] out_9
);


  assign Digit = Data[15:12];
  assign out_2 = Data[31:28];
  assign out_3 = Data[27:24];
  assign out_4 = Data[23:20];
  assign out_5 = Data[19:16];
  assign out_7 = Data[11:8];
  assign out_8 = Data[7:4];
  assign out_9 = Data[3:0];
endmodule

module Frame_Buffer_16x16 (
  input  [3:0] address,
  input  store,
  input  [15:0] data,
  input  clock,
  input  reset,
  output [15:0] out_6,
  output [15:0] out_7,
  output [15:0] out_8,
  output [15:0] out_9,
  output [15:0] out_10,
  output [15:0] out_11,
  output [15:0] out_12,
  output [15:0] out_13,
  output [15:0] out_14,
  output [15:0] out_15,
  output [15:0] out_16,
  output [15:0] out_17,
  output [15:0] out_18,
  output [15:0] out_19,
  output [15:0] out_20,
  output [15:0] out_21
);

  wire demultiplexer_1_out0, demultiplexer_1_out1, demultiplexer_1_out2, demultiplexer_1_out3,
       demultiplexer_1_out4, demultiplexer_1_out5, demultiplexer_1_out6, demultiplexer_1_out7,
       demultiplexer_1_out8, demultiplexer_1_out9, demultiplexer_1_out10, demultiplexer_1_out11,
       demultiplexer_1_out12, demultiplexer_1_out13, demultiplexer_1_out14, demultiplexer_1_out15;

  Demultiplexer #(.select(4)) demultiplexer_1 (
    .out0(demultiplexer_1_out0), .out1(demultiplexer_1_out1), .out2(demultiplexer_1_out2),
    .out3(demultiplexer_1_out3), .out4(demultiplexer_1_out4), .out5(demultiplexer_1_out5),
    .out6(demultiplexer_1_out6), .out7(demultiplexer_1_out7), .out8(demultiplexer_1_out8),
    .out9(demultiplexer_1_out9), .out10(demultiplexer_1_out10), .out11(demultiplexer_1_out11),
    .out12(demultiplexer_1_out12), .out13(demultiplexer_1_out13), .out14(demultiplexer_1_out14),
    .out15(demultiplexer_1_out15), .in(store), .sel(address));
  Register #(.width(16)) register_1 (.D(data), .en(demultiplexer_1_out0), .Q(out_6), .clk(clock), .clr(reset));
  Register #(.width(16)) register_2 (.D(data), .en(demultiplexer_1_out1), .Q(out_7), .clk(clock), .clr(reset));
  Register #(.width(16)) register_3 (.D(data), .en(demultiplexer_1_out2), .Q(out_8), .clk(clock), .clr(reset));
  Register #(.width(16)) register_4 (.D(data), .en(demultiplexer_1_out3), .Q(out_9), .clk(clock), .clr(reset));
  Register #(.width(16)) register_5 (.D(data), .en(demultiplexer_1_out4), .Q(out_10), .clk(clock), .clr(reset));
  Register #(.width(16)) register_6 (.D(data), .en(demultiplexer_1_out5), .Q(out_11), .clk(clock), .clr(reset));
  Register #(.width(16)) register_7 (.D(data), .en(demultiplexer_1_out6), .Q(out_12), .clk(clock), .clr(reset));
  Register #(.width(16)) register_8 (.D(data), .en(demultiplexer_1_out7), .Q(out_13), .clk(clock), .clr(reset));
  Register #(.width(16)) register_9 (.D(data), .en(demultiplexer_1_out8), .Q(out_14), .clk(clock), .clr(reset));
  Register #(.width(16)) register_10 (.D(data), .en(demultiplexer_1_out9), .Q(out_15), .clk(clock), .clr(reset));
  Register #(.width(16)) register_11 (.D(data), .en(demultiplexer_1_out10), .Q(out_16), .clk(clock), .clr(reset));
  Register #(.width(16)) register_12 (.D(data), .en(demultiplexer_1_out11), .Q(out_17), .clk(clock), .clr(reset));
  Register #(.width(16)) register_13 (.D(data), .en(demultiplexer_1_out12), .Q(out_18), .clk(clock), .clr(reset));
  Register #(.width(16)) register_14 (.D(data), .en(demultiplexer_1_out13), .Q(out_19), .clk(clock), .clr(reset));
  Register #(.width(16)) register_15 (.D(data), .en(demultiplexer_1_out14), .Q(out_20), .clk(clock), .clr(reset));
  Register #(.width(16)) register_16 (.D(data), .en(demultiplexer_1_out15), .Q(out_21), .clk(clock), .clr(reset));
endmodule

module Address_Decoder (
  input  [31:0] Address,
  output RAM,
  output FB_LED,
  output TTY,
  output output_3
);


  assign FB_LED = 1'b1;
  assign output_3 = 1'b1;
  assign RAM = 1'b1;
  assign TTY = 1'b1;
endmodule

module Counters (
  input  [7:0] new_ucounter,
  input  reset,
  input  clock,
  output [15:0] cycles,
  output [3:0] icycles,
  output [15:0] cmds
);

  wire nor_1_out;

  nor nor_1 (nor_1_out, new_ucounter[7], new_ucounter[6], new_ucounter[5], new_ucounter[4], new_ucounter[2], new_ucounter[1], new_ucounter[0], new_ucounter[3]);
  Counter #(.max('hffff), .width(16)) counter_1 (
    .Q(cycles), .clk(clock), .clr(reset));  // open: load, D, count, carry, up
  Counter #(.max('hf), .width(4)) counter_2 (
    .load(nor_1_out), .D(4'b0000), .Q(icycles), .clk(clock), .clr(reset));  // open: count, carry, up
  Counter #(.max('hffff), .width(16)) counter_3 (
    .count(nor_1_out), .Q(cmds), .clk(clock), .clr(reset));  // open: load, D, carry, up
  // Probe on cycles
  // Probe on icycles
  // Probe on cmds

  // Notes on the sheet:
  //   Counts the number of clock cycles
  //   since the start.
  //   Counts the number of clock cycles
  //   since the start of current instruction.
  //   Counts the number of instructions
  //   since the start.
  //   Cycle/Cmds Counters
endmodule

module DebugUnit (
  input  reset,
  input  \continue ,
  input  clock,
  input  [15:0] pcreg,
  input  [15:0] break_addr,
  input  break_on_addr,
  input  [7:0] ucounter,
  input  break_on_instr,
  input  break_on_cycle,
  output clock_out
);

  wire and_1_out, and_2_out, and_3_out, nor_1_out, nor_2_out, nor_3_out, or_1_out, shift_register_1_out,
       shift_register_1_q0;
  wire [15:0] xor_1_out;

  Shift_Register #(.length(2), .trigger("falling")) shift_register_1 (
    .in(\continue ), .clk(clock), .out(shift_register_1_out), .clr(reset), .q0(shift_register_1_q0));  // open: shift, load, d0, d1, q1
  assign xor_1_out = pcreg ^ break_addr;  // XOR_Gate xor_1, 16 bits wide
  LED Addr (.in(break_on_addr));
  and and_1 (and_1_out, ~shift_register_1_out, shift_register_1_q0);  // AND_Gate
  nor nor_1 (nor_1_out, xor_1_out[15], xor_1_out[14], xor_1_out[13], xor_1_out[12], xor_1_out[11], xor_1_out[10], xor_1_out[9], xor_1_out[8], xor_1_out[6], xor_1_out[5], xor_1_out[4], xor_1_out[3], xor_1_out[2], xor_1_out[1], xor_1_out[0], xor_1_out[7]);
  and and_2 (and_2_out, nor_1_out, break_on_addr, nor_2_out);
  nor nor_2 (nor_2_out, ucounter[7], ucounter[6], ucounter[5], ucounter[4], ucounter[2], ucounter[1], ucounter[0], ucounter[3]);
  and and_3 (and_3_out, nor_2_out, break_on_instr);
  LED Instr (.in(break_on_instr));
  LED Cycle (.in(break_on_cycle));
  nor nor_3 (nor_3_out, and_2_out, and_3_out, break_on_cycle);
  or or_1 (or_1_out, and_1_out, nor_3_out);
  LED Pass (.in(or_1_out));
  and and_4 (clock_out, clock, or_1_out);

  // Notes on the sheet:
  //   Breaks on PC = break_addr
  //   Breaks on each new instruction
  //   Breaks on each clock pulse
  //   Makes sure the 'continue' button only
  //   lets through 1 clock pulse, until you let go
  //   and press it again.
  //   Outputs 1 only on first cycle (shift bits are unequal).
  //   Debug Unit
  //   PC = break_addr?
endmodule

module ImmediateReg (
  input  [31:0] DataIn,
  input  IMLoad,
  input  CLKin,
  output [31:0] ImmOut
);

  Register #(.width(32)) register_1 (.D(DataIn), .en(IMLoad), .Q(ImmOut), .clk(CLKin));  // open: clr
  // Probe on ImmOut
endmodule
