// Logisim project mimo_32bit_v3.3.3 - Predikcije.circ as structural Verilog: 19 circuits, main circuit MiMo_Pipelined_v2
module MiMo_Pipelined_v2 (
  input  Stop_Addr,
  input  Cycle,
  input  [15:0] Break_Addr
);

  wire ADDR_DEC_output_3, alu_1_carry, alu_1_negative, alu_1_overflow, alu_1_zero, and_1_out, and_2_out,
       and_3_out, and_4_out, and_5_out, and_6_out, and_7_out, and_8_out, and_9_out, and_10_out, and_11_out,
       and_12_out, and_13_out, and_14_out, and_17_out, and_20_out, and_21_out, and_22_out, bubble,
       button_2_out, button_3_out, button_4_out, button_5_out, button_6_out, button_7_out, C, Clear_out,
       Clear_Screen_out, CLK, CLKin, comparator_1_eq, comparator_2_gt, comparator_3_lt, comparator_4_eq,
       comparator_6_gt, comparator_7_eq, comparator_8_eq, cond_met, cont, corrPred, corrPred2, datawrite,
       dwrite, ex_to_ma_1_imload_out, ex_to_ma_1_swrite_out, ex_to_ma_1_twrite_out, FB_LED, flagsForwards,
       flgset, flush, id_to_ex_1_datawrite_out, id_to_ex_1_imload_out, id_to_ex_1_swrite_out,
       id_to_ex_1_twrite_out, imload, instruction_reg_1_set_flags, load_LR, LSB, LSB0, LSB1, LSB2, LSBc,
       LSBc1, LSBc2, LSBc3, LSBc4, MSB, MSB0, MSB1, MSB2, MSBc1, MSBc2, MSBc3, MSBc4, multiplexer_5_out,
       multiplexer_13_out, multiplexer_14_out, multiplexer_20_out, multiplexer_50_out, multiplexer_54_out,
       multiplexer_56_out, multiplexer_57_out, multiplexer_89_out, N, negOp2, nor_1_out, not_1_out,
       not_2_out, not_3_out, not_4_out, not_5_out, not_6_out, not_7_out, not_8_out, not_9_out, not_10_out,
       not_11_out, not_12_out, not_13_out, not_15_out, oneBit, or_1_out, or_2_out, or_4_out, or_5_out,
       or_6_out, or_7_out, predicted_jump, prediction_crct, prev_predict, prev_shld_predict, prev_uncond,
       prevCond, prevCond1, prevCond2, prevDwrite, prevDwrite1, RAMSel, register_5_q, register_6_q,
       register_9_q, register_11_q, register_12_q, register_15_q, register_16_q, register_17_q,
       register_18_q, Reset, rvrsOps, should_predict, str_LR, swrite, tournament, TTYSel, twrite, uncond,
       update_c1, update_c2, update_c3, update_c4, V, Z;
  wire [1:0] addrsel, datasel, id_to_ex_1_addrsel_out, id_to_ex_1_datasel_out, multiplexer_1_out,
       multiplexer_2_out, multiplexer_3_out, multiplexer_4_out, multiplexer_15_out, multiplexer_16_out,
       multiplexer_17_out, multiplexer_18_out, multiplexer_21_out, multiplexer_22_out, multiplexer_23_out,
       multiplexer_24_out, multiplexer_25_out, multiplexer_26_out, multiplexer_27_out, multiplexer_28_out,
       multiplexer_29_out, multiplexer_30_out, multiplexer_31_out, multiplexer_32_out, multiplexer_33_out,
       multiplexer_34_out, multiplexer_35_out, multiplexer_36_out, multiplexer_37_out, multiplexer_38_out,
       multiplexer_39_out, multiplexer_40_out, multiplexer_43_out, multiplexer_44_out, multiplexer_45_out,
       multiplexer_46_out, multiplexer_47_out, multiplexer_48_out, multiplexer_59_out, multiplexer_60_out,
       multiplexer_61_out, multiplexer_62_out, multiplexer_63_out, multiplexer_64_out, multiplexer_65_out,
       multiplexer_66_out, multiplexer_67_out, multiplexer_68_out, multiplexer_69_out, multiplexer_70_out,
       multiplexer_71_out, multiplexer_72_out, multiplexer_73_out, multiplexer_74_out, multiplexer_75_out,
       multiplexer_76_out, multiplexer_77_out, multiplexer_78_out, multiplexer_79_out, multiplexer_80_out,
       multiplexer_81_out, multiplexer_82_out, op2sel, pcsel, pcsel1, pcsel1Prev, prevRegsrc, prevRegsrc1,
       register_4_q, regsrc, shift_register_2_q0, sselForward, tselForward, two_bit_update, two_bit_update_c,
       two_bit_update_c1, two_bit_update_c2, two_bit_update_c3, two_bit_update_c4, update_CPT, update_GPT,
       update_LPT;
  wire [2:0] ex_to_ma_1_dregsel_out, ex_to_ma_1_sregsel_out, ex_to_ma_1_tregsel_out, id_to_ex_1_dregselout,
       id_to_ex_1_sregselout, id_to_ex_1_tregselout, instruction_reg_1_dregsel, lht_1_lpt_addr, lht_1_r0,
       lht_1_r1, lht_1_r2, lht_1_r3, lht_1_r4, lht_1_r5, lht_1_r6, lht_1_r7, lht_2_lpt_addr, lht_2_r0,
       lht_2_r1, lht_2_r2, lht_2_r3, lht_2_r4, lht_2_r5, lht_2_r6, lht_2_r7, ma_to_wb_1_dregsel_out,
       ma_to_wb_1_sregsel_out, ma_to_wb_1_tregsel_out, multiplexer_8_out, multiplexer_88_out, prevRd,
       prevRd1, prevRd2, shift_register_1_out, ssel, tsel;
  wire [3:0] aluop, instruction_reg_1_condition, multiplexer_99_out, showhexa_1_digit, showhexa_1_out_2,
       showhexa_1_out_3, showhexa_1_out_4, showhexa_1_out_5, showhexa_1_out_7, showhexa_1_out_8,
       showhexa_1_out_9, showhexa_2_digit, showhexa_2_out_2, showhexa_2_out_3, showhexa_2_out_4,
       showhexa_2_out_5, showhexa_2_out_7, showhexa_2_out_8, showhexa_2_out_9, showhexa_3_digit,
       showhexa_3_out_2, showhexa_3_out_3, showhexa_3_out_4, showhexa_3_out_5, showhexa_3_out_7,
       showhexa_3_out_8, showhexa_3_out_9, showhexa_4_digit, showhexa_4_out_2, showhexa_4_out_3,
       showhexa_4_out_4, showhexa_4_out_5, showhexa_4_out_7, showhexa_4_out_8, showhexa_4_out_9,
       showhexa_5_digit, showhexa_5_out_2, showhexa_5_out_3, showhexa_5_out_4, showhexa_5_out_5,
       showhexa_5_out_7, showhexa_5_out_8, showhexa_5_out_9, showhexa_6_digit, showhexa_6_out_2,
       showhexa_6_out_3, showhexa_6_out_4, showhexa_6_out_5, showhexa_6_out_7, showhexa_6_out_8,
       showhexa_6_out_9;
  wire [6:0] adder_2_out, adder_3_out, instruction_reg_1_opcode, multiplexer_9_out, multiplexer_10_out,
       register_1_q, register_3_q, register_14_q;
  wire [7:0] multiplexer_58_out;
  wire [9:0] id_to_ex_1_immedout, instruction_reg_1_immed, multiplexer_87_out;
  wire [15:0] counter_1_q, IFaddr;
  wire [31:0] adder_1_out, alu_1_result, datain, ex_to_ma_1_aluout_out, ex_to_ma_1_immed_out,
       ex_to_ma_1_instruction_out, ex_to_ma_1_rs_out, ex_to_ma_1_rt_out, frame_buffer_16x32_1_out_6,
       frame_buffer_16x32_1_out_7, frame_buffer_16x32_1_out_8, frame_buffer_16x32_1_out_9,
       frame_buffer_16x32_1_out_10, frame_buffer_16x32_1_out_11, frame_buffer_16x32_1_out_12,
       frame_buffer_16x32_1_out_13, frame_buffer_16x32_1_out_14, frame_buffer_16x32_1_out_15,
       frame_buffer_16x32_1_out_16, frame_buffer_16x32_1_out_17, frame_buffer_16x32_1_out_18,
       frame_buffer_16x32_1_out_19, frame_buffer_16x32_1_out_20, frame_buffer_16x32_1_out_21,
       id_to_ex_1_instruction_out, id_to_ex_1_rs_out, id_to_ex_1_rt_out, if_to_id_1_instructionout, immed,
       Instruction_RAM_data, LR, ma_to_wb_1_aluout_out, ma_to_wb_1_immed_out, ma_to_wb_1_instruction_out,
       ma_to_wb_1_operand_out, ma_to_wb_1_rs_out, multiplexer_6_out, multiplexer_7_out, multiplexer_49_out,
       multiplexer_90_out, multiplexer_91_out, multiplexer_92_out, multiplexer_93_out, multiplexer_98_out,
       multiplexer_101_out, multiplexer_102_out, not_14_out, pc_1_prev_pc, predicted_immed, ram_11_data,
       register_13_q, register_bank_1_dreg, register_bank_1_r0, register_bank_1_r1, register_bank_1_r2,
       register_bank_1_r3, register_bank_1_r4, register_bank_1_r5, register_bank_1_r6, register_bank_1_r7,
       register_bank_1_treg, regwrite, rom_1_data, Rs;
  wire [31:3] multiplexer_8_out_2;
  wire [31:4] multiplexer_99_out_2;
  wire [31:16] pc_1_pcout;

  Counter #(.max('hffff), .width(16)) counter_1 (
    .count(CLK), .Q(counter_1_q), .up(1'b1), .clk(CLK), .clr(Reset));  // open: load, D, carry
  Clock clock_1 (.out(CLKin));
  Button button_1 (.out(Reset));
  // Probe on counter_1_q
  // Probe on pcsel
  Multiplexer #(.width(2)) multiplexer_1 (.in0(pcsel), .in1(2'b00), .out(multiplexer_1_out), .sel(prev_shld_predict));
  Multiplexer #(.width(2)) multiplexer_2 (.in0(2'b00), .in1(pcsel1), .out(multiplexer_2_out), .sel(predicted_jump));
  LED u_N (.in(N));
  LED u_V (.in(V));
  LED u_Z (.in(Z));
  LED u_C (.in(C));
  Multiplexer #(.width(2)) multiplexer_3 (
    .in0(multiplexer_1_out), .in1(multiplexer_2_out), .out(multiplexer_3_out), .sel(should_predict));
  Multiplexer #(.width(2)) multiplexer_4 (
    .in0(multiplexer_3_out), .in1(pcsel1Prev), .out(multiplexer_4_out), .sel(flush));
  Multiplexer multiplexer_5 (.in0(1'b1), .in1(1'b0), .out(multiplexer_5_out), .sel(bubble));
  and and_1 (and_1_out, predicted_jump, should_predict);
  Hex_Digit_Display hex_digit_display_1 (.value(showhexa_1_out_2));  // open: dp
  Hex_Digit_Display hex_digit_display_2 (.value(showhexa_1_out_3));  // open: dp
  ShowHexa showhexa_1 (
    .Data({pc_1_pcout, IFaddr}), .out_3(showhexa_1_out_3), .out_4(showhexa_1_out_4),
    .out_5(showhexa_1_out_5), .Digit(showhexa_1_digit), .out_7(showhexa_1_out_7), .out_8(showhexa_1_out_8),
    .out_9(showhexa_1_out_9), .out_2(showhexa_1_out_2));
  PC pc_1 (
    .imreg(multiplexer_7_out), .pcsel(multiplexer_4_out), .pcload(multiplexer_5_out), .flush(flush),
    .clock(CLK), .reset(Reset), .should_predict(should_predict), .pcout({pc_1_pcout, IFaddr}),
    .prev_pc(pc_1_prev_pc));
  Multiplexer #(.width(32)) multiplexer_6 (.in0(immed), .in1(predicted_immed), .out(multiplexer_6_out));  // open: sel
  Hex_Digit_Display hex_digit_display_3 (.value(showhexa_1_out_4));  // open: dp
  Hex_Digit_Display hex_digit_display_4 (.value(showhexa_1_out_5));  // open: dp
  Multiplexer #(.width(32)) multiplexer_7 (.in0(multiplexer_6_out), .in1(LR), .out(multiplexer_7_out), .sel(str_LR));
  Button u_Cont (.out(cont));
  Hex_Digit_Display hex_digit_display_5 (.value(showhexa_1_digit));  // open: dp
  Hex_Digit_Display hex_digit_display_6 (.value(showhexa_1_out_7));  // open: dp
  Shift_Register #(.length(3)) shift_register_1 (
    .shift(prev_shld_predict), .in(cond_met), .clk(CLK), .out(shift_register_1_out[0]), .clr(Reset),
    .q0(shift_register_1_out[2]), .q1(shift_register_1_out[1]));  // open: load, d0, d1, d2, q2
  Hex_Digit_Display hex_digit_display_7 (.value(showhexa_1_out_8));  // open: dp
  Hex_Digit_Display hex_digit_display_8 (.value(showhexa_1_out_9));  // open: dp
  Multiplexer #(.width(32)) multiplexer_8 (
    .in0({pc_1_pcout, IFaddr}), .in1(pc_1_prev_pc), .out({multiplexer_8_out_2, multiplexer_8_out}),
    .sel(prev_shld_predict));
  DebugUnit debugunit_1 (
    .reset(Reset), .\continue (cont), .clock(CLKin), .IFaddr(IFaddr), .break_addr(Break_Addr),
    .break_on_addr(Stop_Addr), .break_on_cycle(Cycle), .clock_out(CLK));
  RAM #(.addrWidth(16), .asyncread("true"), .dataWidth(32), .databus("bidir")) Instruction_RAM (
    .addr(IFaddr), .we(1'b0), .oe(1'b1), .clk(CLK), .data(Instruction_RAM_data));
  Adder #(.width(32)) adder_1 (.a(pc_1_prev_pc), .b(32'h1), .out(adder_1_out));  // open: cin, cout
  Multiplexer #(.width(7)) multiplexer_9 (.in0(7'b1001110), .in1(7'b1010100), .out(multiplexer_9_out), .sel(cond_met));
  Multiplexer #(.width(7)) multiplexer_10 (
    .in0(7'b1001110), .in1(7'b1010100), .out(multiplexer_10_out), .sel(predicted_jump));
  Adder #(.width(7)) adder_2 (.a(register_1_q), .b(7'b0000001), .out(adder_2_out));  // open: cin, cout
  not not_1 (not_1_out, prev_uncond);
  Register #(.width(7)) register_1 (.D(adder_2_out), .en(flush), .Q(register_1_q), .clk(CLK), .clr(Reset));
  and and_2 (and_2_out, prev_shld_predict, not_1_out);
  and and_3 (and_3_out, prev_shld_predict, not_2_out);
  not not_2 (not_2_out, prev_uncond);
  and and_4 (and_4_out, prev_shld_predict, not_3_out);
  not not_3 (not_3_out, prev_uncond);
  and and_5 (and_5_out, prev_shld_predict, not_4_out);
  not not_4 (not_4_out, prev_uncond);
  and and_6 (and_6_out, prev_shld_predict, not_5_out);
  not not_5 (not_5_out, prev_uncond);
  and and_7 (and_7_out, prev_shld_predict, not_6_out);
  not not_6 (not_6_out, prev_uncond);
  Register #(.width(32)) register_2 (.D(adder_1_out), .en(load_LR), .Q(LR), .clk(CLK), .clr(Reset));
  // Probe on LR
  TTY #(.cols(16), .rows(4)) tty_1 (.data(multiplexer_9_out), .clk(CLK), .we(prev_shld_predict), .clr(Reset));
  TTY #(.cols(16), .rows(4)) tty_2 (.data(multiplexer_10_out), .clk(CLK), .we(should_predict), .clr(Reset));
  // Probe on register_1_q
  and and_8 (and_8_out, prev_shld_predict, not_7_out);
  not not_7 (not_7_out, prev_uncond);
  // Probe on lht_1_r0
  // Probe on lht_1_r1
  // Probe on lht_1_r2
  // Probe on lht_1_r3
  // Probe on lht_1_r4
  // Probe on lht_1_r5
  // Probe on lht_1_r6
  // Probe on lht_1_r7
  and and_9 (and_9_out, and_3_out, update_c1);
  and and_10 (and_10_out, and_4_out, update_c2);
  and and_11 (and_11_out, and_5_out, update_c3);
  and and_12 (and_12_out, and_6_out, update_c4);
  // Probe on lht_2_r0
  // Probe on lht_2_r1
  // Probe on lht_2_r2
  // Probe on lht_2_r3
  // Probe on lht_2_r4
  // Probe on lht_2_r5
  // Probe on lht_2_r6
  // Probe on lht_2_r7
  and and_13 (and_13_out, prev_shld_predict, not_8_out);
  not not_8 (not_8_out, prev_uncond);
  and and_14 (and_14_out, prev_shld_predict, not_9_out);
  not not_9 (not_9_out, prev_uncond);
  Adder #(.width(7)) adder_3 (.a(register_3_q), .b(7'b0000001), .out(adder_3_out));  // open: cin, cout
  LHT lht_1 (
    .address(multiplexer_8_out), .store(prev_shld_predict), .data_in(cond_met), .clk(CLK), .reset(Reset),
    .lpt_addr(lht_1_lpt_addr), .r0(lht_1_r0), .r1(lht_1_r1), .r2(lht_1_r2), .r3(lht_1_r3), .r4(lht_1_r4),
    .r5(lht_1_r5), .r6(lht_1_r6), .r7(lht_1_r7));
  RAM #(.addrWidth(3), .asyncread("true"), .clearpin("true"), .dataWidth(2)) ram_1 (
    .addr(lht_1_lpt_addr), .we(and_2_out), .oe(should_predict), .clk(CLK), .din(two_bit_update_c),
    .dout({corrPred, LSBc}), .clr(Reset));
  LHT lht_2 (
    .address(multiplexer_8_out), .store(prev_shld_predict), .data_in(cond_met), .clk(CLK), .reset(Reset),
    .lpt_addr(lht_2_lpt_addr), .r0(lht_2_r0), .r1(lht_2_r1), .r2(lht_2_r2), .r3(lht_2_r3), .r4(lht_2_r4),
    .r5(lht_2_r5), .r6(lht_2_r6), .r7(lht_2_r7));
  Comparator #(.mode("unsigned"), .width(4)) comparator_1 (
    .a(Instruction_RAM_data[22:19]), .b(4'b0001), .eq(comparator_1_eq));  // open: gt, lt
  Comparator #(.mode("unsigned"), .width(7)) comparator_2 (
    .a(Instruction_RAM_data[31:25]), .b(7'b0010111), .gt(comparator_2_gt));  // open: eq, lt
  Comparator #(.mode("unsigned"), .width(7)) comparator_3 (
    .a(Instruction_RAM_data[31:25]), .b(7'b0011100), .lt(comparator_3_lt));  // open: gt, eq
  Comparator #(.mode("unsigned"), .width(7)) comparator_4 (
    .a(Instruction_RAM_data[31:25]), .b(7'b0011001), .eq(comparator_4_eq));  // open: gt, lt
  Comparator #(.mode("unsigned"), .width(7)) comparator_5 (
    .a(Instruction_RAM_data[31:25]), .b(7'b0011011), .eq(str_LR));  // open: gt, lt
  Register #(.width(7)) register_3 (.D(adder_3_out), .en(prev_shld_predict), .Q(register_3_q), .clk(CLK), .clr(Reset));
  RAM #(.addrWidth(3), .asyncread("true"), .clearpin("true"), .dataWidth(1)) ram_2 (
    .addr(multiplexer_8_out), .we(flush), .oe(should_predict), .clk(CLK), .din(not_10_out), .dout(oneBit),
    .clr(Reset));
  not not_10 (not_10_out, prev_predict);
  RAM #(.addrWidth(3), .asyncread("true"), .clearpin("true"), .dataWidth(2)) ram_3 (
    .addr(multiplexer_8_out), .we(and_8_out), .oe(should_predict), .clk(CLK), .din(two_bit_update),
    .dout({MSB, LSB}), .clr(Reset));
  RAM #(.addrWidth(3), .asyncread("true"), .clearpin("true"), .dataWidth(2)) ram_4 (
    .addr(multiplexer_8_out), .we(and_9_out), .oe(should_predict), .clk(CLK), .din(two_bit_update_c1),
    .dout({MSBc1, LSBc1}), .clr(Reset));
  RAM #(.addrWidth(3), .asyncread("true"), .clearpin("true"), .dataWidth(2)) ram_5 (
    .addr(multiplexer_8_out), .we(and_10_out), .oe(should_predict), .clk(CLK), .din(two_bit_update_c2),
    .dout({MSBc2, LSBc2}), .clr(Reset));
  RAM #(.addrWidth(3), .asyncread("true"), .clearpin("true"), .dataWidth(2)) ram_6 (
    .addr(multiplexer_8_out), .we(and_11_out), .oe(should_predict), .clk(CLK), .din(two_bit_update_c3),
    .dout({MSBc3, LSBc3}), .clr(Reset));
  RAM #(.addrWidth(3), .asyncread("true"), .clearpin("true"), .dataWidth(2)) ram_7 (
    .addr(multiplexer_8_out), .we(and_12_out), .oe(should_predict), .clk(CLK), .din(two_bit_update_c4),
    .dout({MSBc4, LSBc4}), .clr(Reset));
  RAM #(.addrWidth(3), .asyncread("true"), .clearpin("true"), .dataWidth(2)) ram_8 (
    .addr(shift_register_1_out), .we(and_7_out), .oe(should_predict), .clk(CLK), .din(update_CPT),
    .dout({MSB2, LSB2}), .clr(Reset));
  and and_15 (should_predict, comparator_2_gt, comparator_3_lt);
  Multiplexer #(.width(2)) multiplexer_11 (.in0(2'b01), .in1(2'b10), .out(pcsel1), .sel(comparator_4_eq));
  Button button_2 (.out(button_2_out));
  // Probe on register_3_q
  RAM #(.addrWidth(3), .asyncread("true"), .clearpin("true"), .dataWidth(2)) ram_9 (
    .addr(lht_2_lpt_addr), .we(and_13_out), .oe(should_predict), .clk(CLK), .din(update_GPT),
    .dout({MSB0, LSB0}), .clr(Reset));
  RAM #(.addrWidth(3), .asyncread("true"), .clearpin("true"), .dataWidth(2)) ram_10 (
    .addr(shift_register_1_out), .we(and_14_out), .oe(should_predict), .clk(CLK), .din(update_GPT),
    .dout({MSB1, LSB1}), .clr(Reset));
  Bit_Extendor bit_extendor_1 (.datain(Instruction_RAM_data[9:0]), .dataout(predicted_immed));
  LED led_1 (.in(nor_1_out));
  nor nor_1 (nor_1_out, register_11_q, register_9_q, register_12_q, register_6_q, register_5_q);
  Register #(.width(2)) register_4 (.D(pcsel1), .en(CLK), .Q(register_4_q), .clk(CLK), .clr(Reset));
  Button button_3 (.out(button_3_out));
  LED led_2 (.in(register_5_q));
  or or_1 (or_1_out, button_2_out, button_4_out, button_7_out, button_5_out, button_6_out);
  and and_16 (uncond, comparator_1_eq, should_predict);
  Multiplexer #(.width(2)) multiplexer_12 (.in0(2'b00), .in1(register_4_q), .out(pcsel1Prev), .sel(not_11_out));
  not not_11 (not_11_out, prev_predict);
  Register #(.width(1)) register_5 (
    .D(button_3_out), .en(button_3_out), .Q(register_5_q), .clk(button_3_out), .clr(or_1_out));
  Multiplexer multiplexer_13 (.in0(1'b0), .in1(oneBit), .out(multiplexer_13_out), .sel(register_5_q));
  Button button_4 (.out(button_4_out));
  LED led_3 (.in(register_6_q));
  Register #(.width(1)) register_6 (
    .D(button_4_out), .en(button_4_out), .Q(register_6_q), .clk(button_4_out), .clr(or_2_out));
  or or_2 (or_2_out, button_2_out, button_3_out, button_7_out, button_6_out, button_5_out);
  Multiplexer multiplexer_14 (.in0(multiplexer_13_out), .in1(MSB), .out(multiplexer_14_out), .sel(register_6_q));
  Register #(.width(1)) register_7 (.D(uncond), .en(CLK), .Q(prev_uncond), .clk(CLK), .clr(Reset));
  Register #(.width(1)) register_8 (.D(should_predict), .en(CLK), .Q(prev_shld_predict), .clk(CLK), .clr(Reset));
  Button button_5 (.out(button_5_out));
  or or_3 (predicted_jump, uncond, multiplexer_54_out);
  Multiplexer #(.width(2)) multiplexer_15 (.in0(2'b00), .in1(2'b01), .out(multiplexer_15_out), .sel(cond_met));
  Multiplexer #(.width(2)) multiplexer_16 (.in0(2'b00), .in1(2'b10), .out(multiplexer_16_out), .sel(cond_met));
  Multiplexer #(.width(2)) multiplexer_17 (.in0(2'b01), .in1(2'b11), .out(multiplexer_17_out), .sel(cond_met));
  Multiplexer #(.width(2)) multiplexer_18 (.in0(2'b10), .in1(2'b11), .out(multiplexer_18_out), .sel(cond_met));
  Multiplexer multiplexer_19 (.in0(MSB0), .in1(MSB1), .out(tournament), .sel(MSB2));
  LED led_4 (.in(register_9_q));
  Register #(.width(1)) register_9 (
    .D(button_5_out), .en(button_5_out), .Q(register_9_q), .clk(button_5_out), .clr(or_4_out));
  or or_4 (or_4_out, button_2_out, button_3_out, button_7_out, button_4_out, button_6_out);
  Multiplexer multiplexer_20 (.in0(multiplexer_14_out), .in1(corrPred), .out(multiplexer_20_out), .sel(register_9_q));
  Register #(.width(1)) register_10 (.D(predicted_jump), .en(CLK), .Q(prev_predict), .clk(CLK), .clr(Reset));
  Multiplexer #(.width(2)) multiplexer_21 (.in0(2'b00), .in1(2'b01), .out(multiplexer_21_out), .sel(cond_met));
  Multiplexer #(.width(2)) multiplexer_22 (
    .in0(multiplexer_21_out), .in1(multiplexer_23_out), .out(multiplexer_22_out), .sel(LSB));
  Multiplexer #(.width(2)) multiplexer_23 (.in0(2'b00), .in1(2'b10), .out(multiplexer_23_out), .sel(cond_met));
  Multiplexer #(.width(2)) multiplexer_24 (.in0(2'b01), .in1(2'b11), .out(multiplexer_24_out), .sel(cond_met));
  Multiplexer #(.width(2)) multiplexer_25 (
    .in0(multiplexer_24_out), .in1(multiplexer_26_out), .out(multiplexer_25_out), .sel(LSB));
  Multiplexer #(.width(2)) multiplexer_26 (.in0(2'b10), .in1(2'b11), .out(multiplexer_26_out), .sel(cond_met));
  Multiplexer #(.width(2)) multiplexer_27 (
    .in0(multiplexer_15_out), .in1(multiplexer_16_out), .out(multiplexer_27_out), .sel(LSBc));
  Multiplexer #(.width(2)) multiplexer_28 (
    .in0(multiplexer_17_out), .in1(multiplexer_18_out), .out(multiplexer_28_out), .sel(LSBc));
  and and_17 (and_17_out, prev_shld_predict, not_12_out);
  not not_12 (not_12_out, prev_uncond);
  Multiplexer #(.width(2)) multiplexer_29 (.in0(2'b00), .in1(2'b01), .out(multiplexer_29_out), .sel(cond_met));
  Multiplexer #(.width(2)) multiplexer_30 (.in0(2'b00), .in1(2'b10), .out(multiplexer_30_out), .sel(cond_met));
  Multiplexer #(.width(2)) multiplexer_31 (.in0(2'b01), .in1(2'b11), .out(multiplexer_31_out), .sel(cond_met));
  Multiplexer #(.width(2)) multiplexer_32 (.in0(2'b10), .in1(2'b11), .out(multiplexer_32_out), .sel(cond_met));
  Multiplexer #(.width(2)) multiplexer_33 (.in0(2'b00), .in1(2'b01), .out(multiplexer_33_out), .sel(cond_met));
  Multiplexer #(.width(2)) multiplexer_34 (.in0(2'b00), .in1(2'b10), .out(multiplexer_34_out), .sel(cond_met));
  Multiplexer #(.width(2)) multiplexer_35 (.in0(2'b01), .in1(2'b11), .out(multiplexer_35_out), .sel(cond_met));
  Multiplexer #(.width(2)) multiplexer_36 (.in0(2'b10), .in1(2'b11), .out(multiplexer_36_out), .sel(cond_met));
  Multiplexer #(.width(2)) multiplexer_37 (.in0(2'b00), .in1(2'b01), .out(multiplexer_37_out), .sel(cond_met));
  Multiplexer #(.width(2)) multiplexer_38 (.in0(2'b00), .in1(2'b10), .out(multiplexer_38_out), .sel(cond_met));
  Multiplexer #(.width(2)) multiplexer_39 (.in0(2'b01), .in1(2'b11), .out(multiplexer_39_out), .sel(cond_met));
  Multiplexer #(.width(2)) multiplexer_40 (.in0(2'b10), .in1(2'b11), .out(multiplexer_40_out), .sel(cond_met));
  not not_13 (not_13_out, prediction_crct);
  and and_18 (flush, prev_shld_predict, not_13_out);
  Button button_6 (.out(button_6_out));
  Multiplexer #(.width(2)) multiplexer_41 (
    .in0(multiplexer_22_out), .in1(multiplexer_25_out), .out(two_bit_update), .sel(MSB));
  Multiplexer #(.width(2)) multiplexer_42 (
    .in0(multiplexer_27_out), .in1(multiplexer_28_out), .out(two_bit_update_c), .sel(corrPred));
  Multiplexer #(.width(2)) multiplexer_43 (
    .in0(multiplexer_29_out), .in1(multiplexer_30_out), .out(multiplexer_43_out), .sel(LSB0));
  Multiplexer #(.width(2)) multiplexer_44 (
    .in0(multiplexer_31_out), .in1(multiplexer_32_out), .out(multiplexer_44_out), .sel(LSB0));
  Multiplexer #(.width(2)) multiplexer_45 (
    .in0(multiplexer_33_out), .in1(multiplexer_34_out), .out(multiplexer_45_out), .sel(LSB1));
  Multiplexer #(.width(2)) multiplexer_46 (
    .in0(multiplexer_35_out), .in1(multiplexer_36_out), .out(multiplexer_46_out), .sel(LSB1));
  Multiplexer #(.width(2)) multiplexer_47 (
    .in0(multiplexer_37_out), .in1(multiplexer_38_out), .out(multiplexer_47_out), .sel(LSB2));
  Multiplexer #(.width(2)) multiplexer_48 (
    .in0(multiplexer_39_out), .in1(multiplexer_40_out), .out(multiplexer_48_out), .sel(LSB2));
  Multiplexer #(.width(32)) multiplexer_49 (
    .in0(Instruction_RAM_data), .in1({32{1'b0}}), .out(multiplexer_49_out), .sel(flush));
  LED led_5 (.in(register_11_q));
  Register #(.width(1)) register_11 (
    .D(button_6_out), .en(button_6_out), .Q(register_11_q), .clk(button_6_out), .clr(or_5_out));
  or or_5 (or_5_out, button_2_out, button_3_out, button_7_out, button_4_out, button_5_out);
  Multiplexer multiplexer_50 (.in0(multiplexer_20_out), .in1(corrPred2), .out(multiplexer_50_out), .sel(register_11_q));
  Shift_Register #(.length(2)) shift_register_2 (
    .shift(and_17_out), .in(cond_met), .clk(CLK), .out(shift_register_2_q0[1]), .clr(Reset),
    .q0(shift_register_2_q0[0]));  // open: load, d0, d1, q1
  Multiplexer #(.width(2)) multiplexer_51 (
    .in0(multiplexer_43_out), .in1(multiplexer_44_out), .out(update_LPT), .sel(MSB0));
  Multiplexer #(.width(2)) multiplexer_52 (
    .in0(multiplexer_45_out), .in1(multiplexer_46_out), .out(update_GPT), .sel(MSB1));
  Multiplexer #(.width(2)) multiplexer_53 (
    .in0(multiplexer_47_out), .in1(multiplexer_48_out), .out(update_CPT), .sel(MSB2));
  Button button_7 (.out(button_7_out));
  LED led_6 (.in(register_12_q));
  or or_6 (or_6_out, button_2_out, button_3_out, button_6_out, button_4_out, button_5_out);
  Register #(.width(1)) register_12 (
    .D(button_7_out), .en(button_7_out), .Q(register_12_q), .clk(button_7_out), .clr(or_6_out));
  Multiplexer multiplexer_54 (
    .in0(multiplexer_50_out), .in1(tournament), .out(multiplexer_54_out), .sel(register_12_q));
  Multiplexer #(.select(2)) multiplexer_55 (
    .in0(MSBc1), .in1(MSBc2), .in2(MSBc3), .in3(MSBc4), .out(corrPred2), .sel(shift_register_2_q0));
  Decoder #(.enable("false"), .select(2)) decoder_1 (
    .out0(update_c1), .out1(update_c2), .out2(update_c3), .out3(update_c4), .sel(shift_register_2_q0));
  Hex_Digit_Display hex_digit_display_9 (.value(showhexa_2_out_2));  // open: dp
  Hex_Digit_Display hex_digit_display_10 (.value(showhexa_2_out_3));  // open: dp
  ShowHexa showhexa_2 (
    .Data(multiplexer_49_out), .out_3(showhexa_2_out_3), .out_4(showhexa_2_out_4), .out_5(showhexa_2_out_5),
    .Digit(showhexa_2_digit), .out_7(showhexa_2_out_7), .out_8(showhexa_2_out_8), .out_9(showhexa_2_out_9),
    .out_2(showhexa_2_out_2));
  // Probe on instruction_reg_1_opcode
  IF_to_ID if_to_id_1 (
    .Clk(CLK), .Reset(Reset), .instruction(multiplexer_49_out), .instructionOut(if_to_id_1_instructionout));
  Multiplexer multiplexer_56 (.in0(1'b1), .in1(1'b0), .out(multiplexer_56_out), .sel(bubble));
  Hex_Digit_Display hex_digit_display_11 (.value(showhexa_2_out_4));  // open: dp
  Hex_Digit_Display hex_digit_display_12 (.value(showhexa_2_out_5));  // open: dp
  Hex_Digit_Display hex_digit_display_13 (.value(showhexa_2_digit));  // open: dp
  Hex_Digit_Display hex_digit_display_14 (.value(showhexa_2_out_7));  // open: dp
  Adder adder_4 (.b(8'h1));  // open: a, out, cin, cout
  Multiplexer multiplexer_57 (.in0(1'b1), .in1(1'b0), .out(multiplexer_57_out), .sel(bubble));
  Register #(.width(32)) register_13 (
    .D(if_to_id_1_instructionout), .en(multiplexer_56_out), .Q(register_13_q), .clk(CLK), .clr(Reset));
  Hex_Digit_Display hex_digit_display_15 (.value(showhexa_2_out_8));  // open: dp
  Hex_Digit_Display hex_digit_display_16 (.value(showhexa_2_out_9));  // open: dp
  Multiplexer #(.width(8)) multiplexer_58 (
    .in0({8{1'b0}}), .in1({1'b0, instruction_reg_1_opcode}), .out(multiplexer_58_out), .sel(cond_met));
  Multiplexer #(.width(2)) multiplexer_59 (.in0(2'b00), .in1(2'b01), .out(multiplexer_59_out), .sel(cond_met));
  Multiplexer #(.width(2)) multiplexer_60 (.in0(2'b00), .in1(2'b10), .out(multiplexer_60_out), .sel(cond_met));
  Multiplexer #(.width(2)) multiplexer_61 (.in0(2'b01), .in1(2'b11), .out(multiplexer_61_out), .sel(cond_met));
  Multiplexer #(.width(2)) multiplexer_62 (.in0(2'b10), .in1(2'b11), .out(multiplexer_62_out), .sel(cond_met));
  Multiplexer #(.width(2)) multiplexer_63 (.in0(2'b00), .in1(2'b01), .out(multiplexer_63_out), .sel(cond_met));
  Multiplexer #(.width(2)) multiplexer_64 (.in0(2'b00), .in1(2'b10), .out(multiplexer_64_out), .sel(cond_met));
  Multiplexer #(.width(2)) multiplexer_65 (.in0(2'b01), .in1(2'b11), .out(multiplexer_65_out), .sel(cond_met));
  Multiplexer #(.width(2)) multiplexer_66 (.in0(2'b10), .in1(2'b11), .out(multiplexer_66_out), .sel(cond_met));
  Multiplexer #(.width(2)) multiplexer_67 (.in0(2'b00), .in1(2'b01), .out(multiplexer_67_out), .sel(cond_met));
  Multiplexer #(.width(2)) multiplexer_68 (.in0(2'b00), .in1(2'b10), .out(multiplexer_68_out), .sel(cond_met));
  Multiplexer #(.width(2)) multiplexer_69 (.in0(2'b01), .in1(2'b11), .out(multiplexer_69_out), .sel(cond_met));
  Multiplexer #(.width(2)) multiplexer_70 (.in0(2'b10), .in1(2'b11), .out(multiplexer_70_out), .sel(cond_met));
  Multiplexer #(.width(2)) multiplexer_71 (.in0(2'b00), .in1(2'b01), .out(multiplexer_71_out), .sel(cond_met));
  Multiplexer #(.width(2)) multiplexer_72 (.in0(2'b00), .in1(2'b10), .out(multiplexer_72_out), .sel(cond_met));
  Multiplexer #(.width(2)) multiplexer_73 (.in0(2'b01), .in1(2'b11), .out(multiplexer_73_out), .sel(cond_met));
  Multiplexer #(.width(2)) multiplexer_74 (.in0(2'b10), .in1(2'b11), .out(multiplexer_74_out), .sel(cond_met));
  ROM #(.dataWidth(32)) rom_1 (.addr(multiplexer_58_out), .data({rom_1_data[31:4], load_LR, pcsel, rom_1_data[0]}));
  Multiplexer #(.width(2)) multiplexer_75 (
    .in0(multiplexer_59_out), .in1(multiplexer_60_out), .out(multiplexer_75_out), .sel(LSBc1));
  Multiplexer #(.width(2)) multiplexer_76 (
    .in0(multiplexer_61_out), .in1(multiplexer_62_out), .out(multiplexer_76_out), .sel(LSBc1));
  Multiplexer #(.width(2)) multiplexer_77 (
    .in0(multiplexer_63_out), .in1(multiplexer_64_out), .out(multiplexer_77_out), .sel(LSBc2));
  Multiplexer #(.width(2)) multiplexer_78 (
    .in0(multiplexer_65_out), .in1(multiplexer_66_out), .out(multiplexer_78_out), .sel(LSBc2));
  Multiplexer #(.width(2)) multiplexer_79 (
    .in0(multiplexer_67_out), .in1(multiplexer_68_out), .out(multiplexer_79_out), .sel(LSBc3));
  Multiplexer #(.width(2)) multiplexer_80 (
    .in0(multiplexer_69_out), .in1(multiplexer_70_out), .out(multiplexer_80_out), .sel(LSBc3));
  Multiplexer #(.width(2)) multiplexer_81 (
    .in0(multiplexer_71_out), .in1(multiplexer_72_out), .out(multiplexer_81_out), .sel(LSBc4));
  Multiplexer #(.width(2)) multiplexer_82 (
    .in0(multiplexer_73_out), .in1(multiplexer_74_out), .out(multiplexer_82_out), .sel(LSBc4));
  Hex_Digit_Display hex_digit_display_17 (.value(showhexa_3_out_2));  // open: dp
  Hex_Digit_Display hex_digit_display_18 (.value(showhexa_3_out_3));  // open: dp
  ShowHexa showhexa_3 (
    .Data(register_13_q), .out_3(showhexa_3_out_3), .out_4(showhexa_3_out_4), .out_5(showhexa_3_out_5),
    .Digit(showhexa_3_digit), .out_7(showhexa_3_out_7), .out_8(showhexa_3_out_8), .out_9(showhexa_3_out_9),
    .out_2(showhexa_3_out_2));
  Multiplexer #(.width(2)) multiplexer_83 (
    .in0(multiplexer_75_out), .in1(multiplexer_76_out), .out(two_bit_update_c1), .sel(MSBc1));
  Multiplexer #(.width(2)) multiplexer_84 (
    .in0(multiplexer_77_out), .in1(multiplexer_78_out), .out(two_bit_update_c2), .sel(MSBc2));
  Multiplexer #(.width(2)) multiplexer_85 (
    .in0(multiplexer_79_out), .in1(multiplexer_80_out), .out(two_bit_update_c3), .sel(MSBc3));
  Multiplexer #(.width(2)) multiplexer_86 (
    .in0(multiplexer_81_out), .in1(multiplexer_82_out), .out(two_bit_update_c4), .sel(MSBc4));
  Instruction_Reg instruction_reg_1 (
    .instruction(if_to_id_1_instructionout), .reset(Reset), .clock(CLK), .irload(multiplexer_57_out),
    .immed(instruction_reg_1_immed), .dregsel(instruction_reg_1_dregsel), .sregsel(ssel), .tregsel(tsel),
    .condition(instruction_reg_1_condition), .set_flags(instruction_reg_1_set_flags), .imload(imload),
    .opcode(instruction_reg_1_opcode));
  Hex_Digit_Display hex_digit_display_19 (.value(showhexa_3_out_4));  // open: dp
  Hex_Digit_Display hex_digit_display_20 (.value(showhexa_3_out_5));  // open: dp
  // Probe on instruction_reg_1_dregsel
  // Probe on ssel
  // Probe on tsel
  Multiplexer #(.width(10)) multiplexer_87 (
    .in0({10{1'b0}}), .in1(instruction_reg_1_immed), .out(multiplexer_87_out), .sel(imload));
  Register #(.width(7)) register_14 (.D(instruction_reg_1_opcode), .en(CLK), .Q(register_14_q), .clk(CLK), .clr(Reset));
  Hex_Digit_Display hex_digit_display_21 (.value(showhexa_3_digit));  // open: dp
  Hex_Digit_Display hex_digit_display_22 (.value(showhexa_3_out_7));  // open: dp
  // Probe on instruction_reg_1_condition
  Comparator #(.width(7)) comparator_6 (.a(register_14_q), .b(7'b0011100), .gt(comparator_6_gt));  // open: eq, lt
  RAW_Check raw_check_1 (
    .ssel(ssel), .tsel(tsel), .imload(imload), .prevRd(prevRd), .prevRd1(prevRd1), .prevRd2(prevRd2),
    .prevDatawrite(prevDwrite), .prevCond(prevCond), .prevCond1(prevCond1), .prevDatawrite1(prevDwrite1),
    .flgset(flgset), .prevCond2(prevCond2), .prevDatawrite2(dwrite), .sregsel(sselForward),
    .frwrdFlags(flagsForwards), .tregsel(tselForward));
  Hex_Digit_Display hex_digit_display_23 (.value(showhexa_3_out_8));  // open: dp
  Hex_Digit_Display hex_digit_display_24 (.value(showhexa_3_out_9));  // open: dp
  // Probe on register_bank_1_r0
  Register_Bank register_bank_1 (
    .dselin(ma_to_wb_1_dregsel_out), .regval(regwrite), .dwrite(dwrite), .sselin(ma_to_wb_1_sregsel_out),
    .swrite(swrite), .tselin(ma_to_wb_1_tregsel_out), .twrite(twrite), .clock(CLK),
    .dselout(instruction_reg_1_dregsel), .Reset(Reset), .sselout(ssel), .tselout(tsel),
    .dreg(register_bank_1_dreg), .sreg(Rs), .treg(register_bank_1_treg), .r0(register_bank_1_r0),
    .r1(register_bank_1_r1), .r2(register_bank_1_r2), .r3(register_bank_1_r3), .r4(register_bank_1_r4),
    .r5(register_bank_1_r5), .r6(register_bank_1_r6), .r7(register_bank_1_r7));
  // Probe on register_bank_1_r1
  // Probe on register_bank_1_r2
  // Probe on register_bank_1_r3
  // Probe on register_bank_1_r4
  // Probe on register_bank_1_r5
  // Probe on register_bank_1_r6
  // Probe on register_bank_1_r7
  Comparator #(.width(2)) comparator_7 (.a(2'b01), .b(sselForward), .eq(comparator_7_eq));  // open: gt, lt
  Comparator #(.width(2)) comparator_8 (.a(2'b01), .b(tselForward), .eq(comparator_8_eq));  // open: gt, lt
  Multiplexer #(.width(3)) multiplexer_88 (
    .in0(instruction_reg_1_dregsel), .in1(3'b000), .out(multiplexer_88_out), .sel(bubble));
  Bit_Extendor bit_extendor_2 (.datain(multiplexer_87_out), .dataout(immed));
  and and_19 (bubble, comparator_6_gt, or_7_out);
  or or_7 (or_7_out, comparator_7_eq, comparator_8_eq);
  Multiplexer multiplexer_89 (.in0(cond_met), .in1(1'b0), .out(multiplexer_89_out), .sel(bubble));
  check_condition check_condition_1 (
    .C(C), .Z(Z), .V(V), .N(N), .condition(instruction_reg_1_condition), .cond_met(cond_met));
  Shift_Register #(.length(3)) shift_register_3 (
    .shift(CLK), .in(multiplexer_89_out), .clk(CLK), .out(prevCond2), .clr(Reset), .q0(prevCond),
    .q1(prevCond1));  // open: load, d0, d1, d2, q2
  Shift_Register #(.length(3), .width(3)) shift_register_4 (
    .shift(CLK), .in(multiplexer_88_out), .clk(CLK), .out(prevRd2), .clr(Reset), .q0(prevRd), .q1(prevRd1));  // open: load, d0, d1, d2, q2
  and and_20 (and_20_out, cond_met, instruction_reg_1_set_flags);
  xnor xnor_1 (prediction_crct, cond_met, prev_predict);
  // Probe on register_bank_1_dreg
  // Probe on Rs
  // Probe on register_bank_1_treg
  ID_to_EX id_to_ex_1 (
    .Bubble(bubble), .Clk(CLK), .Reset(Reset), .sselForward(sselForward), .tselForward(tselForward),
    .aluop(rom_1_data[10:7]), .negOp2(rom_1_data[11]), .rvrsOps(rom_1_data[12]), .datasel(rom_1_data[14:13]),
    .datawrite(rom_1_data[15]), .addrsel(rom_1_data[17:16]), .regsrc(rom_1_data[19:18]),
    .dwrite(rom_1_data[20]), .swrite(rom_1_data[21]), .twrite(rom_1_data[22]), .instruction(register_13_q),
    .set_flags(and_20_out), .Rd(register_bank_1_dreg), .Rs(Rs), .Rt(register_bank_1_treg),
    .immed(multiplexer_87_out), .dregsel(instruction_reg_1_dregsel), .sregsel(ssel), .tregsel(tsel),
    .imload(imload), .op2sel(rom_1_data[6:5]), .Rs2(multiplexer_101_out), .Rs3(multiplexer_102_out),
    .Rs1(multiplexer_98_out), .Rt2(multiplexer_101_out), .Rt3(multiplexer_102_out), .Rt1(multiplexer_98_out),
    .aluop_out(aluop), .negOp2_out(negOp2), .rvrsOps_out(rvrsOps), .datasel_out(id_to_ex_1_datasel_out),
    .datawrite_out(id_to_ex_1_datawrite_out), .addrsel_out(id_to_ex_1_addrsel_out), .dwrite_out(prevDwrite),
    .swrite_out(id_to_ex_1_swrite_out), .twrite_out(id_to_ex_1_twrite_out),
    .imload_out(id_to_ex_1_imload_out), .flags_set(flgset), .instruction_out(id_to_ex_1_instruction_out),
    .regsrc_out(prevRegsrc), .dregselOut(id_to_ex_1_dregselout), .sregselOut(id_to_ex_1_sregselout),
    .tregselOut(id_to_ex_1_tregselout), .immedOut(id_to_ex_1_immedout), .op2sel_out(op2sel),
    .Rs_Out(id_to_ex_1_rs_out), .Rt_Out(id_to_ex_1_rt_out));  // open: Rd_Out
  Multiplexer #(.select(2), .width(32)) multiplexer_90 (
    .in0(id_to_ex_1_rt_out), .in1({{22{1'b0}}, id_to_ex_1_immedout}), .in2({32{1'b0}}), .in3(32'h1),
    .out(multiplexer_90_out), .sel(op2sel));
  // Probe on op2sel
  assign not_14_out = ~multiplexer_90_out;  // NOT_Gate not_14, 32 bits wide
  Hex_Digit_Display hex_digit_display_25 (.value(showhexa_4_out_2));  // open: dp
  Hex_Digit_Display hex_digit_display_26 (.value(showhexa_4_out_3));  // open: dp
  ShowHexa showhexa_4 (
    .Data(id_to_ex_1_instruction_out), .out_3(showhexa_4_out_3), .out_4(showhexa_4_out_4),
    .out_5(showhexa_4_out_5), .Digit(showhexa_4_digit), .out_7(showhexa_4_out_7), .out_8(showhexa_4_out_8),
    .out_9(showhexa_4_out_9), .out_2(showhexa_4_out_2));
  Multiplexer #(.width(32)) multiplexer_91 (
    .in0(multiplexer_90_out), .in1(not_14_out), .out(multiplexer_91_out), .sel(negOp2));
  Hex_Digit_Display hex_digit_display_27 (.value(showhexa_4_out_4));  // open: dp
  Hex_Digit_Display hex_digit_display_28 (.value(showhexa_4_out_5));  // open: dp
  Multiplexer #(.width(32)) multiplexer_92 (
    .in0(id_to_ex_1_rs_out), .in1(multiplexer_91_out), .out(multiplexer_92_out), .sel(rvrsOps));
  Multiplexer #(.width(32)) multiplexer_93 (
    .in0(multiplexer_91_out), .in1(id_to_ex_1_rs_out), .out(multiplexer_93_out), .sel(rvrsOps));
  Hex_Digit_Display hex_digit_display_29 (.value(showhexa_4_digit));  // open: dp
  Hex_Digit_Display hex_digit_display_30 (.value(showhexa_4_out_7));  // open: dp
  // Probe on aluop
  Hex_Digit_Display hex_digit_display_31 (.value(showhexa_4_out_8));  // open: dp
  Hex_Digit_Display hex_digit_display_32 (.value(showhexa_4_out_9));  // open: dp
  ALU alu_1 (
    .A(multiplexer_92_out), .B(multiplexer_93_out), .aluop(aluop), .Result(alu_1_result),
    .Overflow(alu_1_overflow), .Carry(alu_1_carry), .Negative(alu_1_negative), .Zero(alu_1_zero));
  Register #(.width(1)) register_15 (.D(alu_1_carry), .en(flgset), .Q(register_15_q), .clk(CLK), .clr(Reset));
  Register #(.width(1)) register_16 (.D(alu_1_zero), .en(flgset), .Q(register_16_q), .clk(CLK), .clr(Reset));
  Multiplexer multiplexer_94 (.in0(register_15_q), .in1(alu_1_carry), .out(C), .sel(flagsForwards));
  Multiplexer multiplexer_95 (.in0(register_16_q), .in1(alu_1_zero), .out(Z), .sel(flagsForwards));
  Register #(.width(1)) register_17 (.D(alu_1_negative), .en(flgset), .Q(register_17_q), .clk(CLK), .clr(Reset));
  Multiplexer multiplexer_96 (.in0(register_17_q), .in1(alu_1_negative), .out(N), .sel(flagsForwards));
  Register #(.width(1)) register_18 (.D(alu_1_overflow), .en(flgset), .Q(register_18_q), .clk(CLK), .clr(Reset));
  Multiplexer multiplexer_97 (.in0(register_18_q), .in1(alu_1_overflow), .out(V), .sel(flagsForwards));
  Multiplexer #(.select(2), .width(32)) multiplexer_98 (
    .in0(id_to_ex_1_rs_out), .in1({{22{1'b0}}, id_to_ex_1_immedout}), .in3(alu_1_result),
    .out(multiplexer_98_out), .sel(prevRegsrc));  // open: in2
  EX_to_MA ex_to_ma_1 (
    .Clk(CLK), .Reset(Reset), .datasel(id_to_ex_1_datasel_out), .datawrite(id_to_ex_1_datawrite_out),
    .addrsel(id_to_ex_1_addrsel_out), .regsrc(prevRegsrc), .dwrite(prevDwrite),
    .swrite(id_to_ex_1_swrite_out), .twrite(id_to_ex_1_twrite_out), .Rs(id_to_ex_1_rs_out),
    .Rt(id_to_ex_1_rt_out), .instruction(id_to_ex_1_instruction_out),
    .immed({{22{1'b0}}, id_to_ex_1_immedout}), .dregsel(id_to_ex_1_dregselout),
    .sregsel(id_to_ex_1_sregselout), .tregsel(id_to_ex_1_tregselout), .aluout(alu_1_result),
    .imload(id_to_ex_1_imload_out), .datasel_out(datasel), .datawrite_out(datawrite), .addrsel_out(addrsel),
    .dwrite_out(prevDwrite1), .swrite_out(ex_to_ma_1_swrite_out), .twrite_out(ex_to_ma_1_twrite_out),
    .imload_out(ex_to_ma_1_imload_out), .regsrc_out(prevRegsrc1), .Rs_Out(ex_to_ma_1_rs_out),
    .Rt_Out(ex_to_ma_1_rt_out), .instruction_out(ex_to_ma_1_instruction_out),
    .immed_Out(ex_to_ma_1_immed_out), .dregsel_Out(ex_to_ma_1_dregsel_out),
    .sregsel_Out(ex_to_ma_1_sregsel_out), .tregsel_Out(ex_to_ma_1_tregsel_out),
    .aluout_Out(ex_to_ma_1_aluout_out));
  Button Clear (.out(Clear_out));
  Multiplexer #(.select(2), .width(32)) multiplexer_99 (
    .in0(ex_to_ma_1_immed_out), .in1(ex_to_ma_1_aluout_out), .in2(ex_to_ma_1_rs_out),
    .out({multiplexer_99_out_2, multiplexer_99_out}), .sel(addrsel));  // open: in3
  // Probe on addrsel
  // Probe on datasel
  Address_Decoder ADDR_DEC (
    .Address({multiplexer_99_out_2, multiplexer_99_out}), .RAM(RAMSel), .FB_LED(FB_LED), .TTY(TTYSel),
    .output_3(ADDR_DEC_output_3));
  DotMatrix #(.inputtype("row"), .matrixcols(32), .matrixrows(16)) dotmatrix_1 (
    .row0(frame_buffer_16x32_1_out_6), .row1(frame_buffer_16x32_1_out_7), .row2(frame_buffer_16x32_1_out_8),
    .row3(frame_buffer_16x32_1_out_9), .row4(frame_buffer_16x32_1_out_10),
    .row5(frame_buffer_16x32_1_out_11), .row6(frame_buffer_16x32_1_out_12),
    .row7(frame_buffer_16x32_1_out_13), .row8(frame_buffer_16x32_1_out_14),
    .row9(frame_buffer_16x32_1_out_15), .row10(frame_buffer_16x32_1_out_16),
    .row11(frame_buffer_16x32_1_out_17), .row12(frame_buffer_16x32_1_out_18),
    .row13(frame_buffer_16x32_1_out_19), .row14(frame_buffer_16x32_1_out_20),
    .row15(frame_buffer_16x32_1_out_21));
  Frame_Buffer_16x32 frame_buffer_16x32_1 (
    .address(multiplexer_99_out), .store(FB_LED), .data(datain), .clock(CLK), .reset(Clear_out),
    .out_6(frame_buffer_16x32_1_out_6), .out_7(frame_buffer_16x32_1_out_7),
    .out_8(frame_buffer_16x32_1_out_8), .out_9(frame_buffer_16x32_1_out_9),
    .out_10(frame_buffer_16x32_1_out_10), .out_11(frame_buffer_16x32_1_out_11),
    .out_12(frame_buffer_16x32_1_out_12), .out_13(frame_buffer_16x32_1_out_13),
    .out_14(frame_buffer_16x32_1_out_14), .out_15(frame_buffer_16x32_1_out_15),
    .out_16(frame_buffer_16x32_1_out_16), .out_17(frame_buffer_16x32_1_out_17),
    .out_18(frame_buffer_16x32_1_out_18), .out_19(frame_buffer_16x32_1_out_19),
    .out_20(frame_buffer_16x32_1_out_20), .out_21(frame_buffer_16x32_1_out_21));
  Multiplexer #(.select(2), .width(32)) multiplexer_100 (
    .in0(ex_to_ma_1_rs_out), .in1(ex_to_ma_1_rt_out), .in2(ex_to_ma_1_aluout_out), .out(datain), .sel(datasel));  // open: in3
  // Probe on {multiplexer_99_out_2, multiplexer_99_out}
  // Probe on datain
  not not_15 (not_15_out, datawrite);
  and and_21 (and_21_out, RAMSel, datawrite);
  and and_22 (and_22_out, RAMSel, not_15_out);
  RAM #(.addrWidth(16), .asyncread("true"), .dataWidth(32), .databus("bidir")) ram_11 (
    .addr({multiplexer_99_out_2[15:4], multiplexer_99_out}), .we(and_21_out), .oe(and_22_out), .clk(CLK),
    .data(ram_11_data));
  Button Clear_Screen (.out(Clear_Screen_out));
  Hex_Digit_Display hex_digit_display_33 (.value(showhexa_5_out_2));  // open: dp
  Hex_Digit_Display hex_digit_display_34 (.value(showhexa_5_out_3));  // open: dp
  ShowHexa showhexa_5 (
    .Data(ex_to_ma_1_instruction_out), .out_3(showhexa_5_out_3), .out_4(showhexa_5_out_4),
    .out_5(showhexa_5_out_5), .Digit(showhexa_5_digit), .out_7(showhexa_5_out_7), .out_8(showhexa_5_out_8),
    .out_9(showhexa_5_out_9), .out_2(showhexa_5_out_2));
  // Probe on datain[6:0]
  TTY #(.cols(16), .rows(4)) tty_3 (.data(datain[6:0]), .clk(CLK), .we(TTYSel), .clr(Clear_Screen_out));
  Hex_Digit_Display hex_digit_display_35 (.value(showhexa_5_out_4));  // open: dp
  Hex_Digit_Display hex_digit_display_36 (.value(showhexa_5_out_5));  // open: dp
  Hex_Digit_Display hex_digit_display_37 (.value(showhexa_5_digit));  // open: dp
  Hex_Digit_Display hex_digit_display_38 (.value(showhexa_5_out_7));  // open: dp
  assign ram_11_data = datawrite ? datain : 32'bz;  // Controlled_Buffer controlled_buffer_1
  Hex_Digit_Display hex_digit_display_39 (.value(showhexa_5_out_8));  // open: dp
  Hex_Digit_Display hex_digit_display_40 (.value(showhexa_5_out_9));  // open: dp
  Multiplexer #(.select(2), .width(32)) multiplexer_101 (
    .in0(ex_to_ma_1_rs_out), .in1(ex_to_ma_1_immed_out), .in2(ram_11_data), .in3(ex_to_ma_1_aluout_out),
    .out(multiplexer_101_out), .sel(prevRegsrc1));
  MA_to_WB ma_to_wb_1 (
    .Clk(CLK), .Reset(Reset), .regsrc(prevRegsrc1), .dwrite(prevDwrite1), .swrite(ex_to_ma_1_swrite_out),
    .twrite(ex_to_ma_1_twrite_out), .instruction(ex_to_ma_1_instruction_out), .aluout(ex_to_ma_1_aluout_out),
    .Rs(ex_to_ma_1_rs_out), .immed(ex_to_ma_1_immed_out), .dregsel(ex_to_ma_1_dregsel_out),
    .sregsel(ex_to_ma_1_sregsel_out), .tregsel(ex_to_ma_1_tregsel_out), .operand(ram_11_data),
    .imload(ex_to_ma_1_imload_out), .dwrite_out(dwrite), .swrite_out(swrite), .twrite_out(twrite),
    .instruction_out(ma_to_wb_1_instruction_out), .aluout_Out(ma_to_wb_1_aluout_out), .regsrc_out(regsrc),
    .Rs_Out(ma_to_wb_1_rs_out), .immed_Out(ma_to_wb_1_immed_out), .dregsel_Out(ma_to_wb_1_dregsel_out),
    .sregsel_Out(ma_to_wb_1_sregsel_out), .tregsel_Out(ma_to_wb_1_tregsel_out),
    .operand_Out(ma_to_wb_1_operand_out));
  Multiplexer #(.select(2), .width(32)) multiplexer_102 (
    .in0(ma_to_wb_1_rs_out), .in1(ma_to_wb_1_immed_out), .in2(ma_to_wb_1_operand_out),
    .in3(ma_to_wb_1_aluout_out), .out(multiplexer_102_out), .sel(regsrc));
  Multiplexer #(.select(2), .width(32)) multiplexer_103 (
    .in0(ma_to_wb_1_rs_out), .in1(ma_to_wb_1_immed_out), .in2(ma_to_wb_1_operand_out),
    .in3(ma_to_wb_1_aluout_out), .out(regwrite), .sel(regsrc));
  // Probe on regsrc
  Hex_Digit_Display hex_digit_display_41 (.value(showhexa_6_out_2));  // open: dp
  ShowHexa showhexa_6 (
    .Data(ma_to_wb_1_instruction_out), .out_3(showhexa_6_out_3), .out_4(showhexa_6_out_4),
    .out_5(showhexa_6_out_5), .Digit(showhexa_6_digit), .out_7(showhexa_6_out_7), .out_8(showhexa_6_out_8),
    .out_9(showhexa_6_out_9), .out_2(showhexa_6_out_2));
  Hex_Digit_Display hex_digit_display_42 (.value(showhexa_6_out_3));  // open: dp
  Hex_Digit_Display hex_digit_display_43 (.value(showhexa_6_out_4));  // open: dp
  Hex_Digit_Display hex_digit_display_44 (.value(showhexa_6_out_5));  // open: dp
  Hex_Digit_Display hex_digit_display_45 (.value(showhexa_6_digit));  // open: dp
  Hex_Digit_Display hex_digit_display_46 (.value(showhexa_6_out_7));  // open: dp
  Hex_Digit_Display hex_digit_display_47 (.value(showhexa_6_out_8));  // open: dp
  Hex_Digit_Display hex_digit_display_48 (.value(showhexa_6_out_9));  // open: dp

  // Other names for the same wires on the sheet: MSBc = corrPred; twoBit = MSB; br_addr[15:0] = Break_Addr;
  //   dbgadr = Stop_Addr; dbgcyc = Cycle; stall = bubble

  // Notes on the sheet:
  //   Flags
  //   PC
  //   MiMo - Microprogrammed CPU Model
  //   Address
  //   Debug
  //   3bit GHR
  //   v0 Pipelined
  //   previous PC+1
  //   Instruction RAM
  //   Link Register
  //   Incorrect Predictions
  //   Jump outcome
  //   Jump prediction
  //   is unconditional?
  //   is branch?
  //   is rts?
  //   is branch / jump command?
  //   No predict
  //   (Branch not taken)
  //   Total Predictions
  //   8x2 CPT
  //   2^2 Correlating Predictor
  //   8x2 LPT
  //   8x2 GPT
  //   1-bit
  //   1 bit prediction table
  //   2 bit prediction table
  //   Correlating Predictor using LHT
  //   Tournament Predictor
  //   Predictions Methods
  //   2-bit
  //   Correlating LHT
  //   we need to flush the pipeline
  //   If we previously made a prediction and it was wrong
  //   Correlating 2 by 2
  //   Tournament
  //   opcode
  //   IF
  //   1st address is reserved
  //   cond_met
  //   contents of rom_1 (hex, n*v repeats v):
  //   0 100000 1c1500 1c0000 1c0080 1c1080 1c0100 1c0180 1c0200 1c0280 1c0300 1c0380 1c0400 1c0480 1c0a80
  //   80 0 380 280 1c0580 1c0600 1c0680 1c0780 1c0700 3 5 b 13 8000 180000 1a0000 190000
  //   Control ROM
  //   ID
  //   Not needed in this version
  //   Registers
  //   If the previous instruction is ldr, we need to stall for 1 cycle
  //   IF
  //   ctrl signals
  //   Not needed in this version
  //   Value in Rd
  //   Value in Rs
  //   Value in Rt
  //   EX
  //   ALU
  //   Address
  //   Data
  //   Frame Buffer LED 16x32
  //   Operand RAM
  //   TTY
  //   MA
  //   WB
endmodule

module IF_to_ID (
  input  Clk,
  input  Reset,
  input  [31:0] instruction,
  output [31:0] instructionOut
);


  assign instructionOut = instruction;
endmodule

module ID_to_EX (
  input  Clk,
  input  [31:0] Rs1,
  input  [31:0] Rt1,
  input  Reset,
  input  Bubble,
  input  [31:0] Rs2,
  input  [31:0] Rt2,
  input  [1:0] sselForward,
  input  [1:0] tselForward,
  input  [31:0] Rs3,
  input  [31:0] Rt3,
  input  [9:0] immed,
  input  [2:0] dregsel,
  input  [2:0] sregsel,
  input  [2:0] tregsel,
  input  [31:0] Rd,
  input  [31:0] Rs,
  input  [31:0] Rt,
  input  set_flags,
  input  [31:0] instruction,
  input  imload,
  input  [1:0] op2sel,
  input  [3:0] aluop,
  input  negOp2,
  input  rvrsOps,
  input  [1:0] datasel,
  input  datawrite,
  input  [1:0] addrsel,
  input  [1:0] regsrc,
  input  dwrite,
  input  swrite,
  input  twrite,
  output [9:0] immedOut,
  output [2:0] dregselOut,
  output [2:0] sregselOut,
  output [2:0] tregselOut,
  output [31:0] Rd_Out,
  output [31:0] Rs_Out,
  output [31:0] Rt_Out,
  output flags_set,
  output [31:0] instruction_out,
  output imload_out,
  output [1:0] op2sel_out,
  output [3:0] aluop_out,
  output negOp2_out,
  output rvrsOps_out,
  output [1:0] datasel_out,
  output datawrite_out,
  output [1:0] addrsel_out,
  output [1:0] regsrc_out,
  output dwrite_out,
  output swrite_out,
  output twrite_out
);

  wire multiplexer_1_out;
  wire [1:0] multiplexer_10_out, multiplexer_13_out;
  wire [2:0] multiplexer_4_out, multiplexer_5_out, multiplexer_6_out;
  wire [9:0] multiplexer_3_out;
  wire [31:0] multiplexer_2_out, multiplexer_7_out, multiplexer_8_out, multiplexer_9_out, multiplexer_11_out,
       multiplexer_12_out;

  Multiplexer multiplexer_1 (.in0(set_flags), .in1(1'b0), .out(multiplexer_1_out), .sel(Bubble));
  Multiplexer #(.width(32)) multiplexer_2 (.in0(instruction), .in1({32{1'b0}}), .out(multiplexer_2_out), .sel(Bubble));
  Shift_Register #(.length(1), .width(4)) shift_register_1 (
    .shift(Clk), .in(aluop), .clk(Clk), .out(aluop_out), .clr(Reset));  // open: load, d0, q0
  Shift_Register #(.length(1)) shift_register_2 (
    .shift(Clk), .in(negOp2), .clk(Clk), .out(negOp2_out), .clr(Reset));  // open: load, d0, q0
  Shift_Register #(.length(1)) shift_register_3 (
    .shift(Clk), .in(rvrsOps), .clk(Clk), .out(rvrsOps_out), .clr(Reset));  // open: load, d0, q0
  Shift_Register #(.length(1), .width(2)) shift_register_4 (
    .shift(Clk), .in(datasel), .clk(Clk), .out(datasel_out), .clr(Reset));  // open: load, d0, q0
  Shift_Register #(.length(1)) shift_register_5 (
    .shift(Clk), .in(datawrite), .clk(Clk), .out(datawrite_out), .clr(Reset));  // open: load, d0, q0
  Shift_Register #(.length(1), .width(2)) shift_register_6 (
    .shift(Clk), .in(addrsel), .clk(Clk), .out(addrsel_out), .clr(Reset));  // open: load, d0, q0
  Shift_Register #(.length(1)) shift_register_7 (
    .shift(Clk), .in(dwrite), .clk(Clk), .out(dwrite_out), .clr(Reset));  // open: load, d0, q0
  Shift_Register #(.length(1)) shift_register_8 (
    .shift(Clk), .in(swrite), .clk(Clk), .out(swrite_out), .clr(Reset));  // open: load, d0, q0
  Shift_Register #(.length(1)) shift_register_9 (
    .shift(Clk), .in(twrite), .clk(Clk), .out(twrite_out), .clr(Reset));  // open: load, d0, q0
  Multiplexer #(.width(10)) multiplexer_3 (.in0(immed), .in1({10{1'b0}}), .out(multiplexer_3_out), .sel(Bubble));
  Multiplexer #(.width(3)) multiplexer_4 (.in0(dregsel), .in1(3'b000), .out(multiplexer_4_out), .sel(Bubble));
  Multiplexer #(.width(3)) multiplexer_5 (.in0(sregsel), .in1(3'b000), .out(multiplexer_5_out), .sel(Bubble));
  Multiplexer #(.width(3)) multiplexer_6 (.in0(tregsel), .in1(3'b000), .out(multiplexer_6_out), .sel(Bubble));
  Shift_Register #(.length(1)) shift_register_10 (
    .shift(Clk), .in(imload), .clk(Clk), .out(imload_out), .clr(Reset));  // open: load, d0, q0
  Register #(.width(10)) register_1 (.D(multiplexer_3_out), .en(Clk), .Q(immedOut), .clk(Clk), .clr(Reset));
  Register #(.width(3)) register_2 (.D(multiplexer_4_out), .en(Clk), .Q(dregselOut), .clk(Clk), .clr(Reset));
  Register #(.width(3)) register_3 (.D(multiplexer_5_out), .en(Clk), .Q(sregselOut), .clk(Clk), .clr(Reset));
  Register #(.width(3)) register_4 (.D(multiplexer_6_out), .en(Clk), .Q(tregselOut), .clk(Clk), .clr(Reset));
  Multiplexer #(.width(32)) multiplexer_7 (.in0(Rd), .in1({32{1'b0}}), .out(multiplexer_7_out), .sel(Bubble));
  Multiplexer #(.width(32)) multiplexer_8 (.in0(Rs), .in1({32{1'b0}}), .out(multiplexer_8_out), .sel(Bubble));
  Multiplexer #(.width(32)) multiplexer_9 (.in0(Rt), .in1({32{1'b0}}), .out(multiplexer_9_out), .sel(Bubble));
  Register #(.width(1)) register_5 (.D(multiplexer_1_out), .en(Clk), .Q(flags_set), .clk(Clk), .clr(Reset));
  Register #(.width(32)) register_6 (.D(multiplexer_2_out), .en(Clk), .Q(instruction_out), .clk(Clk), .clr(Reset));
  Multiplexer #(.select(2), .width(2)) multiplexer_10 (
    .in0({1'b0, imload}), .in1({1'b0, imload}), .in2(regsrc), .in3(regsrc), .out(multiplexer_10_out),
    .sel(regsrc));
  Shift_Register #(.length(1), .width(2)) shift_register_11 (
    .shift(Clk), .in(multiplexer_10_out), .clk(Clk), .out(regsrc_out), .clr(Reset));  // open: load, d0, q0
  Register #(.width(32)) register_7 (.D(multiplexer_7_out), .en(Clk), .Q(Rd_Out), .clk(Clk), .clr(Reset));
  Multiplexer #(.select(2), .width(32)) multiplexer_11 (
    .in0(multiplexer_8_out), .in1(Rs1), .in2(Rs2), .in3(Rs3), .out(multiplexer_11_out), .sel(sselForward));
  Multiplexer #(.select(2), .width(32)) multiplexer_12 (
    .in0(multiplexer_9_out), .in1(Rt1), .in2(Rt2), .in3(Rt3), .out(multiplexer_12_out), .sel(tselForward));
  Multiplexer #(.select(2), .width(2)) multiplexer_13 (
    .in0({1'b0, imload}), .in1({1'b0, imload}), .in2(op2sel), .in3(op2sel), .out(multiplexer_13_out),
    .sel(op2sel));
  Shift_Register #(.length(1), .width(2)) shift_register_12 (
    .shift(Clk), .in(multiplexer_13_out), .clk(Clk), .out(op2sel_out), .clr(Reset));  // open: load, d0, q0
  Register #(.width(32)) register_8 (.D(multiplexer_11_out), .en(Clk), .Q(Rs_Out), .clk(Clk), .clr(Reset));
  Register #(.width(32)) register_9 (.D(multiplexer_12_out), .en(Clk), .Q(Rt_Out), .clk(Clk), .clr(Reset));
endmodule

module EX_to_MA (
  input  Clk,
  input  Reset,
  input  [31:0] immed,
  input  [2:0] dregsel,
  input  [2:0] sregsel,
  input  [2:0] tregsel,
  input  [31:0] Rs,
  input  [31:0] Rt,
  input  [31:0] aluout,
  input  [31:0] instruction,
  input  imload,
  input  [1:0] datasel,
  input  datawrite,
  input  [1:0] addrsel,
  input  [1:0] regsrc,
  input  dwrite,
  input  swrite,
  input  twrite,
  output [31:0] immed_Out,
  output [2:0] dregsel_Out,
  output [2:0] sregsel_Out,
  output [2:0] tregsel_Out,
  output [31:0] Rs_Out,
  output [31:0] Rt_Out,
  output [31:0] aluout_Out,
  output [31:0] instruction_out,
  output imload_out,
  output [1:0] datasel_out,
  output datawrite_out,
  output [1:0] addrsel_out,
  output [1:0] regsrc_out,
  output dwrite_out,
  output swrite_out,
  output twrite_out
);

  wire [1:0] multiplexer_1_out;

  Shift_Register #(.length(1), .width(2)) shift_register_1 (
    .shift(Clk), .in(datasel), .clk(Clk), .out(datasel_out), .clr(Reset));  // open: load, d0, q0
  Shift_Register #(.length(1)) shift_register_2 (
    .shift(Clk), .in(datawrite), .clk(Clk), .out(datawrite_out), .clr(Reset));  // open: load, d0, q0
  Shift_Register #(.length(1), .width(2)) shift_register_3 (
    .shift(Clk), .in(addrsel), .clk(Clk), .out(addrsel_out), .clr(Reset));  // open: load, d0, q0
  Shift_Register #(.length(1)) shift_register_4 (
    .shift(Clk), .in(dwrite), .clk(Clk), .out(dwrite_out), .clr(Reset));  // open: load, d0, q0
  Shift_Register #(.length(1)) shift_register_5 (
    .shift(Clk), .in(swrite), .clk(Clk), .out(swrite_out), .clr(Reset));  // open: load, d0, q0
  Shift_Register #(.length(1)) shift_register_6 (
    .shift(Clk), .in(twrite), .clk(Clk), .out(twrite_out), .clr(Reset));  // open: load, d0, q0
  Shift_Register #(.length(1)) shift_register_7 (
    .shift(Clk), .in(imload), .clk(Clk), .out(imload_out), .clr(Reset));  // open: load, d0, q0
  Register #(.width(32)) register_1 (.D(immed), .en(Clk), .Q(immed_Out), .clk(Clk), .clr(Reset));
  Register #(.width(3)) register_2 (.D(dregsel), .en(Clk), .Q(dregsel_Out), .clk(Clk), .clr(Reset));
  Register #(.width(3)) register_3 (.D(sregsel), .en(Clk), .Q(sregsel_Out), .clk(Clk), .clr(Reset));
  Register #(.width(3)) register_4 (.D(tregsel), .en(Clk), .Q(tregsel_Out), .clk(Clk), .clr(Reset));
  Register #(.width(32)) register_5 (.D(Rs), .en(Clk), .Q(Rs_Out), .clk(Clk), .clr(Reset));
  Register #(.width(32)) register_6 (.D(Rt), .en(Clk), .Q(Rt_Out), .clk(Clk), .clr(Reset));
  Register #(.width(32)) register_7 (.D(aluout), .en(Clk), .Q(aluout_Out), .clk(Clk), .clr(Reset));
  Register #(.width(32)) register_8 (.D(instruction), .en(Clk), .Q(instruction_out), .clk(Clk), .clr(Reset));
  Multiplexer #(.select(2), .width(2)) multiplexer_1 (
    .in0({1'b0, imload}), .in1({1'b0, imload}), .in2(regsrc), .in3(regsrc), .out(multiplexer_1_out),
    .sel(regsrc));
  Shift_Register #(.length(1), .width(2)) shift_register_8 (
    .shift(Clk), .in(multiplexer_1_out), .clk(Clk), .out(regsrc_out), .clr(Reset));  // open: load, d0, q0
endmodule

module MA_to_WB (
  input  Clk,
  input  Reset,
  input  [31:0] immed,
  input  [2:0] dregsel,
  input  [2:0] sregsel,
  input  [2:0] tregsel,
  input  [31:0] operand,
  input  [31:0] Rs,
  input  [31:0] aluout,
  input  [31:0] instruction,
  input  imload,
  input  [1:0] regsrc,
  input  dwrite,
  input  swrite,
  input  twrite,
  output [31:0] immed_Out,
  output [2:0] dregsel_Out,
  output [2:0] sregsel_Out,
  output [2:0] tregsel_Out,
  output [31:0] operand_Out,
  output [31:0] Rs_Out,
  output [31:0] aluout_Out,
  output [31:0] instruction_out,
  output [1:0] regsrc_out,
  output dwrite_out,
  output swrite_out,
  output twrite_out
);

  wire [1:0] multiplexer_1_out;

  Shift_Register #(.length(1)) shift_register_1 (
    .shift(Clk), .in(dwrite), .clk(Clk), .out(dwrite_out), .clr(Reset));  // open: load, d0, q0
  Shift_Register #(.length(1)) shift_register_2 (
    .shift(Clk), .in(swrite), .clk(Clk), .out(swrite_out), .clr(Reset));  // open: load, d0, q0
  Shift_Register #(.length(1)) shift_register_3 (
    .shift(Clk), .in(twrite), .clk(Clk), .out(twrite_out), .clr(Reset));  // open: load, d0, q0
  Register #(.width(32)) register_1 (.D(aluout), .en(Clk), .Q(aluout_Out), .clk(Clk), .clr(Reset));
  Register #(.width(32)) register_2 (.D(instruction), .en(Clk), .Q(instruction_out), .clk(Clk), .clr(Reset));
  Register #(.width(32)) register_3 (.D(immed), .en(Clk), .Q(immed_Out), .clk(Clk), .clr(Reset));
  Register #(.width(3)) register_4 (.D(dregsel), .en(Clk), .Q(dregsel_Out), .clk(Clk), .clr(Reset));
  Register #(.width(3)) register_5 (.D(sregsel), .en(Clk), .Q(sregsel_Out), .clk(Clk), .clr(Reset));
  Register #(.width(3)) register_6 (.D(tregsel), .en(Clk), .Q(tregsel_Out), .clk(Clk), .clr(Reset));
  Register #(.width(32)) register_7 (.D(operand), .en(Clk), .Q(operand_Out), .clk(Clk), .clr(Reset));
  Register #(.width(32)) register_8 (.D(Rs), .en(Clk), .Q(Rs_Out), .clk(Clk), .clr(Reset));
  Multiplexer #(.select(2), .width(2)) multiplexer_1 (
    .in0({1'b0, imload}), .in1({1'b0, imload}), .in2(regsrc), .in3(regsrc), .out(multiplexer_1_out),
    .sel(regsrc));
  Shift_Register #(.length(1), .width(2)) shift_register_4 (
    .shift(Clk), .in(multiplexer_1_out), .clk(Clk), .out(regsrc_out), .clr(Reset));  // open: load, d0, q0
endmodule

module Branch_Predictor (
  input  in_1,
  output should_jump
);


  assign should_jump = in_1;
endmodule

module Instruction_Reg (
  input  [31:0] instruction,
  input  reset,
  input  clock,
  input  irload,
  output [9:0] immed,
  output [2:0] dregsel,
  output [2:0] sregsel,
  output [2:0] tregsel,
  output [3:0] condition,
  output set_flags,
  output imload,
  output [6:0] opcode
);

  Register #(.width(32)) register_1 (
    .D(instruction), .en(irload),
    .Q({opcode, imload, set_flags, condition, tregsel, sregsel, dregsel, immed}), .clk(clock), .clr(reset));

  // Notes on the sheet:
  //   IR Logic
endmodule

module check_condition (
  input  C,
  input  Z,
  input  V,
  input  N,
  input  [3:0] condition,
  output cond_met
);

  wire and_1_out, and_2_out, and_3_out, and_4_out, and_5_out, and_6_out, and_7_out, and_8_out, and_9_out,
       and_10_out, and_11_out, and_12_out, and_13_out, and_14_out, and_15_out, and_16_out, and_17_out,
       and_18_out, decoder_1_out1, decoder_1_out2, decoder_1_out3, decoder_1_out4, decoder_1_out5,
       decoder_1_out6, decoder_1_out7, decoder_1_out8, decoder_1_out9, decoder_1_out10, decoder_1_out11,
       decoder_1_out12, decoder_1_out13, decoder_1_out14, decoder_1_out15, not_1_out, not_2_out, not_3_out,
       not_4_out, not_5_out, not_6_out, not_7_out, xnor_1_out, xnor_2_out, xor_1_out, xor_2_out;

  Decoder #(.enable("false"), .select(4)) decoder_1 (
    .out1(decoder_1_out1), .out2(decoder_1_out2), .out3(decoder_1_out3), .out4(decoder_1_out4),
    .out5(decoder_1_out5), .out6(decoder_1_out6), .out7(decoder_1_out7), .out8(decoder_1_out8),
    .out9(decoder_1_out9), .out10(decoder_1_out10), .out11(decoder_1_out11), .out12(decoder_1_out12),
    .out13(decoder_1_out13), .out14(decoder_1_out14), .out15(decoder_1_out15), .sel(condition));  // open: out0
  and and_1 (and_1_out, decoder_1_out10, not_1_out);
  not not_1 (not_1_out, Z);
  and and_2 (and_2_out, decoder_1_out10, C);
  and and_3 (and_3_out, decoder_1_out11, not_2_out);
  not not_2 (not_2_out, C);
  and and_4 (and_4_out, decoder_1_out11, Z);
  xnor xnor_1 (xnor_1_out, N, V);
  xor xor_1 (xor_1_out, N, V);
  not not_3 (not_3_out, Z);
  xnor xnor_2 (xnor_2_out, N, V);
  xor xor_2 (xor_2_out, N, V);
  and and_5 (and_5_out, decoder_1_out2, Z);
  and and_6 (and_6_out, decoder_1_out3, not_4_out);
  not not_4 (not_4_out, Z);
  and and_7 (and_7_out, decoder_1_out4, C);
  and and_8 (and_8_out, decoder_1_out5, not_5_out);
  not not_5 (not_5_out, C);
  and and_9 (and_9_out, decoder_1_out6, N);
  and and_10 (and_10_out, decoder_1_out7, not_6_out);
  not not_6 (not_6_out, N);
  and and_11 (and_11_out, decoder_1_out8, V);
  and and_12 (and_12_out, decoder_1_out9, not_7_out);
  not not_7 (not_7_out, V);
  and and_13 (and_13_out, and_1_out, and_2_out);
  and and_14 (and_14_out, and_3_out, and_4_out);
  and and_15 (and_15_out, decoder_1_out12, xnor_1_out);
  and and_16 (and_16_out, decoder_1_out13, xor_1_out);
  and and_17 (and_17_out, decoder_1_out14, not_3_out, xnor_2_out);
  and and_18 (and_18_out, decoder_1_out15, Z, xor_2_out);
  or or_1 (cond_met, decoder_1_out1, and_5_out, and_6_out, and_7_out, and_8_out, and_9_out, and_10_out, and_11_out, and_12_out, and_13_out, and_14_out, and_15_out, and_16_out, and_17_out, and_18_out);

  // Notes on the sheet:
  //   Flags
  //   HI
  //   LS
  //   GE
  //   LT
  //   GT
  //   AL (Always)
  //   EQ
  //   NE
  //   CS
  //   CC
  //   MI
  //   PL
  //   VS
  //   VC
  //   LE
endmodule

module RAW_Check_prev (
  input  [2:0] ssel,
  input  [2:0] tsel,
  input  imload,
  input  [2:0] prevRd,
  input  prevDatawrite,
  input  prevCond,
  input  [2:0] prevRd1,
  input  prevCond1,
  input  prevDatawrite1,
  input  [2:0] prevRd2,
  input  prevCond2,
  input  prevDatawrite2,
  input  flgset,
  output RAW,
  output RAW1,
  output RAW2,
  output stall
);

  wire and_1_out, and_2_out, and_3_out, comparator_1_eq, comparator_2_eq, comparator_3_eq, comparator_4_eq,
       comparator_5_eq, comparator_6_eq, not_1_out, not_2_out, not_3_out, or_1_out, or_2_out, or_3_out;

  Comparator #(.mode("unsigned"), .width(3)) comparator_1 (.a(prevRd), .b(ssel), .eq(comparator_1_eq));  // open: gt, lt
  Comparator #(.mode("unsigned"), .width(3)) comparator_2 (.a(prevRd), .b(tsel), .eq(comparator_2_eq));  // open: gt, lt
  Comparator #(.mode("unsigned"), .width(3)) comparator_3 (
    .a(prevRd1), .b(ssel), .eq(comparator_3_eq));  // open: gt, lt
  Comparator #(.mode("unsigned"), .width(3)) comparator_4 (
    .a(prevRd1), .b(tsel), .eq(comparator_4_eq));  // open: gt, lt
  not not_1 (not_1_out, imload);
  Comparator #(.mode("unsigned"), .width(3)) comparator_5 (
    .a(prevRd2), .b(ssel), .eq(comparator_5_eq));  // open: gt, lt
  Comparator #(.mode("unsigned"), .width(3)) comparator_6 (
    .a(prevRd2), .b(tsel), .eq(comparator_6_eq));  // open: gt, lt
  not not_2 (not_2_out, imload);
  and and_1 (and_1_out, comparator_2_eq, not_3_out);
  not not_3 (not_3_out, imload);
  and and_2 (and_2_out, comparator_4_eq, not_1_out);
  and and_3 (and_3_out, comparator_6_eq, not_2_out);
  or or_1 (or_1_out, comparator_1_eq, and_1_out);
  or or_2 (or_2_out, comparator_3_eq, and_2_out);
  or or_3 (or_3_out, comparator_5_eq, and_3_out);
  and and_4 (RAW, or_1_out, prevDatawrite, prevCond);
  and and_5 (RAW1, or_2_out, prevCond1, prevDatawrite1);
  and and_6 (RAW2, or_3_out, prevCond2, prevDatawrite2);

  assign stall = flgset;

  // Other names for the same wires on the sheet: Rs[2:0] = ssel; Rt[2:0] = tsel

  // Notes on the sheet:
  //   2. The flags were previously set (flgset=1)
  //   Read After Write (RAW) occurs under multiple conditions:
  //   while the previous instruction's dwrite signal is equal to 1
  //   ( the instruction is supposed to write to the register bank )
  //   and the condition was met for the instruction
  //   1. Any of the 3 previous Rd values are equal to the current Rs value
  //   or the current Rt value while imload=0
endmodule

module RAW_Check (
  input  [2:0] ssel,
  input  [2:0] tsel,
  input  imload,
  input  [2:0] prevRd,
  input  [2:0] prevRd1,
  input  [2:0] prevRd2,
  input  prevDatawrite,
  input  prevCond,
  input  prevCond1,
  input  prevDatawrite1,
  input  flgset,
  input  prevCond2,
  input  prevDatawrite2,
  output [1:0] sregsel,
  output frwrdFlags,
  output [1:0] tregsel
);

  wire and_1_out, and_2_out, and_3_out, and_5_out, and_6_out, and_8_out, and_9_out, comparator_1_eq,
       comparator_2_eq, comparator_3_eq, comparator_4_eq, comparator_5_eq, comparator_6_eq, not_1_out,
       not_2_out, not_3_out, not_4_out, not_5_out, not_6_out, not_7_out, not_8_out, not_9_out;
  wire [2:0] and_4_out, and_7_out;

  Comparator #(.mode("unsigned"), .width(3)) comparator_1 (.a(prevRd), .b(tsel), .eq(comparator_1_eq));  // open: gt, lt
  Comparator #(.mode("unsigned"), .width(3)) comparator_2 (
    .a(prevRd1), .b(tsel), .eq(comparator_2_eq));  // open: gt, lt
  Comparator #(.mode("unsigned"), .width(3)) comparator_3 (
    .a(prevRd2), .b(tsel), .eq(comparator_3_eq));  // open: gt, lt
  Comparator #(.mode("unsigned"), .width(3)) comparator_4 (.a(prevRd), .b(ssel), .eq(comparator_4_eq));  // open: gt, lt
  Comparator #(.mode("unsigned"), .width(3)) comparator_5 (
    .a(prevRd1), .b(ssel), .eq(comparator_5_eq));  // open: gt, lt
  Comparator #(.mode("unsigned"), .width(3)) comparator_6 (
    .a(prevRd2), .b(ssel), .eq(comparator_6_eq));  // open: gt, lt
  and and_1 (and_1_out, comparator_1_eq, not_1_out);
  not not_1 (not_1_out, imload);
  and and_2 (and_2_out, comparator_2_eq, not_2_out);
  not not_2 (not_2_out, imload);
  and and_3 (and_3_out, comparator_3_eq, not_3_out);
  not not_3 (not_3_out, imload);
  and and_4 (and_4_out[0], comparator_4_eq, prevDatawrite, prevCond);
  and and_5 (and_5_out, comparator_5_eq, prevCond1, prevDatawrite1);
  and and_6 (and_6_out, comparator_6_eq, prevCond2, prevDatawrite2);
  and and_7 (and_7_out[0], and_1_out, prevDatawrite, prevCond);
  and and_8 (and_8_out, and_2_out, prevCond1, prevDatawrite1);
  and and_9 (and_9_out, and_3_out, prevCond2, prevDatawrite2);
  not not_4 (not_4_out, and_4_out[0]);
  and and_10 (and_4_out[1], not_4_out, and_5_out);
  not not_5 (not_5_out, and_4_out[0]);
  not not_6 (not_6_out, and_7_out[0]);
  not not_7 (not_7_out, and_7_out[0]);
  not not_8 (not_8_out, and_4_out[1]);
  and and_11 (and_7_out[1], not_6_out, and_8_out);
  and and_12 (and_4_out[2], not_8_out, not_5_out, and_6_out);
  not not_9 (not_9_out, and_7_out[1]);
  and and_13 (and_7_out[2], not_9_out, not_7_out, and_9_out);
  Multiplexer #(.select(3), .width(2)) multiplexer_1 (
    .in0(2'b00), .in1(2'b01), .in2(2'b10), .in4(2'b11), .out(sregsel), .sel(and_4_out));  // open: in3, in5, in6, in7
  Multiplexer #(.select(3), .width(2)) multiplexer_2 (
    .in0(2'b00), .in1(2'b01), .in2(2'b10), .in4(2'b11), .out(tregsel), .sel(and_7_out));  // open: in3, in5, in6, in7

  assign frwrdFlags = flgset;

  // Other names for the same wires on the sheet: Rs[2:0] = ssel; Rt[2:0] = tsel

  // Notes on the sheet:
  //   2. The flags were previously set (flgset=1)
  //   Read After Write (RAW) occurs under multiple conditions:
  //   while the previous instruction's dwrite signal is equal to 1
  //   ( the instruction is supposed to write to the register bank )
  //   and the condition was met for the instruction
  //   1. Any of the 3 previous Rd values are equal to the current Rs value
  //   or the current Rt value while imload=0
endmodule

module Register_Bank (
  input  [31:0] regval,
  input  Reset,
  input  clock,
  input  [2:0] dselout,
  input  [2:0] sselout,
  input  [2:0] tselout,
  input  dwrite,
  input  swrite,
  input  twrite,
  input  [2:0] dselin,
  input  [2:0] sselin,
  input  [2:0] tselin,
  output [31:0] r0,
  output [31:0] r1,
  output [31:0] r2,
  output [31:0] r3,
  output [31:0] r4,
  output [31:0] r5,
  output [31:0] r6,
  output [31:0] r7,
  output [31:0] dreg,
  output [31:0] sreg,
  output [31:0] treg
);

  wire demultiplexer_1_out0, demultiplexer_1_out1, demultiplexer_1_out2, demultiplexer_1_out3,
       demultiplexer_1_out4, demultiplexer_1_out5, demultiplexer_1_out6, demultiplexer_1_out7;

  Demultiplexer #(.select(3)) demultiplexer_1 (
    .out0(demultiplexer_1_out0), .out1(demultiplexer_1_out1), .out2(demultiplexer_1_out2),
    .out3(demultiplexer_1_out3), .out4(demultiplexer_1_out4), .out5(demultiplexer_1_out5),
    .out6(demultiplexer_1_out6), .out7(demultiplexer_1_out7), .in(dwrite), .sel(dselin));
  Demultiplexer #(.select(3)) demultiplexer_2 (
    .out0(demultiplexer_1_out0), .out1(demultiplexer_1_out1), .out2(demultiplexer_1_out2),
    .out3(demultiplexer_1_out3), .out4(demultiplexer_1_out4), .out5(demultiplexer_1_out5),
    .out6(demultiplexer_1_out6), .out7(demultiplexer_1_out7), .in(swrite), .sel(sselin));
  Demultiplexer #(.select(3)) demultiplexer_3 (
    .out0(demultiplexer_1_out0), .out1(demultiplexer_1_out1), .out2(demultiplexer_1_out2),
    .out3(demultiplexer_1_out3), .out4(demultiplexer_1_out4), .out5(demultiplexer_1_out5),
    .out6(demultiplexer_1_out6), .out7(demultiplexer_1_out7), .in(twrite), .sel(tselin));
  Register #(.width(32)) register_1 (.D(regval), .en(demultiplexer_1_out0), .Q(r0), .clk(clock), .clr(Reset));
  Register #(.width(32)) register_2 (.D(regval), .en(demultiplexer_1_out1), .Q(r1), .clk(clock), .clr(Reset));
  Register #(.width(32)) register_3 (.D(regval), .en(demultiplexer_1_out2), .Q(r2), .clk(clock), .clr(Reset));
  Register #(.width(32)) register_4 (.D(regval), .en(demultiplexer_1_out3), .Q(r3), .clk(clock), .clr(Reset));
  Register #(.width(32)) register_5 (.D(regval), .en(demultiplexer_1_out4), .Q(r4), .clk(clock), .clr(Reset));
  Register #(.width(32)) register_6 (.D(regval), .en(demultiplexer_1_out5), .Q(r5), .clk(clock), .clr(Reset));
  Register #(.width(32)) register_7 (.D(regval), .en(demultiplexer_1_out6), .Q(r6), .clk(clock), .clr(Reset));
  Register #(.width(32)) register_8 (.D(regval), .en(demultiplexer_1_out7), .Q(r7), .clk(clock), .clr(Reset));
  Multiplexer #(.select(3), .width(32)) multiplexer_1 (
    .in0(r0), .in1(r1), .in2(r2), .in3(r3), .in4(r4), .in5(r5), .in6(r6), .in7(r7), .out(dreg), .sel(dselout));
  Multiplexer #(.select(3), .width(32)) multiplexer_2 (
    .in0(r0), .in1(r1), .in2(r2), .in3(r3), .in4(r4), .in5(r5), .in6(r6), .in7(r7), .out(sreg), .sel(sselout));
  Multiplexer #(.select(3), .width(32)) multiplexer_3 (
    .in0(r0), .in1(r1), .in2(r2), .in3(r3), .in4(r4), .in5(r5), .in6(r6), .in7(r7), .out(treg), .sel(tselout));

  // Notes on the sheet:
  //   Register File
endmodule

module ALU (
  input  [31:0] A,
  input  [31:0] B,
  input  [3:0] aluop,
  output Overflow,
  output Carry,
  output Zero,
  output Negative,
  output [31:0] Result
);

  wire adder_1_cout, and_2_out, and_3_out, or_3_out, subtractor_1_bout, xnor_1_out, xnor_2_out, xor_2_out,
       xor_3_out;
  wire [31:0] adder_1_out, and_1_out, divider_1_out, divider_1_rem, multiplier_1_out, nand_1_out, nor_1_out,
       not_1_out, or_1_out, shifter_1_out, shifter_2_out, shifter_3_out, shifter_4_out, shifter_5_out,
       subtractor_1_out, xor_1_out;

  Adder #(.width(32)) adder_1 (.a(A), .b(B), .out(adder_1_out), .cin(1'b0), .cout(adder_1_cout));
  Subtractor #(.width(32)) subtractor_1 (.a(A), .b(B), .out(subtractor_1_out), .bin(1'b0), .bout(subtractor_1_bout));
  Multiplier #(.width(32)) multiplier_1 (.a(A), .b(B), .out(multiplier_1_out), .cin({32{1'b0}}));  // open: cout
  Divider #(.width(32)) divider_1 (.a(A), .b(B), .out(divider_1_out), .upper({32{1'b0}}), .rem(divider_1_rem));
  assign and_1_out = A & B;  // AND_Gate and_1, 32 bits wide
  assign or_1_out = A | B;  // OR_Gate or_1, 32 bits wide
  assign xor_1_out = A ^ B;  // XOR_Gate xor_1, 32 bits wide
  assign nand_1_out = ~(A & B);  // NAND_Gate nand_1, 32 bits wide
  assign nor_1_out = ~(A | B);  // NOR_Gate nor_1, 32 bits wide
  assign not_1_out = ~A;  // NOT_Gate not_1, 32 bits wide
  Shifter #(.width(32)) shifter_1 (.in(A), .\dist (B[4:0]), .out(shifter_1_out));
  Shifter #(.shift("lr"), .width(32)) shifter_2 (.in(A), .\dist (B[4:0]), .out(shifter_2_out));
  Shifter #(.shift("ar"), .width(32)) shifter_3 (.in(A), .\dist (B[4:0]), .out(shifter_3_out));
  Shifter #(.shift("rl"), .width(32)) shifter_4 (.in(A), .\dist (B[4:0]), .out(shifter_4_out));
  Shifter #(.shift("rr"), .width(32)) shifter_5 (.in(A), .\dist (B[4:0]), .out(shifter_5_out));
  xor xor_2 (xor_2_out, B[31], A[31]);
  and and_2 (and_2_out, xor_2_out, xnor_1_out);
  xnor xnor_1 (xnor_1_out, B[31], subtractor_1_out[31]);
  xnor xnor_2 (xnor_2_out, B[31], A[31]);
  xor xor_3 (xor_3_out, A[31], adder_1_out[31]);
  Multiplexer #(.select(4), .width(32)) multiplexer_1 (
    .in0(adder_1_out), .in1(subtractor_1_out), .in2(multiplier_1_out), .in3(divider_1_out),
    .in4(divider_1_rem), .in5(and_1_out), .in6(or_1_out), .in7(xor_1_out), .in8(nand_1_out), .in9(nor_1_out),
    .in10(not_1_out), .in11(shifter_1_out), .in12(shifter_2_out), .in13(shifter_3_out), .in14(shifter_4_out),
    .in15(shifter_5_out), .out({Negative, Result[30:0]}), .sel(aluop));
  and and_3 (and_3_out, xnor_2_out, xor_3_out);
  or or_2 (Overflow, and_2_out, and_3_out);
  Multiplexer #(.select(4)) multiplexer_2 (
    .in0(adder_1_cout), .in1(subtractor_1_bout), .in2(1'b0), .in3(1'b0), .in4(1'b0), .in5(1'b0), .in6(1'b0),
    .in7(1'b0), .in8(1'b0), .in9(1'b0), .in10(1'b0), .in11(1'b0), .in12(1'b0), .in13(1'b0), .in14(1'b0),
    .in15(1'b0), .out(Carry), .sel(aluop));
  or or_3 (or_3_out, Result[0], Result[1], Result[2], Result[3], Result[4], Result[5], Result[6], Result[7], Result[8], Result[9], Result[10], Result[11], Result[12], Result[13], Result[14], Result[15], Result[16], Result[17], Result[18], Result[19], Result[20], Result[21], Result[22], Result[23], Result[24], Result[25], Result[26], Result[27], Result[28], Result[29], Result[30], Negative);
  not not_2 (Zero, or_3_out);

  assign Result[31] = Negative;

  // Notes on the sheet:
  //   32-bit ALU
  //   B MSB
  //   A MSB
  //   B MSB
  //   A MSB
  //   A MSB != B MSB?
  //   A MSB = B MSB?
  //   B MSB = output MSB
  //   A/B MSB != output MSB
endmodule

module PC (
  input  flush,
  input  should_predict,
  input  [31:0] imreg,
  input  pcload,
  input  clock,
  input  reset,
  input  [1:0] pcsel,
  output [31:0] prev_pc,
  output [31:0] pcout
);

  wire [31:0] adder_1_out, adder_2_out, multiplexer_1_out, multiplexer_2_out, subtractor_1_out;

  Adder #(.width(32)) adder_1 (.a(multiplexer_2_out), .b(32'h1), .out(adder_1_out));  // open: cin, cout
  Subtractor #(.width(32)) subtractor_1 (.a(imreg), .b(multiplexer_2_out), .out(subtractor_1_out));  // open: bin, bout
  Adder #(.width(32)) adder_2 (.a(multiplexer_2_out), .b(subtractor_1_out), .out(adder_2_out));  // open: cin, cout
  Multiplexer #(.select(2), .width(32)) multiplexer_1 (
    .in0(adder_1_out), .in1(imreg), .in2(adder_2_out), .out(multiplexer_1_out), .sel(pcsel));  // open: in3
  Multiplexer #(.width(32)) multiplexer_2 (.in0(pcout), .in1(prev_pc), .out(multiplexer_2_out), .sel(flush));
  Register #(.width(32)) register_1 (.D(multiplexer_1_out), .en(pcload), .Q(pcout), .clk(clock), .clr(reset));
  Register #(.width(32)) register_2 (.D(pcout), .en(should_predict), .Q(prev_pc), .clk(clock), .clr(reset));

  // Notes on the sheet:
  //   PC Logic
endmodule

module ShowHexa (
  input  [31:0] Data,
  output [3:0] out_2,
  output [3:0] out_3,
  output [3:0] out_4,
  output [3:0] out_5,
  output [3:0] Digit,
  output [3:0] out_7,
  output [3:0] out_8,
  output [3:0] out_9
);


  assign Digit = Data[15:12];
  assign out_2 = Data[31:28];
  assign out_3 = Data[27:24];
  assign out_4 = Data[23:20];
  assign out_5 = Data[19:16];
  assign out_7 = Data[11:8];
  assign out_8 = Data[7:4];
  assign out_9 = Data[3:0];
endmodule

module Frame_Buffer_16x32 (
  input  [3:0] address,
  input  store,
  input  [31:0] data,
  input  clock,
  input  reset,
  output [31:0] out_6,
  output [31:0] out_7,
  output [31:0] out_8,
  output [31:0] out_9,
  output [31:0] out_10,
  output [31:0] out_11,
  output [31:0] out_12,
  output [31:0] out_13,
  output [31:0] out_14,
  output [31:0] out_15,
  output [31:0] out_16,
  output [31:0] out_17,
  output [31:0] out_18,
  output [31:0] out_19,
  output [31:0] out_20,
  output [31:0] out_21
);

  wire demultiplexer_1_out0, demultiplexer_1_out1, demultiplexer_1_out2, demultiplexer_1_out3,
       demultiplexer_1_out4, demultiplexer_1_out5, demultiplexer_1_out6, demultiplexer_1_out7,
       demultiplexer_1_out8, demultiplexer_1_out9, demultiplexer_1_out10, demultiplexer_1_out11,
       demultiplexer_1_out12, demultiplexer_1_out13, demultiplexer_1_out14, demultiplexer_1_out15;

  Demultiplexer #(.select(4)) demultiplexer_1 (
    .out0(demultiplexer_1_out0), .out1(demultiplexer_1_out1), .out2(demultiplexer_1_out2),
    .out3(demultiplexer_1_out3), .out4(demultiplexer_1_out4), .out5(demultiplexer_1_out5),
    .out6(demultiplexer_1_out6), .out7(demultiplexer_1_out7), .out8(demultiplexer_1_out8),
    .out9(demultiplexer_1_out9), .out10(demultiplexer_1_out10), .out11(demultiplexer_1_out11),
    .out12(demultiplexer_1_out12), .out13(demultiplexer_1_out13), .out14(demultiplexer_1_out14),
    .out15(demultiplexer_1_out15), .in(store), .sel(address));
  Register #(.width(32)) register_1 (.D(data), .en(demultiplexer_1_out0), .Q(out_6), .clk(clock), .clr(reset));
  Register #(.width(32)) register_2 (.D(data), .en(demultiplexer_1_out1), .Q(out_7), .clk(clock), .clr(reset));
  Register #(.width(32)) register_3 (.D(data), .en(demultiplexer_1_out2), .Q(out_8), .clk(clock), .clr(reset));
  Register #(.width(32)) register_4 (.D(data), .en(demultiplexer_1_out3), .Q(out_9), .clk(clock), .clr(reset));
  Register #(.width(32)) register_5 (.D(data), .en(demultiplexer_1_out4), .Q(out_10), .clk(clock), .clr(reset));
  Register #(.width(32)) register_6 (.D(data), .en(demultiplexer_1_out5), .Q(out_11), .clk(clock), .clr(reset));
  Register #(.width(32)) register_7 (.D(data), .en(demultiplexer_1_out6), .Q(out_12), .clk(clock), .clr(reset));
  Register #(.width(32)) register_8 (.D(data), .en(demultiplexer_1_out7), .Q(out_13), .clk(clock), .clr(reset));
  Register #(.width(32)) register_9 (.D(data), .en(demultiplexer_1_out8), .Q(out_14), .clk(clock), .clr(reset));
  Register #(.width(32)) register_10 (.D(data), .en(demultiplexer_1_out9), .Q(out_15), .clk(clock), .clr(reset));
  Register #(.width(32)) register_11 (.D(data), .en(demultiplexer_1_out10), .Q(out_16), .clk(clock), .clr(reset));
  Register #(.width(32)) register_12 (.D(data), .en(demultiplexer_1_out11), .Q(out_17), .clk(clock), .clr(reset));
  Register #(.width(32)) register_13 (.D(data), .en(demultiplexer_1_out12), .Q(out_18), .clk(clock), .clr(reset));
  Register #(.width(32)) register_14 (.D(data), .en(demultiplexer_1_out13), .Q(out_19), .clk(clock), .clr(reset));
  Register #(.width(32)) register_15 (.D(data), .en(demultiplexer_1_out14), .Q(out_20), .clk(clock), .clr(reset));
  Register #(.width(32)) register_16 (.D(data), .en(demultiplexer_1_out15), .Q(out_21), .clk(clock), .clr(reset));
endmodule

module Address_Decoder (
  input  [31:0] Address,
  output RAM,
  output FB_LED,
  output TTY,
  output output_3
);

  Decoder #(.enable("false"), .select(2)) decoder_1 (
    .out0(RAM), .out1(FB_LED), .out2(TTY), .out3(output_3), .sel(Address[31:30]));
endmodule

module DebugUnit (
  input  reset,
  input  \continue ,
  input  clock,
  input  [15:0] IFaddr,
  input  [15:0] break_addr,
  input  break_on_addr,
  input  break_on_cycle,
  output clock_out
);

  wire and_1_out, and_2_out, nor_1_out, nor_2_out, or_1_out, shift_register_1_out, shift_register_1_q0;
  wire [15:0] xor_1_out;

  Shift_Register #(.length(2), .trigger("falling")) shift_register_1 (
    .in(\continue ), .clk(clock), .out(shift_register_1_out), .clr(reset), .q0(shift_register_1_q0));  // open: shift, load, d0, d1, q1
  assign xor_1_out = IFaddr ^ break_addr;  // XOR_Gate xor_1, 16 bits wide
  LED Addr (.in(break_on_addr));
  and and_1 (and_1_out, ~shift_register_1_out, shift_register_1_q0);  // AND_Gate
  nor nor_1 (nor_1_out, xor_1_out[15], xor_1_out[14], xor_1_out[13], xor_1_out[12], xor_1_out[11], xor_1_out[10], xor_1_out[9], xor_1_out[8], xor_1_out[6], xor_1_out[5], xor_1_out[4], xor_1_out[3], xor_1_out[2], xor_1_out[1], xor_1_out[0], xor_1_out[7]);
  and and_2 (and_2_out, nor_1_out, break_on_addr);
  LED Cycle (.in(break_on_cycle));
  nor nor_2 (nor_2_out, and_2_out, break_on_cycle);
  or or_1 (or_1_out, and_1_out, nor_2_out);
  LED Pass (.in(or_1_out));
  and and_3 (clock_out, clock, or_1_out);

  // Notes on the sheet:
  //   Breaks on PC = break_addr
  //   Breaks on each clock pulse
  //   Makes sure the 'continue' button only
  //   lets through 1 clock pulse, until you let go
  //   and press it again.
  //   Outputs 1 only on first cycle (shift bits are unequal).
  //   Debug Unit
  //   IF address = break_addr?
endmodule

module Bit_Extendor (
  input  [9:0] datain,
  output [31:0] dataout
);

  Multiplexer #(.width(22)) multiplexer_1 (.in0({22{1'b0}}), .in1({22{1'b1}}), .out(dataout[31:10]), .sel(datain[9]));

  assign dataout[9:0] = datain;
endmodule

module LHT (
  input  clk,
  input  reset,
  input  store,
  input  data_in,
  input  [2:0] address,
  output [2:0] r0,
  output [2:0] r1,
  output [2:0] r2,
  output [2:0] r3,
  output [2:0] lpt_addr,
  output [2:0] r4,
  output [2:0] r5,
  output [2:0] r6,
  output [2:0] r7
);

  wire and_1_out, and_2_out, and_3_out, and_4_out, and_5_out, and_6_out, and_7_out, and_8_out,
       decoder_1_out0, decoder_1_out1, decoder_1_out2, decoder_1_out3, decoder_1_out4, decoder_1_out5,
       decoder_1_out6, decoder_1_out7;

  Decoder #(.enable("false"), .select(3)) decoder_1 (
    .out0(decoder_1_out0), .out1(decoder_1_out1), .out2(decoder_1_out2), .out3(decoder_1_out3),
    .out4(decoder_1_out4), .out5(decoder_1_out5), .out6(decoder_1_out6), .out7(decoder_1_out7), .sel(address));
  and and_1 (and_1_out, store, decoder_1_out0);
  and and_2 (and_2_out, store, decoder_1_out1);
  and and_3 (and_3_out, store, decoder_1_out2);
  and and_4 (and_4_out, store, decoder_1_out3);
  and and_5 (and_5_out, store, decoder_1_out4);
  and and_6 (and_6_out, store, decoder_1_out5);
  and and_7 (and_7_out, store, decoder_1_out6);
  and and_8 (and_8_out, store, decoder_1_out7);
  Shift_Register #(.length(3)) shift_register_1 (
    .shift(and_1_out), .in(data_in), .clk(clk), .out(r0[0]), .clr(reset), .q0(r0[2]), .q1(r0[1]));  // open: load, d0, d1, d2, q2
  Shift_Register #(.length(3)) shift_register_2 (
    .shift(and_2_out), .in(data_in), .clk(clk), .out(r1[0]), .clr(reset), .q0(r1[2]), .q1(r1[1]));  // open: load, d0, d1, d2, q2
  Shift_Register #(.length(3)) shift_register_3 (
    .shift(and_3_out), .in(data_in), .clk(clk), .out(r2[0]), .clr(reset), .q0(r2[2]), .q1(r2[1]));  // open: load, d0, d1, d2, q2
  Shift_Register #(.length(3)) shift_register_4 (
    .shift(and_4_out), .in(data_in), .clk(clk), .out(r3[0]), .clr(reset), .q0(r3[2]), .q1(r3[1]));  // open: load, d0, d1, d2, q2
  Shift_Register #(.length(3)) shift_register_5 (
    .shift(and_5_out), .in(data_in), .clk(clk), .out(r4[0]), .clr(reset), .q0(r4[2]), .q1(r4[1]));  // open: load, d0, d1, d2, q2
  Shift_Register #(.length(3)) shift_register_6 (
    .shift(and_6_out), .in(data_in), .clk(clk), .out(r5[0]), .clr(reset), .q0(r5[2]), .q1(r5[1]));  // open: load, d0, d1, d2, q2
  Shift_Register #(.length(3)) shift_register_7 (
    .shift(and_7_out), .in(data_in), .clk(clk), .out(r6[0]), .clr(reset), .q0(r6[2]), .q1(r6[1]));  // open: load, d0, d1, d2, q2
  Shift_Register #(.length(3)) shift_register_8 (
    .shift(and_8_out), .in(data_in), .clk(clk), .out(r7[0]), .clr(reset), .q0(r7[2]), .q1(r7[1]));  // open: load, d0, d1, d2, q2
  Multiplexer #(.select(3), .width(3)) multiplexer_1 (
    .in0(r0), .in1(r1), .in2(r2), .in3(r3), .in4(r4), .in5(r5), .in6(r6), .in7(r7), .out(lpt_addr),
    .sel(address));

  // Notes on the sheet:
  //   8x3 LHT
endmodule
